// Logisim project 流水线实验源文件.circ as structural Verilog: 21 circuits, main circuit ◇单周期MIPS
module \单周期MIPS  (
  input  IR1,
  input  IR2,
  input  IR3,
  output RegWrite,
  output MemWrite,
  output [31:0] PC,
  output [31:0] IR,
  output [31:0] RDin,
  output [31:0] MDin,
  output [31:0] LedData
);

  wire and_1_out, and_2_out, BSEL, CLK, clock_2_out, comparator_1_eq, comparator_2_eq, comparator_2_lt,
       d_ff_1_q, ERET, Go, IR1_t, IR2_t, IR3_t, IRA, IRB, IRC, JALSEL, JRSEL, JSEL, mips_alu_1_equal,
       multiplexer_2_out, multiplexer_3_out, nand_1_out, not_1_out, not_2_out, not_3_out, not_4_out,
       not_5_out, not_7_out, or_1_out, or_2_out, SignedExt, SYSCALL, W1, W2, W3, WAITGO,
       \单周期硬布线控制器_1_alu_src , \单周期硬布线控制器_1_beq , \单周期硬布线控制器_1_bne , \单周期硬布线控制器_1_memtoreg ,
       \单周期硬布线控制器_1_regdst ;
  wire [3:0] \单周期硬布线控制器_1_alu_op ;
  wire [4:0] controlled_buffer_4_out, multiplexer_4_out, multiplexer_5_out, multiplexer_6_out;
  wire [12:0] CNT_num;
  wire [15:0] \总周期数 ;
  wire [31:0] adder_2_out, bit_extender_1_out, bit_extender_2_out, controlled_buffer_1_out,
       controlled_buffer_8_out, mips_alu_1_result, multiplexer_1_out, multiplexer_7_out, multiplexer_8_out,
       multiplexer_9_out, PC_t, ram_1_data, registerfile_1_p7, shifter_1_out;

  Clock #(.highDuration(1), .lowDuration(1)) clock_1 ();  // open: out
  Button _1 (.out(IRA));
  Button _2 (.out(IRB));
  Button _3 (.out(IRC));
  Button \u_继续运行  (.out(Go));
  LED #(.active("true")) led_1 (.in(W1));
  LED #(.active("true")) led_2 (.in(W2));
  LED #(.active("true")) led_3 (.in(W3));
  Hex_Digit_Display hex_digit_display_1 (.value(LedData[31:28]));  // open: dp
  Hex_Digit_Display hex_digit_display_2 (.value(LedData[27:24]));  // open: dp
  Hex_Digit_Display hex_digit_display_3 (.value(LedData[23:20]));  // open: dp
  assign controlled_buffer_1_out = or_1_out ? {PC_t[31:28], IR[25:0], 2'b00} : 32'bz;  // Controlled_Buffer controlled_buffer_1
  or or_1 (or_1_out, JSEL, JALSEL);
  assign controlled_buffer_1_out = JRSEL ? registerfile_1_p7 : 32'bz;  // Controlled_Buffer controlled_buffer_2
  assign controlled_buffer_1_out = not_1_out ? multiplexer_1_out : 32'bz;  // Controlled_Buffer controlled_buffer_3
  Multiplexer #(.select(1), .width(32), .disabled("Z"), .enable("false")) multiplexer_1 (
    .in0(PC_t), .in1(adder_2_out), .out(multiplexer_1_out), .sel(BSEL));
  not not_1 (not_1_out, or_2_out);
  or or_2 (or_2_out, JSEL, JALSEL, JRSEL);
  Hex_Digit_Display hex_digit_display_4 (.value(LedData[15:12]));  // open: dp
  Hex_Digit_Display hex_digit_display_5 (.value(LedData[19:16]));  // open: dp
  not not_2 (not_2_out, multiplexer_2_out);
  Multiplexer #(.select(1), .width(1), .disabled("Z"), .enable("false")) multiplexer_2 (
    .in0(1'b0), .in1(WAITGO), .out(multiplexer_2_out), .sel(SYSCALL));
  Hex_Digit_Display hex_digit_display_6 (.value(LedData[11:8]));  // open: dp
  Hex_Digit_Display hex_digit_display_7 (.value(LedData[7:4]));  // open: dp
  // Probe on \总周期数 
  Counter #(.width(16), .max('hffff), .ongoal("wrap"), .trigger("rising"), .behavior("old")) counter_1 (
    .count(not_3_out), .Q(\总周期数 ), .clk(CLK));  // open: load, D, carry, clr, preset
  not not_3 (not_3_out, multiplexer_3_out);
  Multiplexer #(.select(1), .width(1), .disabled("Z"), .enable("false")) multiplexer_3 (
    .in0(1'b0), .in1(WAITGO), .out(multiplexer_3_out), .sel(SYSCALL));
  Register #(.width(32), .trigger("rising"), .Select("low")) u_PC (
    .D(controlled_buffer_1_out), .en(not_2_out), .Q(PC), .clk(CLK));  // open: clr
  Hex_Digit_Display hex_digit_display_8 (.value(LedData[3:0]));  // open: dp
  Adder #(.width(32)) adder_1 (.a(PC), .b(32'h4), .out(PC_t));  // open: cin, cout
  or or_3 (IR1_t, IR1, IRA);
  or or_4 (IR2_t, IR2, IRB);
  // Mips_Probe mips_probe_1: pin names not known; wires that end beside it: IR
  ROM #(.addrWidth(10), .dataWidth(32), .Select("high")) rom_1 (.addr(PC[11:2]), .data(IR));
  or or_5 (IR3_t, IR3, IRC);
  Multiplexer #(.select(1), .width(5), .disabled("Z"), .enable("false")) multiplexer_4 (
    .in0(IR[20:16]), .in1(5'b00100), .out(multiplexer_4_out), .sel(SYSCALL));
  Multiplexer #(.select(1), .width(5), .disabled("Z"), .enable("false")) multiplexer_5 (
    .in0(IR[25:21]), .in1(5'b00010), .out(multiplexer_5_out), .sel(SYSCALL));
  \单周期硬布线控制器  \u_单周期硬布线控制器_1  (
    .Func(IR[5:0]), .OP(IR[31:26]), .ALU_OP(\单周期硬布线控制器_1_alu_op ), .MemToReg(\单周期硬布线控制器_1_memtoreg ),
    .MemWrite(MemWrite), .ALU_SRC(\单周期硬布线控制器_1_alu_src ), .RegWrite(RegWrite), .SysCALL(SYSCALL),
    .SignedExt(SignedExt), .RegDst(\单周期硬布线控制器_1_regdst ), .JR(JRSEL), .JMP(JSEL), .Beq(\单周期硬布线控制器_1_beq ),
    .JAL(JALSEL), .Bne(\单周期硬布线控制器_1_bne ), ._25(IR[25]), .ERET(ERET));
  assign controlled_buffer_4_out = not_4_out ? multiplexer_6_out : 5'bz;  // Controlled_Buffer controlled_buffer_4
  Multiplexer #(.select(1), .width(5), .disabled("Z"), .enable("false")) multiplexer_6 (
    .in0(multiplexer_4_out), .in1(IR[15:11]), .out(multiplexer_6_out), .sel(\单周期硬布线控制器_1_regdst ));
  not not_4 (not_4_out, JALSEL);
  assign controlled_buffer_4_out = JALSEL ? {5{1'b1}} : 5'bz;  // Controlled_Buffer controlled_buffer_5
  assign RDin = JALSEL ? PC_t : 32'bz;  // Controlled_Buffer controlled_buffer_6
  assign bit_extender_1_out = {{16{1'b0}}, IR[15:0]};  // Bit_Extender bit_extender_1
  assign bit_extender_2_out = {{16{IR[15]}}, IR[15:0]};  // Bit_Extender bit_extender_2
  Multiplexer #(.select(1), .width(32), .disabled("Z"), .enable("false")) multiplexer_7 (
    .in0(mips_alu_1_result), .in1(ram_1_data), .out(multiplexer_7_out), .sel(\单周期硬布线控制器_1_memtoreg ));
  assign RDin = not_5_out ? multiplexer_7_out : 32'bz;  // Controlled_Buffer controlled_buffer_7
  not not_5 (not_5_out, JALSEL);
  Multiplexer #(.select(1), .width(32), .disabled("Z"), .enable("false")) multiplexer_8 (
    .in0(bit_extender_1_out), .in1(bit_extender_2_out), .out(multiplexer_8_out), .sel(SignedExt));
  Shifter #(.width(32), .shift("ll")) shifter_1 (.in(bit_extender_2_out), .\dist (5'b00010), .out(shifter_1_out));
  Comparator #(.width(32), .mode("twosComplement")) comparator_1 (
    .a(32'h22), .b(registerfile_1_p7), .eq(comparator_1_eq));  // open: gt, lt
  Adder #(.width(32)) adder_2 (.a(shifter_1_out), .b(PC_t), .out(adder_2_out));  // open: cin, cout
  // RegisterFile registerfile_1: pin names not known; wires that end beside it: RDin, CLK, RegWrite, controlled_buffer_4_out, multiplexer_5_out, multiplexer_4_out, registerfile_1_p7, MDin
  D_Flip_Flop #(.trigger("high"), .Pre_Clr_Positions("LEGACY"), .NegatePresetClear("false"), .enable("true"), .NewFFLayout("false")) d_ff_1 (.Q(d_ff_1_q));  // open: clk, D, Qn, preset, en, reset
  or or_6 (BSEL, and_2_out, and_1_out);
  and and_1 (and_1_out, \单周期硬布线控制器_1_beq , mips_alu_1_equal);
  assign controlled_buffer_8_out = comparator_1_eq ? MDin : 32'bz;  // Controlled_Buffer controlled_buffer_8
  Register #(.width(32), .trigger("rising"), .Select("low")) register_1 (
    .D(controlled_buffer_8_out), .Q(LedData), .clk(CLK));  // open: en, clr
  not not_6 (WAITGO, comparator_1_eq);
  // Probe on 13'h5
  Clock #(.highDuration(1), .lowDuration(1)) clock_2 (.out(clock_2_out));
  and and_2 (and_2_out, \单周期硬布线控制器_1_bne , not_7_out);
  not not_7 (not_7_out, mips_alu_1_equal);
  Comparator #(.width(13), .mode("twosComplement")) comparator_2 (
    .a(CNT_num), .b(13'h5), .eq(comparator_2_eq), .lt(comparator_2_lt));  // open: gt
  Multiplexer #(.select(1), .width(32), .disabled("Z"), .enable("false")) multiplexer_9 (
    .in0(MDin), .in1(multiplexer_8_out), .out(multiplexer_9_out), .sel(\单周期硬布线控制器_1_alu_src ));
  nand nand_1 (nand_1_out, d_ff_1_q, comparator_2_eq);
  Counter #(.width(13), .max('h1fff), .ongoal("stay"), .trigger("rising"), .behavior("old")) counter_2 (
    .count(comparator_2_lt), .Q(CNT_num), .clk(clock_2_out));  // open: load, D, carry, clr, preset
  MIPS_ALU mips_alu_1 (
    .X(registerfile_1_p7), .Y(multiplexer_9_out), .AluOP(\单周期硬布线控制器_1_alu_op ), .Equal(mips_alu_1_equal),
    .Result(mips_alu_1_result), .shamt(IR[10:6]));  // open: Result_2
  assign CLK = nand_1_out ? clock_2_out : 1'bz;  // Controlled_Buffer controlled_buffer_9
  Pull_Resistor #(.pull(1)) pull_resistor_1 (.node(CLK));
  RAM #(.addrWidth(10), .dataWidth(32), .bus("separate"), .Select("high")) ram_1 (
    .addr(mips_alu_1_result[11:2]), .din(MDin), .data(ram_1_data), .str(MemWrite), .clk(CLK));  // open: sel, ld, clr

  // Other names for the same wires on the sheet: RETA[31:0] = PC_t; target[25:0] = IR[25:0]; oldpc[31:0] = PC

  // Notes on the sheet:
  //   中断源
  //   中断等待指示
  //   总复位信号应将除ROM以外所有存储组件全部清零
  //   数码管输出
  //   数码管输出应该用寄存器锁存，否则显示数据只能一闪而过
  //   指令存储器
  //   指令字
  //   contents of rom_1 (hex, n*v repeats v):
  //   20110001 8000005 20110001 20120002 20130003 8000009 20110001 20120002 20130003 800000d 20110001
  //   20120002 20130003 8000011 20110001 20120002 20130003 c0000b8 20100001 20110001 118fc0 112020
  //   20020022 c 118882 12200001 8000015 112020 20020022 c 20110001 118880 112020 20020022 c 12200001
  //   800001f 20110001 118fc0 112020 20020022 c 1188c3 112020 20020022 c 118903 112020 20020022 c 118903
  //   112020 20020022 c 118903 112020 20020022 c 118903 112020 20020022 c 118903 112020 20020022 c 118903
  //   112020 20020022 c 118903 112020 20020022 c 20100001 109fc0 139fc3 8021 2012000c 24160003 26100001
  //   3210000f 20080008 20090001 139900 2709825 132020 20020022 c 1094022 1500fff9 22100001 2018000f
  //   2188024 108700 20080008 20090001 139902 2709825 132021 20020022 c 1094022 1500fff9 108702 2c9b022
  //   12c00001 8000050 4020 1084027 84400 3508ffff 82021 20020022 c 2010ffff 20110000 ae300000 22100001
  //   22310004 ae300000 22100001 22310004 ae300000 22100001 22310004 ae300000 22100001 22310004 ae300000
  //   22100001 22310004 ae300000 22100001 22310004 ae300000 22100001 22310004 ae300000 22100001 22310004
  //   ae300000 22100001 22310004 ae300000 22100001 22310004 ae300000 22100001 22310004 ae300000 22100001
  //   22310004 ae300000 22100001 22310004 ae300000 22100001 22310004 ae300000 22100001 22310004 ae300000
  //   22100001 22310004 22100001 8020 2011003c 8e130000 8e340000 274402a 11000002 ae330000 ae140000
  //   2231fffc 1611fff8 102020 20020022 c 22100004 2011003c 1611fff2 20020032 c 20100000 22100001 102020
  //   20020022 c 22100002 102020 20020022 c 22100003 102020 20020022 c 22100004 102020 20020022 c 22100005
  //   102020 20020022 c 22100006 102020 20020022 c 22100007 102020 20020022 c 22100008 102020 20020022
  //   20020022 c 3e00008
  //   OP
  //   Func
  //   rs
  //   Beq
  //   JMP
  //   JR
  //   Bne
  //   OP
  //   JAL
  //   Func
  //   Syscall
  //   为方便自动评测，需要输出PC，IR，寄存器堆写如数据RDin
  //   MemToReg
  //   MemWrite
  //   AluOP
  //   AluSrcB
  //   RegWrite
  //   RegDst
  //   RAM写使能MemWrite、RAM写入数据MDin等信号
  //   控制位
  //   暂停节拍，不能为0
  //   用这个时钟源需要去掉电路中的其他时钟源
  //   戳工具置1进入计数暂停模式，ctrl+k时钟自动运行到对应节拍暂停
  //   ctrl+k关闭时钟连续运行，将控制位置零，进入单步调试模式调试
  //   可计数暂停的时钟源
endmodule

module \有中断24条指令单周期cpu  (
  output RegWrite,
  output MemWrite,
  output [31:0] PC,
  output [31:0] IR,
  output [31:0] RDin,
  output [31:0] MDin
);

  wire and_2_out, and_3_out, BSEL, CLK, comparator_1_eq, comparator_2_eq, controlled_buffer_8_out,
       decoder_1_out1, decoder_1_out2, decoder_1_out3, ERET, Go, IE_q, IE_qn, IEIN, interamendPC, INTERRUPT,
       IR1, IR2, IR3, JALSEL, JRSEL, JSEL, mips_alu_1_equal, multiplexer_2_out, multiplexer_4_out, not_1_out,
       not_2_out, not_3_out, not_4_out, not_5_out, not_6_out, not_8_out, or_1_out, or_2_out,
       priority_encoder_1_gs, SignedExt, SYSCALL, W1, W2, W3, WAITGO, \中断按键参考电路_1_与中断屏蔽位与 ,
       \中断按键参考电路_2_与中断屏蔽位与 , \中断按键参考电路_3_与中断屏蔽位与 , \单周期硬布线控制器_1_alu_src , \单周期硬布线控制器_1_beq ,
       \单周期硬布线控制器_1_bne , \单周期硬布线控制器_1_memtoreg , \单周期硬布线控制器_1_memwrite , \单周期硬布线控制器_1_regdst ,
       \单周期硬布线控制器_1_regwrite ;
  wire [1:0] priority_encoder_1_out, register_1_q;
  wire [3:0] \单周期硬布线控制器_1_alu_op ;
  wire [4:0] controlled_buffer_11_out, multiplexer_6_out, multiplexer_7_out, multiplexer_8_out;
  wire [15:0] \总周期数 ;
  wire [25:0] target;
  wire [31:0] adder_2_out, bit_extender_1_out, bit_extender_2_out, controlled_buffer_1_out,
       controlled_buffer_3_out, controlled_buffer_7_out, controlled_buffer_10_out, controlled_buffer_14_out,
       EPCADDR, interruptaddr, LedData, mips_alu_1_result, multiplexer_1_out, multiplexer_9_out,
       multiplexer_10_out, multiplexer_11_out, oldpc, ram_1_data, registerfile_1_p7, registerfile_1_p8,
       shifter_1_out, shifter_2_out, shifter_3_out;
  wire [31:26] rom_1_data;

  Clock #(.highDuration(1), .lowDuration(1)) clock_1 (.out(CLK));
  Button _1 (.out(IR1));
  Button _2 (.out(IR2));
  Button _3 (.out(IR3));
  Button \u_继续运行  (.out(Go));
  LED #(.active("true")) led_1 (.in(W1));
  LED #(.active("true")) led_2 (.in(W2));
  LED #(.active("true")) led_3 (.in(W3));
  Hex_Digit_Display hex_digit_display_1 (.value(LedData[31:28]));  // open: dp
  Register #(.width(2), .trigger("rising"), .Select("low")) register_1 (
    .D(priority_encoder_1_out), .en(interamendPC), .Q(register_1_q), .clk(CLK));  // open: clr
  Hex_Digit_Display hex_digit_display_2 (.value(LedData[27:24]));  // open: dp
  Hex_Digit_Display hex_digit_display_3 (.value(LedData[23:20]));  // open: dp
  Decoder #(.select(2), .tristate("false"), .disabled(0), .enable("true")) decoder_1 (
    .out1(decoder_1_out1), .out2(decoder_1_out2), .out3(decoder_1_out3), .sel(register_1_q), .en(ERET));  // open: out0
  Hex_Digit_Display hex_digit_display_4 (.value(LedData[15:12]));  // open: dp
  Hex_Digit_Display hex_digit_display_5 (.value(LedData[19:16]));  // open: dp
  Multiplexer #(.select(1), .width(32), .disabled("Z"), .enable("false")) multiplexer_1 (
    .in0(PC), .in1(adder_2_out), .out(multiplexer_1_out), .sel(BSEL));
  Hex_Digit_Display hex_digit_display_6 (.value(LedData[11:8]));  // open: dp
  Hex_Digit_Display hex_digit_display_7 (.value(LedData[7:4]));  // open: dp
  // Probe on \总周期数 
  assign controlled_buffer_1_out = ERET ? EPCADDR : 32'bz;  // Controlled_Buffer controlled_buffer_1
  assign controlled_buffer_1_out = INTERRUPT ? interruptaddr : 32'bz;  // Controlled_Buffer controlled_buffer_2
  assign controlled_buffer_3_out = or_1_out ? {PC[31:26], target} : 32'bz;  // Controlled_Buffer controlled_buffer_3
  or or_1 (or_1_out, JSEL, JALSEL);
  assign controlled_buffer_3_out = JRSEL ? registerfile_1_p7 : 32'bz;  // Controlled_Buffer controlled_buffer_4
  assign controlled_buffer_3_out = not_1_out ? multiplexer_1_out : 32'bz;  // Controlled_Buffer controlled_buffer_5
  not not_1 (not_1_out, or_2_out);
  or or_2 (or_2_out, JSEL, JALSEL, JRSEL);
  Hex_Digit_Display hex_digit_display_8 (.value(LedData[3:0]));  // open: dp
  \中断按键参考电路  \u_中断按键参考电路_1  (
    .\与中断屏蔽位与 (\中断按键参考电路_1_与中断屏蔽位与 ), .\同步清零信号 (decoder_1_out1), .out_5(W1), .CLK(CLK), .in_2(IR1));
  \中断按键参考电路  \u_中断按键参考电路_2  (
    .\与中断屏蔽位与 (\中断按键参考电路_2_与中断屏蔽位与 ), .\同步清零信号 (decoder_1_out2), .out_5(W2), .CLK(CLK), .in_2(IR2));
  \中断按键参考电路  \u_中断按键参考电路_3  (
    .\与中断屏蔽位与 (\中断按键参考电路_3_与中断屏蔽位与 ), .\同步清零信号 (decoder_1_out3), .out_5(W3), .CLK(CLK), .in_2(IR3));
  assign controlled_buffer_1_out = not_2_out ? controlled_buffer_3_out : 32'bz;  // Controlled_Buffer controlled_buffer_6
  not not_2 (not_2_out, interamendPC);
  not not_3 (not_3_out, multiplexer_2_out);
  Multiplexer #(.select(1), .width(1), .disabled("Z"), .enable("false")) multiplexer_2 (
    .in0(1'b0), .in1(WAITGO), .out(multiplexer_2_out), .sel(SYSCALL));
  Register #(.width(32), .trigger("rising"), .Select("low")) u_PC (
    .D(controlled_buffer_1_out), .en(not_3_out), .Q(oldpc), .clk(CLK));  // open: clr
  Priority_Encoder #(.select(2), .disabled("Z")) priority_encoder_1 (
    .in1(\中断按键参考电路_1_与中断屏蔽位与 ), .in2(\中断按键参考电路_2_与中断屏蔽位与 ), .in3(\中断按键参考电路_3_与中断屏蔽位与 ),
    .out(priority_encoder_1_out), .gs(priority_encoder_1_gs));  // open: in0, en_out, en_in
  assign controlled_buffer_7_out = INTERRUPT ? oldpc : 32'bz;  // Controlled_Buffer controlled_buffer_7
  Register #(.width(32), .trigger("rising"), .Select("low")) EPC (
    .D(controlled_buffer_7_out), .Q(EPCADDR), .clk(CLK));  // open: en, clr
  or or_3 (interamendPC, INTERRUPT, ERET);
  D_Flip_Flop #(.trigger("rising"), .Pre_Clr_Positions("LEGACY"), .NegatePresetClear("false"), .enable("true"), .NewFFLayout("false")) IE (
    .clk(CLK), .D(IEIN), .Q(IE_q), .Qn(IE_qn));  // open: preset, en, reset
  Adder #(.width(32)) adder_1 (.a(oldpc), .b(32'h1), .out(PC));  // open: cin, cout
  Shifter #(.width(32), .shift("lr")) shifter_1 (.in(32'h2e4), .\dist (5'b00010), .out(shifter_1_out));
  Shifter #(.width(32), .shift("lr")) shifter_2 (.in(32'h364), .\dist (5'b00010), .out(shifter_2_out));
  Shifter #(.width(32), .shift("lr")) shifter_3 (.in(32'h3e4), .\dist (5'b00010), .out(shifter_3_out));
  and and_1 (INTERRUPT, priority_encoder_1_gs, IE_q);
  assign controlled_buffer_8_out = INTERRUPT ? 1'b0 : 1'bz;  // Controlled_Buffer controlled_buffer_8
  assign controlled_buffer_8_out = ERET ? 1'b1 : 1'bz;  // Controlled_Buffer controlled_buffer_9
  // Probe on interruptaddr
  Multiplexer #(.select(2), .width(32), .disabled("Z"), .enable("false")) multiplexer_3 (
    .in1(shifter_1_out), .in2(shifter_2_out), .in3(shifter_3_out), .out(interruptaddr),
    .sel(priority_encoder_1_out));  // open: in0
  not not_4 (not_4_out, IE_qn);
  Multiplexer #(.select(1), .width(1), .disabled("Z"), .enable("false")) multiplexer_4 (
    .in0(not_4_out), .in1(controlled_buffer_8_out), .out(multiplexer_4_out), .sel(interamendPC));
  ROM #(.addrWidth(10), .dataWidth(32), .Select("high")) rom_1 (.addr(oldpc[9:0]), .data({rom_1_data, target}));
  Multiplexer #(.select(1), .width(1), .disabled("Z"), .enable("false")) multiplexer_5 (
    .in0(multiplexer_4_out), .in1(1'b1), .out(IEIN), .sel(comparator_1_eq));
  Comparator #(.width(32), .mode("twosComplement")) comparator_1 (
    .a(oldpc), .b({32{1'b0}}), .eq(comparator_1_eq));  // open: gt, lt
  Multiplexer #(.select(1), .width(5), .disabled("Z"), .enable("false")) multiplexer_6 (
    .in0(target[20:16]), .in1(5'b00100), .out(multiplexer_6_out), .sel(SYSCALL));
  Multiplexer #(.select(1), .width(5), .disabled("Z"), .enable("false")) multiplexer_7 (
    .in0(target[25:21]), .in1(5'b00010), .out(multiplexer_7_out), .sel(SYSCALL));
  \单周期硬布线控制器  \u_单周期硬布线控制器_1  (
    .Func(target[5:0]), .OP(rom_1_data), .ALU_OP(\单周期硬布线控制器_1_alu_op ), .MemToReg(\单周期硬布线控制器_1_memtoreg ),
    .MemWrite(\单周期硬布线控制器_1_memwrite ), .ALU_SRC(\单周期硬布线控制器_1_alu_src ), .RegWrite(\单周期硬布线控制器_1_regwrite ),
    .SysCALL(SYSCALL), .SignedExt(SignedExt), .RegDst(\单周期硬布线控制器_1_regdst ), .JR(JRSEL), .JMP(JSEL),
    .Beq(\单周期硬布线控制器_1_beq ), .JAL(JALSEL), .Bne(\单周期硬布线控制器_1_bne ), ._25(target[25]), .ERET(ERET));
  assign controlled_buffer_10_out = JALSEL ? PC : 32'bz;  // Controlled_Buffer controlled_buffer_10
  assign controlled_buffer_11_out = not_5_out ? multiplexer_8_out : 5'bz;  // Controlled_Buffer controlled_buffer_11
  Multiplexer #(.select(1), .width(5), .disabled("Z"), .enable("false")) multiplexer_8 (
    .in0(multiplexer_6_out), .in1(target[15:11]), .out(multiplexer_8_out), .sel(\单周期硬布线控制器_1_regdst ));
  not not_5 (not_5_out, JALSEL);
  assign controlled_buffer_11_out = JALSEL ? {5{1'b1}} : 5'bz;  // Controlled_Buffer controlled_buffer_12
  assign bit_extender_1_out = {{16{1'b0}}, target[15:0]};  // Bit_Extender bit_extender_1
  assign bit_extender_2_out = {{16{target[15]}}, target[15:0]};  // Bit_Extender bit_extender_2
  // Probe on bit_extender_2_out
  Adder #(.width(32)) adder_2 (.a(bit_extender_2_out), .b(PC), .out(adder_2_out));  // open: cin, cout
  assign controlled_buffer_10_out = not_6_out ? multiplexer_9_out : 32'bz;  // Controlled_Buffer controlled_buffer_13
  Multiplexer #(.select(1), .width(32), .disabled("Z"), .enable("false")) multiplexer_9 (
    .in0(mips_alu_1_result), .in1(ram_1_data), .out(multiplexer_9_out), .sel(\单周期硬布线控制器_1_memtoreg ));
  not not_6 (not_6_out, JALSEL);
  Multiplexer #(.select(1), .width(32), .disabled("Z"), .enable("false")) multiplexer_10 (
    .in0(bit_extender_1_out), .in1(bit_extender_2_out), .out(multiplexer_10_out), .sel(SignedExt));
  Comparator #(.width(32), .mode("twosComplement")) comparator_2 (
    .a(32'h22), .b(registerfile_1_p7), .eq(comparator_2_eq));  // open: gt, lt
  assign controlled_buffer_14_out = comparator_2_eq ? registerfile_1_p8 : 32'bz;  // Controlled_Buffer controlled_buffer_14
  // RegisterFile registerfile_1: pin names not known; wires that end beside it: controlled_buffer_10_out, CLK, \单周期硬布线控制器_1_regwrite , controlled_buffer_11_out, multiplexer_7_out, multiplexer_6_out, registerfile_1_p7, registerfile_1_p8
  or or_4 (BSEL, and_3_out, and_2_out);
  and and_2 (and_2_out, \单周期硬布线控制器_1_beq , mips_alu_1_equal);
  Register #(.width(32), .trigger("rising"), .Select("low")) register_2 (
    .D(controlled_buffer_14_out), .Q(LedData), .clk(CLK));  // open: en, clr
  not not_7 (WAITGO, comparator_2_eq);
  and and_3 (and_3_out, \单周期硬布线控制器_1_bne , not_8_out);
  not not_8 (not_8_out, mips_alu_1_equal);
  Multiplexer #(.select(1), .width(32), .disabled("Z"), .enable("false")) multiplexer_11 (
    .in0(registerfile_1_p8), .in1(multiplexer_10_out), .out(multiplexer_11_out), .sel(\单周期硬布线控制器_1_alu_src ));
  MIPS_ALU mips_alu_1 (
    .X(registerfile_1_p7), .Y(multiplexer_11_out), .AluOP(\单周期硬布线控制器_1_alu_op ), .Equal(mips_alu_1_equal),
    .Result(mips_alu_1_result), .shamt(target[10:6]));  // open: Result_2
  RAM #(.addrWidth(10), .dataWidth(32), .bus("separate"), .Select("high")) ram_1 (
    .addr(mips_alu_1_result[9:0]), .din(registerfile_1_p8), .data(ram_1_data), .str(\单周期硬布线控制器_1_memwrite ),
    .clk(CLK));  // open: sel, ld, clr

  // Other names for the same wires on the sheet: RETA[31:0] = PC

  // Notes on the sheet:
  //   中断源
  //   中断等待指示
  //   总复位信号应将除ROM以外所有存储组件全部清零
  //   数码管输出
  //   数码管输出应该用寄存器锁存，否则显示数据只能一闪而过
  //   为方便自动评测，需要输出PC，IR，寄存器文件写入端口RDin，内存写入端口MDin等信号
  //   指令存储器
  //   指令字
  //   contents of rom_1 (hex, n*v repeats v):
  //   201d03ff 20110001 8000006 20110001 20120002 20130003 800000a 20110001 20120002 20130003 800000e
  //   20110001 20120002 20130003 8000012 20110001 20120002 20130003 c000119 20100001 20110001 118fc0
  //   112020 20020022 c 118882 12200001 8000016 112020 20020022 c 20110001 118880 112020 20020022 c
  //   12200001 8000020 20110001 118fc0 112020 20020022 c 1188c3 112020 20020022 c 118903 112020 20020022 c
  //   118903 112020 20020022 c 118903 112020 20020022 c 118903 112020 20020022 c 118903 112020 20020022 c
  //   118903 112020 20020022 c 118903 112020 20020022 c 20100001 109fc0 139fc3 8021 2012000c 24160003
  //   26100001 3210000f 20080008 20090001 139900 2709825 132020 20020022 c 1094022 1500fff9 22100001
  //   2018000f 2188024 108700 20080008 20090001 139902 2709825 132021 20020022 c 1094022 1500fff9 108702
  //   2c9b022 12c00001 8000051 4020 1084027 84400 3508ffff 82021 20020022 c 2010ffff 20110000 ae300000
  //   22100001 22310004 ae300000 22100001 22310004 ae300000 22100001 22310004 ae300000 22100001 22310004
  //   ae300000 22100001 22310004 ae300000 22100001 22310004 ae300000 22100001 22310004 ae300000 22100001
  //   22310004 ae300000 22100001 22310004 ae300000 22100001 22310004 ae300000 22100001 22310004 ae300000
  //   22100001 22310004 ae300000 22100001 22310004 ae300000 22100001 22310004 ae300000 22100001 22310004
  //   ae300000 22100001 22310004 22100001 8020 2011003c 8e130000 8e340000 274402a 11000002 ae330000
  //   ae140000 2231fffc 1611fff8 102020 20020022 c 22100004 2011003c 1611fff2 20020032 c 27bdfff0 afa20000
  //   afb00004 afb10008 afa4000c 24110007 24100001 102020 24020022 c 108100 26100001 2631ffff 102020
  //   24020022 c 12200002 0 80000c3 24110008 108100 2631ffff 102020 24020022 c 1620fffa 8fa20000 8fb00004
  //   8fb10008 8fa4000c 27bd0010 42000018 27bdfff0 afa20000 afb00004 afb10008 afa4000c 24110007 24100002
  //   102020 24020022 c 108100 26100002 2631ffff 102020 24020022 c 12200002 0 80000e3 24110008 108100
  //   2631ffff 102020 24020022 c 1620fffa 8fa20000 8fb00004 8fb10008 8fa4000c 27bd0010 42000018 27bdfff0
  //   afa20000 afb00004 afb10008 afa4000c 24110007 24100003 102020 24020022 c 108100 26100003 2631ffff
  //   102020 24020022 c 12200002 0 8000103 24110008 108100 2631ffff 102020 24020022 c 1620fffa 8fa20000
  //   8fb00004 8fb10008 8fa4000c 27bd0010 42000018 20100000 22100001 102020 20020022 c 22100002 102020
  //   20020022 c 22100003 102020 20020022 c 22100004 102020 20020022 c 22100005 102020 20020022 c 22100006
  //   102020 20020022 c 22100007 102020 20020022 c 22100008 102020 20020022 c 3e00008
  //   OP
  //   Func
  //   rs
  //   JMP
  //   JR
  //   OP
  //   Func
  //   Beq
  //   Bne
  //   AluOP
  //   AluSrcB
  //   RegWrite
  //   JAL
  //   RegDst
  //   Syscall
  //   MemToReg
  //   MemWrite
  //   地址错误的中断处理
endmodule

// 单周期硬布线控制器
module \单周期硬布线控制器  (
  input  [5:0] OP,
  input  [5:0] Func,
  input  _25,
  output [3:0] ALU_OP,
  output MemToReg,
  output MemWrite,
  output ALU_SRC,
  output RegWrite,
  output SysCALL,
  output SignedExt,
  output RegDst,
  output Beq,
  output Bne,
  output JR,
  output JMP,
  output JAL,
  output ERET
);

  wire comparator_1_eq, comparator_2_eq;

  \运算控制器自动生成  \u_运算控制器自动生成_1  (
    .OP0(OP[0]), .OP1(OP[1]), .OP2(OP[2]), .OP3(OP[3]), .OP4(OP[4]), .OP5(OP[5]), .F0(Func[0]), .F1(Func[1]),
    .F2(Func[2]), .F3(Func[3]), .F4(Func[4]), .F5(Func[5]), .S0(ALU_OP[0]), .S1(ALU_OP[1]), .S2(ALU_OP[2]),
    .S3(ALU_OP[3]));
  \控制信号自动生成  \u_控制信号自动生成_1  (
    .OP0(OP[0]), .OP1(OP[1]), .OP2(OP[2]), .OP3(OP[3]), .OP4(OP[4]), .OP5(OP[5]), .F0(Func[0]), .F1(Func[1]),
    .F2(Func[2]), .F3(Func[3]), .F4(Func[4]), .F5(Func[5]), .MemToReg(MemToReg), .MemWrite(MemWrite),
    .ALU_SRC(ALU_SRC), .RegWrite(RegWrite), .SysCALL(SysCALL), .SignedExt(SignedExt), .RegDst(RegDst),
    .BEQ(Beq), .BNE(Bne), .JR(JR), .JUMP(JMP), .JAL(JAL));
  Comparator #(.width(8), .mode("twosComplement")) comparator_1 (
    .a({OP, _25, 1'b0}), .b(8'h42), .eq(comparator_1_eq));  // open: gt, lt
  Comparator #(.width(6), .mode("twosComplement")) comparator_2 (
    .a(6'b011000), .b(Func), .eq(comparator_2_eq));  // open: gt, lt
  and and_1 (ERET, comparator_1_eq, comparator_2_eq);

  // Other names for the same wires on the sheet: OP_CODE[5:0] = OP

  // Notes on the sheet:
  //   运算器控制器，根据指令生成运算器功能选择信号
  //   控制信号生成，产生数据通路需要的其他控制信号
endmodule

// 运算器控制器
module \运算控制器自动生成  (
  input  OP0,
  input  OP1,
  input  OP2,
  input  OP3,
  input  OP4,
  input  OP5,
  input  F0,
  input  F1,
  input  F2,
  input  F3,
  input  F4,
  input  F5,
  output S0,
  output S1,
  output S2,
  output S3
);

  wire and_1_out, and_2_out, and_3_out, and_4_out, and_5_out, and_6_out, and_7_out, and_8_out, and_9_out,
       and_10_out, and_11_out, and_12_out, and_13_out, and_14_out, and_15_out, and_16_out, and_17_out,
       and_18_out, and_19_out, and_20_out, and_21_out, and_22_out, and_23_out, and_24_out, and_25_out,
       not_1_out, not_2_out, not_3_out, not_4_out, not_5_out, not_6_out, not_7_out, not_8_out, not_9_out,
       not_10_out, not_11_out, not_12_out, not_13_out, not_14_out, not_15_out, not_16_out, not_17_out,
       not_18_out, not_19_out, not_20_out, not_21_out, not_22_out, not_23_out, not_24_out, not_25_out,
       not_26_out, not_27_out, not_28_out, not_29_out, not_30_out, not_31_out, not_32_out, not_33_out,
       not_34_out, not_35_out, not_36_out, not_37_out, not_38_out, not_39_out, not_40_out, not_41_out,
       not_42_out, not_43_out, not_44_out, not_45_out, not_46_out, not_47_out, not_48_out, not_49_out,
       not_50_out, not_51_out, not_52_out, not_53_out, not_54_out, not_55_out, not_56_out, not_57_out,
       not_58_out, not_59_out, not_60_out, not_61_out, not_62_out, not_63_out, not_64_out, not_65_out,
       not_66_out, not_67_out, not_68_out, not_69_out, not_70_out, not_71_out, not_72_out, not_73_out,
       not_74_out, not_75_out, not_76_out, not_77_out, not_78_out, not_79_out, not_80_out, not_81_out,
       not_82_out, not_83_out, not_84_out, not_85_out, not_86_out, not_87_out, not_88_out, not_89_out,
       not_90_out, not_91_out, not_92_out, not_93_out, not_94_out, not_95_out, not_96_out, not_97_out,
       not_98_out, not_99_out, not_100_out, not_101_out, not_102_out, not_103_out, not_104_out, not_105_out,
       not_106_out, not_107_out, not_108_out, not_109_out, not_110_out, not_111_out, not_112_out,
       not_113_out, not_114_out, not_115_out, not_116_out, not_117_out, not_118_out, not_119_out,
       not_120_out, not_121_out, not_122_out, not_123_out, not_124_out, not_125_out, not_126_out,
       not_127_out, not_128_out, not_129_out, not_130_out, not_131_out, not_132_out, not_133_out,
       not_134_out, not_135_out, not_136_out, not_137_out, not_138_out, not_139_out, not_140_out,
       not_141_out, not_142_out, not_143_out, not_144_out, not_145_out, not_146_out, not_147_out,
       not_148_out, not_149_out, not_150_out, not_151_out, not_152_out, not_153_out, not_154_out,
       not_155_out, not_156_out, not_157_out, not_158_out, not_159_out, not_160_out, not_161_out;

  not not_1 (not_1_out, OP0);
  not not_2 (not_2_out, OP1);
  not not_3 (not_3_out, OP2);
  not not_4 (not_4_out, OP4);
  not not_5 (not_5_out, OP5);
  not not_6 (not_6_out, F0);
  not not_7 (not_7_out, F1);
  not not_8 (not_8_out, F3);
  not not_9 (not_9_out, F4);
  not not_10 (not_10_out, OP0);
  not not_11 (not_11_out, OP1);
  not not_12 (not_12_out, OP2);
  not not_13 (not_13_out, OP4);
  not not_14 (not_14_out, OP5);
  not not_15 (not_15_out, F1);
  not not_16 (not_16_out, F2);
  not not_17 (not_17_out, F3);
  not not_18 (not_18_out, F4);
  not not_19 (not_19_out, OP0);
  not not_20 (not_20_out, OP1);
  not not_21 (not_21_out, OP2);
  not not_22 (not_22_out, OP4);
  not not_23 (not_23_out, OP5);
  not not_24 (not_24_out, F0);
  not not_25 (not_25_out, F2);
  not not_26 (not_26_out, F4);
  not not_27 (not_27_out, OP0);
  not not_28 (not_28_out, OP1);
  not not_29 (not_29_out, OP2);
  not not_30 (not_30_out, OP4);
  not not_31 (not_31_out, OP5);
  not not_32 (not_32_out, F2);
  not not_33 (not_33_out, F3);
  not not_34 (not_34_out, F4);
  not not_35 (not_35_out, F5);
  not not_36 (not_36_out, OP0);
  not not_37 (not_37_out, OP1);
  not not_38 (not_38_out, OP4);
  not not_39 (not_39_out, OP5);
  not not_40 (not_40_out, OP0);
  not not_41 (not_41_out, OP2);
  not not_42 (not_42_out, OP4);
  not not_43 (not_43_out, OP5);
  not not_44 (not_44_out, OP1);
  not not_45 (not_45_out, OP2);
  not not_46 (not_46_out, OP4);
  not not_47 (not_47_out, OP5);
  not not_48 (not_48_out, OP2);
  not not_49 (not_49_out, OP4);
  not not_50 (not_50_out, OP0);
  not not_51 (not_51_out, OP1);
  not not_52 (not_52_out, OP2);
  not not_53 (not_53_out, OP3);
  not not_54 (not_54_out, OP4);
  not not_55 (not_55_out, OP5);
  not not_56 (not_56_out, F0);
  not not_57 (not_57_out, F1);
  not not_58 (not_58_out, F3);
  not not_59 (not_59_out, F4);
  not not_60 (not_60_out, OP0);
  not not_61 (not_61_out, OP1);
  not not_62 (not_62_out, OP2);
  not not_63 (not_63_out, OP3);
  not not_64 (not_64_out, OP4);
  not not_65 (not_65_out, OP5);
  not not_66 (not_66_out, F0);
  not not_67 (not_67_out, F2);
  not not_68 (not_68_out, F3);
  not not_69 (not_69_out, F4);
  not not_70 (not_70_out, OP0);
  not not_71 (not_71_out, OP1);
  not not_72 (not_72_out, OP2);
  not not_73 (not_73_out, OP3);
  not not_74 (not_74_out, OP4);
  not not_75 (not_75_out, OP5);
  not not_76 (not_76_out, F0);
  not not_77 (not_77_out, F2);
  not not_78 (not_78_out, F4);
  not not_79 (not_79_out, OP0);
  not not_80 (not_80_out, OP1);
  not not_81 (not_81_out, OP2);
  not not_82 (not_82_out, OP3);
  not not_83 (not_83_out, OP4);
  not not_84 (not_84_out, OP5);
  not not_85 (not_85_out, F3);
  not not_86 (not_86_out, F4);
  not not_87 (not_87_out, OP0);
  not not_88 (not_88_out, OP1);
  not not_89 (not_89_out, OP4);
  not not_90 (not_90_out, OP5);
  not not_91 (not_91_out, OP0);
  not not_92 (not_92_out, OP2);
  not not_93 (not_93_out, OP4);
  not not_94 (not_94_out, OP5);
  not not_95 (not_95_out, OP0);
  not not_96 (not_96_out, OP1);
  not not_97 (not_97_out, OP2);
  not not_98 (not_98_out, OP4);
  not not_99 (not_99_out, OP5);
  not not_100 (not_100_out, F0);
  not not_101 (not_101_out, F1);
  not not_102 (not_102_out, F3);
  not not_103 (not_103_out, F4);
  not not_104 (not_104_out, OP0);
  not not_105 (not_105_out, OP1);
  not not_106 (not_106_out, OP2);
  not not_107 (not_107_out, OP4);
  not not_108 (not_108_out, OP5);
  not not_109 (not_109_out, F0);
  not not_110 (not_110_out, F2);
  not not_111 (not_111_out, F3);
  not not_112 (not_112_out, F4);
  not not_113 (not_113_out, OP0);
  not not_114 (not_114_out, OP1);
  not not_115 (not_115_out, OP2);
  not not_116 (not_116_out, OP4);
  not not_117 (not_117_out, OP5);
  not not_118 (not_118_out, F1);
  not not_119 (not_119_out, F2);
  not not_120 (not_120_out, F3);
  not not_121 (not_121_out, F4);
  not not_122 (not_122_out, OP0);
  not not_123 (not_123_out, OP1);
  not not_124 (not_124_out, OP2);
  not not_125 (not_125_out, OP4);
  not not_126 (not_126_out, OP5);
  not not_127 (not_127_out, F2);
  not not_128 (not_128_out, F4);
  not not_129 (not_129_out, OP0);
  not not_130 (not_130_out, OP1);
  not not_131 (not_131_out, OP4);
  not not_132 (not_132_out, OP5);
  not not_133 (not_133_out, OP1);
  not not_134 (not_134_out, OP2);
  not not_135 (not_135_out, OP4);
  not not_136 (not_136_out, OP5);
  not not_137 (not_137_out, OP2);
  not not_138 (not_138_out, OP4);
  not not_139 (not_139_out, OP0);
  not not_140 (not_140_out, OP1);
  not not_141 (not_141_out, OP2);
  not not_142 (not_142_out, OP3);
  not not_143 (not_143_out, OP4);
  not not_144 (not_144_out, OP5);
  not not_145 (not_145_out, F2);
  not not_146 (not_146_out, F4);
  not not_147 (not_147_out, OP0);
  not not_148 (not_148_out, OP1);
  not not_149 (not_149_out, OP2);
  not not_150 (not_150_out, OP3);
  not not_151 (not_151_out, OP4);
  not not_152 (not_152_out, OP5);
  not not_153 (not_153_out, F3);
  not not_154 (not_154_out, F4);
  not not_155 (not_155_out, OP0);
  not not_156 (not_156_out, OP2);
  not not_157 (not_157_out, OP4);
  not not_158 (not_158_out, OP5);
  not not_159 (not_159_out, OP1);
  not not_160 (not_160_out, OP4);
  not not_161 (not_161_out, OP5);
  and and_1 (and_1_out, not_1_out, not_2_out, not_3_out, not_4_out, not_5_out, not_6_out, not_7_out, not_8_out, not_9_out, F5);
  and and_2 (and_2_out, not_10_out, not_11_out, not_12_out, not_13_out, not_14_out, not_15_out, not_16_out, not_17_out, not_18_out, F5);
  and and_3 (and_3_out, not_19_out, not_20_out, not_21_out, not_22_out, not_23_out, not_24_out, F1, not_25_out, F3, not_26_out, F5);
  and and_4 (and_4_out, not_27_out, not_28_out, not_29_out, not_30_out, not_31_out, F0, F1, not_32_out, not_33_out, not_34_out, not_35_out);
  and and_5 (and_5_out, not_36_out, not_37_out, OP3, not_38_out, not_39_out);
  and and_6 (and_6_out, not_40_out, not_41_out, OP3, not_42_out, not_43_out);
  and and_7 (and_7_out, not_44_out, not_45_out, OP3, not_46_out, not_47_out);
  and and_8 (and_8_out, OP0, OP1, not_48_out, not_49_out, OP5);
  and and_9 (and_9_out, not_50_out, not_51_out, not_52_out, not_53_out, not_54_out, not_55_out, not_56_out, not_57_out, F2, not_58_out, not_59_out, F5);
  and and_10 (and_10_out, not_60_out, not_61_out, not_62_out, not_63_out, not_64_out, not_65_out, not_66_out, F1, not_67_out, not_68_out, not_69_out);
  and and_11 (and_11_out, not_70_out, not_71_out, not_72_out, not_73_out, not_74_out, not_75_out, not_76_out, F1, not_77_out, not_78_out, F5);
  and and_12 (and_12_out, not_79_out, not_80_out, not_81_out, not_82_out, not_83_out, not_84_out, F0, F1, F2, not_85_out, not_86_out, F5);
  and and_13 (and_13_out, not_87_out, not_88_out, OP2, OP3, not_89_out, not_90_out);
  and and_14 (and_14_out, not_91_out, OP1, not_92_out, OP3, not_93_out, not_94_out);
  and and_15 (and_15_out, not_95_out, not_96_out, not_97_out, not_98_out, not_99_out, not_100_out, not_101_out, not_102_out, not_103_out, F5);
  and and_16 (and_16_out, not_104_out, not_105_out, not_106_out, not_107_out, not_108_out, not_109_out, not_110_out, not_111_out, not_112_out, F5);
  and and_17 (and_17_out, not_113_out, not_114_out, not_115_out, not_116_out, not_117_out, not_118_out, not_119_out, not_120_out, not_121_out, F5);
  and and_18 (and_18_out, not_122_out, not_123_out, not_124_out, not_125_out, not_126_out, F0, F1, not_127_out, F3, not_128_out, F5);
  and and_19 (and_19_out, not_129_out, not_130_out, OP3, not_131_out, not_132_out);
  and and_20 (and_20_out, not_133_out, not_134_out, OP3, not_135_out, not_136_out);
  and and_21 (and_21_out, OP0, OP1, not_137_out, not_138_out, OP5);
  and and_22 (and_22_out, not_139_out, not_140_out, not_141_out, not_142_out, not_143_out, not_144_out, F1, not_145_out, F3, not_146_out, F5);
  and and_23 (and_23_out, not_147_out, not_148_out, not_149_out, not_150_out, not_151_out, not_152_out, F0, F2, not_153_out, not_154_out, F5);
  and and_24 (and_24_out, not_155_out, OP1, not_156_out, OP3, not_157_out, not_158_out);
  and and_25 (and_25_out, OP0, not_159_out, OP2, OP3, not_160_out, not_161_out);
  or or_1 (S0, and_1_out, and_2_out, and_3_out, and_4_out, and_5_out, and_6_out, and_7_out, and_8_out);
  or or_2 (S1, and_9_out, and_10_out, and_11_out, and_12_out, and_13_out, and_14_out);
  or or_3 (S2, and_15_out, and_16_out, and_17_out, and_18_out, and_19_out, and_20_out, and_21_out);
  or or_4 (S3, and_22_out, and_23_out, and_24_out, and_25_out);
endmodule

// 控制信号生成
module \控制信号自动生成  (
  input  OP0,
  input  OP1,
  input  OP2,
  input  OP3,
  input  OP4,
  input  OP5,
  input  F0,
  input  F1,
  input  F2,
  input  F3,
  input  F4,
  input  F5,
  output MemToReg,
  output MemWrite,
  output ALU_SRC,
  output RegWrite,
  output SysCALL,
  output SignedExt,
  output RegDst,
  output BEQ,
  output BNE,
  output JR,
  output JUMP,
  output JAL
);

  wire and_3_out, and_4_out, and_5_out, and_6_out, and_7_out, and_8_out, and_9_out, and_10_out, and_11_out,
       and_12_out, and_13_out, and_15_out, and_16_out, and_17_out, and_18_out, and_19_out, and_20_out,
       and_21_out, and_22_out, not_1_out, not_2_out, not_3_out, not_4_out, not_5_out, not_6_out, not_7_out,
       not_8_out, not_9_out, not_10_out, not_11_out, not_12_out, not_13_out, not_14_out, not_15_out,
       not_16_out, not_17_out, not_18_out, not_19_out, not_20_out, not_21_out, not_22_out, not_23_out,
       not_24_out, not_25_out, not_26_out, not_27_out, not_28_out, not_29_out, not_30_out, not_31_out,
       not_32_out, not_33_out, not_34_out, not_35_out, not_36_out, not_37_out, not_38_out, not_39_out,
       not_40_out, not_41_out, not_42_out, not_43_out, not_44_out, not_45_out, not_46_out, not_47_out,
       not_48_out, not_49_out, not_50_out, not_51_out, not_52_out, not_53_out, not_54_out, not_55_out,
       not_56_out, not_57_out, not_58_out, not_59_out, not_60_out, not_61_out, not_62_out, not_63_out,
       not_64_out, not_65_out, not_66_out, not_67_out, not_68_out, not_69_out, not_70_out, not_71_out,
       not_72_out, not_73_out, not_74_out, not_75_out, not_76_out, not_77_out, not_78_out, not_79_out,
       not_80_out, not_81_out, not_82_out, not_83_out, not_84_out, not_85_out, not_86_out, not_87_out,
       not_88_out, not_89_out, not_90_out, not_91_out, not_92_out, not_93_out, not_94_out, not_95_out,
       not_96_out, not_97_out, not_98_out, not_99_out, not_100_out, not_101_out, not_102_out, not_103_out,
       not_104_out, not_105_out, not_106_out, not_107_out, not_108_out, not_109_out, not_110_out,
       not_111_out, not_112_out, not_113_out, not_114_out, not_115_out, not_116_out, not_117_out,
       not_118_out, not_119_out, not_120_out, not_121_out, not_122_out, not_123_out, not_124_out,
       not_125_out, not_126_out, not_127_out, not_128_out, not_129_out, not_130_out, not_131_out,
       not_132_out, not_133_out, not_134_out, not_135_out, not_136_out, not_137_out, not_138_out,
       not_139_out, not_140_out, not_141_out, not_142_out, not_143_out, not_144_out, not_145_out,
       not_146_out, not_147_out, not_148_out, not_149_out, not_150_out, not_151_out, not_152_out,
       not_153_out, not_154_out, not_155_out, not_156_out, not_157_out;

  not not_1 (not_1_out, OP2);
  not not_2 (not_2_out, OP3);
  not not_3 (not_3_out, OP4);
  not not_4 (not_4_out, OP2);
  not not_5 (not_5_out, OP4);
  not not_6 (not_6_out, OP0);
  not not_7 (not_7_out, OP2);
  not not_8 (not_8_out, OP4);
  not not_9 (not_9_out, OP5);
  not not_10 (not_10_out, OP1);
  not not_11 (not_11_out, OP4);
  not not_12 (not_12_out, OP5);
  not not_13 (not_13_out, OP2);
  not not_14 (not_14_out, OP4);
  not not_15 (not_15_out, OP0);
  not not_16 (not_16_out, OP1);
  not not_17 (not_17_out, OP2);
  not not_18 (not_18_out, OP4);
  not not_19 (not_19_out, OP5);
  not not_20 (not_20_out, F0);
  not not_21 (not_21_out, F2);
  not not_22 (not_22_out, F3);
  not not_23 (not_23_out, F4);
  not not_24 (not_24_out, OP0);
  not not_25 (not_25_out, OP1);
  not not_26 (not_26_out, OP2);
  not not_27 (not_27_out, OP4);
  not not_28 (not_28_out, OP5);
  not not_29 (not_29_out, F1);
  not not_30 (not_30_out, F3);
  not not_31 (not_31_out, F4);
  not not_32 (not_32_out, OP0);
  not not_33 (not_33_out, OP1);
  not not_34 (not_34_out, OP2);
  not not_35 (not_35_out, OP4);
  not not_36 (not_36_out, OP5);
  not not_37 (not_37_out, F2);
  not not_38 (not_38_out, F3);
  not not_39 (not_39_out, F4);
  not not_40 (not_40_out, F5);
  not not_41 (not_41_out, OP0);
  not not_42 (not_42_out, OP1);
  not not_43 (not_43_out, OP2);
  not not_44 (not_44_out, OP4);
  not not_45 (not_45_out, OP5);
  not not_46 (not_46_out, F2);
  not not_47 (not_47_out, F4);
  not not_48 (not_48_out, OP0);
  not not_49 (not_49_out, OP1);
  not not_50 (not_50_out, OP2);
  not not_51 (not_51_out, OP4);
  not not_52 (not_52_out, OP5);
  not not_53 (not_53_out, F3);
  not not_54 (not_54_out, F4);
  not not_55 (not_55_out, OP0);
  not not_56 (not_56_out, OP2);
  not not_57 (not_57_out, OP4);
  not not_58 (not_58_out, OP5);
  not not_59 (not_59_out, OP1);
  not not_60 (not_60_out, OP4);
  not not_61 (not_61_out, OP5);
  not not_62 (not_62_out, OP2);
  not not_63 (not_63_out, OP3);
  not not_64 (not_64_out, OP4);
  not not_65 (not_65_out, OP0);
  not not_66 (not_66_out, OP1);
  not not_67 (not_67_out, OP2);
  not not_68 (not_68_out, OP3);
  not not_69 (not_69_out, OP4);
  not not_70 (not_70_out, OP5);
  not not_71 (not_71_out, F0);
  not not_72 (not_72_out, F1);
  not not_73 (not_73_out, F4);
  not not_74 (not_74_out, F5);
  not not_75 (not_75_out, OP0);
  not not_76 (not_76_out, OP2);
  not not_77 (not_77_out, OP4);
  not not_78 (not_78_out, OP5);
  not not_79 (not_79_out, OP1);
  not not_80 (not_80_out, OP4);
  not not_81 (not_81_out, OP5);
  not not_82 (not_82_out, OP2);
  not not_83 (not_83_out, OP4);
  not not_84 (not_84_out, OP0);
  not not_85 (not_85_out, OP1);
  not not_86 (not_86_out, OP2);
  not not_87 (not_87_out, OP3);
  not not_88 (not_88_out, OP4);
  not not_89 (not_89_out, OP5);
  not not_90 (not_90_out, F0);
  not not_91 (not_91_out, F2);
  not not_92 (not_92_out, F3);
  not not_93 (not_93_out, F4);
  not not_94 (not_94_out, OP0);
  not not_95 (not_95_out, OP1);
  not not_96 (not_96_out, OP2);
  not not_97 (not_97_out, OP3);
  not not_98 (not_98_out, OP4);
  not not_99 (not_99_out, OP5);
  not not_100 (not_100_out, F1);
  not not_101 (not_101_out, F3);
  not not_102 (not_102_out, F4);
  not not_103 (not_103_out, OP0);
  not not_104 (not_104_out, OP1);
  not not_105 (not_105_out, OP2);
  not not_106 (not_106_out, OP3);
  not not_107 (not_107_out, OP4);
  not not_108 (not_108_out, OP5);
  not not_109 (not_109_out, F2);
  not not_110 (not_110_out, F3);
  not not_111 (not_111_out, F4);
  not not_112 (not_112_out, F5);
  not not_113 (not_113_out, OP0);
  not not_114 (not_114_out, OP1);
  not not_115 (not_115_out, OP2);
  not not_116 (not_116_out, OP3);
  not not_117 (not_117_out, OP4);
  not not_118 (not_118_out, OP5);
  not not_119 (not_119_out, F2);
  not not_120 (not_120_out, F4);
  not not_121 (not_121_out, OP0);
  not not_122 (not_122_out, OP1);
  not not_123 (not_123_out, OP2);
  not not_124 (not_124_out, OP3);
  not not_125 (not_125_out, OP4);
  not not_126 (not_126_out, OP5);
  not not_127 (not_127_out, F3);
  not not_128 (not_128_out, F4);
  not not_129 (not_129_out, OP0);
  not not_130 (not_130_out, OP1);
  not not_131 (not_131_out, OP3);
  not not_132 (not_132_out, OP4);
  not not_133 (not_133_out, OP5);
  not not_134 (not_134_out, OP1);
  not not_135 (not_135_out, OP3);
  not not_136 (not_136_out, OP4);
  not not_137 (not_137_out, OP5);
  not not_138 (not_138_out, OP0);
  not not_139 (not_139_out, OP1);
  not not_140 (not_140_out, OP2);
  not not_141 (not_141_out, OP3);
  not not_142 (not_142_out, OP4);
  not not_143 (not_143_out, OP5);
  not not_144 (not_144_out, F0);
  not not_145 (not_145_out, F1);
  not not_146 (not_146_out, F2);
  not not_147 (not_147_out, F4);
  not not_148 (not_148_out, F5);
  not not_149 (not_149_out, OP0);
  not not_150 (not_150_out, OP2);
  not not_151 (not_151_out, OP3);
  not not_152 (not_152_out, OP4);
  not not_153 (not_153_out, OP5);
  not not_154 (not_154_out, OP2);
  not not_155 (not_155_out, OP3);
  not not_156 (not_156_out, OP4);
  not not_157 (not_157_out, OP5);
  and and_1 (MemToReg, OP0, OP1, not_1_out, not_2_out, not_3_out, OP5);
  and and_2 (MemWrite, OP0, OP1, not_4_out, OP3, not_5_out, OP5);
  and and_3 (and_3_out, not_6_out, not_7_out, OP3, not_8_out, not_9_out);
  and and_4 (and_4_out, not_10_out, OP3, not_11_out, not_12_out);
  or or_1 (ALU_SRC, and_3_out, and_4_out, and_5_out);
  and and_5 (and_5_out, OP0, OP1, not_13_out, not_14_out, OP5);
  and and_6 (and_6_out, not_15_out, not_16_out, not_17_out, not_18_out, not_19_out, not_20_out, not_21_out, not_22_out, not_23_out);
  and and_7 (and_7_out, not_24_out, not_25_out, not_26_out, not_27_out, not_28_out, not_29_out, not_30_out, not_31_out, F5);
  and and_8 (and_8_out, not_32_out, not_33_out, not_34_out, not_35_out, not_36_out, F1, not_37_out, not_38_out, not_39_out, not_40_out);
  and and_9 (and_9_out, not_41_out, not_42_out, not_43_out, not_44_out, not_45_out, F1, not_46_out, F3, not_47_out, F5);
  and and_10 (and_10_out, not_48_out, not_49_out, not_50_out, not_51_out, not_52_out, F0, F2, not_53_out, not_54_out, F5);
  and and_11 (and_11_out, not_55_out, not_56_out, OP3, not_57_out, not_58_out);
  and and_12 (and_12_out, not_59_out, OP3, not_60_out, not_61_out);
  and and_13 (and_13_out, OP0, OP1, not_62_out, not_63_out, not_64_out);
  and and_14 (SysCALL, not_65_out, not_66_out, not_67_out, not_68_out, not_69_out, not_70_out, not_71_out, not_72_out, F2, F3, not_73_out, not_74_out);
  and and_15 (and_15_out, not_75_out, not_76_out, OP3, not_77_out, not_78_out);
  or or_2 (SignedExt, and_15_out, and_16_out, and_17_out);
  and and_16 (and_16_out, not_79_out, OP3, not_80_out, not_81_out);
  and and_17 (and_17_out, OP0, OP1, not_82_out, not_83_out, OP5);
  and and_18 (and_18_out, not_84_out, not_85_out, not_86_out, not_87_out, not_88_out, not_89_out, not_90_out, not_91_out, not_92_out, not_93_out);
  and and_19 (and_19_out, not_94_out, not_95_out, not_96_out, not_97_out, not_98_out, not_99_out, not_100_out, not_101_out, not_102_out, F5);
  and and_20 (and_20_out, not_103_out, not_104_out, not_105_out, not_106_out, not_107_out, not_108_out, F1, not_109_out, not_110_out, not_111_out, not_112_out);
  and and_21 (and_21_out, not_113_out, not_114_out, not_115_out, not_116_out, not_117_out, not_118_out, F1, not_119_out, F3, not_120_out, F5);
  and and_22 (and_22_out, not_121_out, not_122_out, not_123_out, not_124_out, not_125_out, not_126_out, F0, F2, not_127_out, not_128_out, F5);
  and and_23 (BEQ, not_129_out, not_130_out, OP2, not_131_out, not_132_out, not_133_out);
  and and_24 (BNE, OP0, not_134_out, OP2, not_135_out, not_136_out, not_137_out);
  and and_25 (JR, not_138_out, not_139_out, not_140_out, not_141_out, not_142_out, not_143_out, not_144_out, not_145_out, not_146_out, F3, not_147_out, not_148_out);
  and and_26 (JUMP, not_149_out, OP1, not_150_out, not_151_out, not_152_out, not_153_out);
  and and_27 (JAL, OP0, OP1, not_154_out, not_155_out, not_156_out, not_157_out);
  or or_3 (RegWrite, and_6_out, and_7_out, and_8_out, and_9_out, and_10_out, and_11_out, and_12_out, and_13_out);
  or or_4 (RegDst, and_18_out, and_19_out, and_20_out, and_21_out, and_22_out);
endmodule

// ALU
module MIPS_ALU (
  input  [4:0] shamt,
  input  [31:0] X,
  input  [31:0] Y,
  input  [3:0] AluOP,
  output Equal,
  output [31:0] Result,
  output [31:0] Result_2
);

  wire [0:0] comparator_1_lt, comparator_2_lt;
  wire [31:0] adder_1_out, AND_out, divider_1_out, divider_1_rem, multiplier_1_cout, multiplier_1_out,
       NOR_out, OR_out, shifter_1_out, shifter_2_out, shifter_3_out, subtractor_1_out, XOR_out;

  assign AND_out = X & Y;  // AND_Gate AND, 32 bits wide
  assign OR_out = X | Y;  // OR_Gate OR, 32 bits wide
  Shifter #(.width(32), .shift("ll")) shifter_1 (.in(Y), .\dist (shamt), .out(shifter_1_out));
  Shifter #(.width(32), .shift("ar")) shifter_2 (.in(Y), .\dist (shamt), .out(shifter_2_out));
  Shifter #(.width(32), .shift("lr")) shifter_3 (.in(Y), .\dist (shamt), .out(shifter_3_out));
  Multiplier #(.width(32)) multiplier_1 (.a(X), .b(Y), .out(multiplier_1_out), .cout(multiplier_1_cout));  // open: cin
  Divider #(.width(32)) divider_1 (.a(X), .b(Y), .out(divider_1_out), .rem(divider_1_rem));  // open: upper
  Adder #(.width(32)) adder_1 (.a(X), .b(Y), .out(adder_1_out));  // open: cin, cout
  Subtractor #(.width(32)) subtractor_1 (.a(X), .b(Y), .out(subtractor_1_out));  // open: bin, bout
  assign XOR_out = X ^ Y;  // XOR_Gate XOR, 32 bits wide
  assign NOR_out = ~(X | Y);  // NOR_Gate NOR, 32 bits wide
  Comparator #(.width(32), .mode("twosComplement")) comparator_1 (
    .a(X), .b(Y), .eq(Equal), .lt(comparator_1_lt[0]));  // open: gt
  Comparator #(.width(32), .mode("unsigned")) comparator_2 (.a(X), .b(Y), .lt(comparator_2_lt[0]));  // open: gt, eq
  Multiplexer #(.select(4), .width(32), .disabled("Z"), .enable("false")) multiplexer_1 (
    .in0(shifter_1_out), .in1(shifter_2_out), .in2(shifter_3_out), .in3(multiplier_1_out),
    .in4(divider_1_out), .in5(adder_1_out), .in6(subtractor_1_out), .in7(AND_out), .in8(OR_out),
    .in9(XOR_out), .in10(NOR_out), .in11({{31{1'b0}}, comparator_1_lt[0]}),
    .in12({{31{1'b0}}, comparator_2_lt[0]}), .in13({32{1'b0}}), .in14({32{1'b0}}), .in15({32{1'b0}}),
    .out(Result), .sel(AluOP));
  Multiplexer #(.select(4), .width(32), .disabled("Z"), .enable("false")) multiplexer_2 (
    .in0({32{1'b0}}), .in1({32{1'b0}}), .in2({32{1'b0}}), .in3(multiplier_1_cout), .in4(divider_1_rem),
    .in5({32{1'b0}}), .in6({32{1'b0}}), .in7({32{1'b0}}), .in8({32{1'b0}}), .in9({32{1'b0}}),
    .in10({32{1'b0}}), .in11({32{1'b0}}), .in12({32{1'b0}}), .in13({32{1'b0}}), .in14({32{1'b0}}),
    .in15({32{1'b0}}), .out(Result_2), .sel(AluOP));

  // Other names for the same wires on the sheet: Result2[31:0] = Result_2; S[3:0] = AluOP

  // Notes on the sheet:
  //   不要改变此引脚区域内容，也不要改变ALU封装形式
  //   输入引脚
  //   输出引脚
endmodule

module MIPS_Regifile (
  input  [31:0] Din,
  input  Clk,
  input  WE,
  input  [4:0] R1_num,
  input  [4:0] W_num,
  input  [4:0] R2_num,
  output [31:0] R1,
  output [31:0] R2
);

  // RegisterFile registerfile_1: pin names not known; wires that end beside it: Din, Clk, WE, W_num, R1_num, R2_num, R1, R2
endmodule

module \理想流水线  (
  output RegWrite,
  output MemWrite,
  output [31:0] IF_PC,
  output [31:0] ID_PC,
  output [31:0] EX_PC,
  output [31:0] M_PC,
  output [31:0] WB_PC,
  output [31:0] RDin,
  output [31:0] MDin,
  output [31:0] LedData
);

  wire CLK, clock_1_out, clock_2_out, comparator_1_eq, comparator_1_lt, d_ff_1_q, ERET, ex_mem_1_out_16,
       ex_mem_1_out_18, ex_mem_1_out_27, \ex_mem_1_传输状态out_表明当前传输数据有效 , Go, id_ex_1_out_33, id_ex_1_out_34,
       id_ex_1_out_35, id_ex_1_out_36, id_ex_1_out_47, \id_ex_1_传输状态out_表明当前传输数据有效 , IDSYSCALL,
       \if_id_1_传输状态out_表明当前传输数据有效 , IR1, IR2, IR3, JALSEL, JRSEL, JSEL, mem_wb_1_out_15, nand_1_out,
       not_1_out, not_2_out, RST, SignedExt, W1, W2, W3, WEHalt, \单周期硬布线控制器_1_alu_src ,
       \单周期硬布线控制器_1_memtoreg , \单周期硬布线控制器_1_memwrite , \单周期硬布线控制器_1_regdst , \单周期硬布线控制器_1_regwrite ;
  wire [3:0] id_ex_1_out_37, \单周期硬布线控制器_1_alu_op ;
  wire [4:0] FinalrW, id_ex_1_out_38, id_ex_1_out_44, IDrW;
  wire [12:0] CNT_num;
  wire [15:0] \LoadUse次数 , \总周期数 , \插入气泡数 , \无条件分支数 , \条件分支成功数 ;
  wire [25:0] target;
  wire [31:0] adder_1_out, bit_extender_1_out, bit_extender_2_out, EX_IR, ex_mem_1_out_22, ex_mem_1_out_25,
       id_ex_1_out_39, id_ex_1_out_40, id_ex_1_out_41, id_ex_1_out_45, ID_IR, IF_IR, MEM_IR, mem_wb_1_out_19,
       mem_wb_1_out_20, mips_alu_1_result, multiplexer_2_out, multiplexer_3_out, ram_1_data,
       registerfile_1_p8, rom_1_data, WB_IR;
  wire [31:26] if_id_1_out_8;

  Button \u_总复位  (.out(RST));
  Button _1 (.out(IR1));
  Button _2 (.out(IR2));
  Button _3 (.out(IR3));
  // Probe on \总周期数 
  // Probe on \总周期数 
  Button \u_继续运行  (.out(Go));
  LED #(.active("true")) led_1 (.in(W1));
  LED #(.active("true")) led_2 (.in(W2));
  LED #(.active("true")) led_3 (.in(W3));
  Hex_Digit_Display hex_digit_display_1 (.value(LedData[31:28]));  // open: dp
  // Probe on IF_PC[19:0]
  // Mips_Probe mips_probe_1: pin names not known; wires that end beside it: IF_IR
  not not_1 (not_1_out, WEHalt);
  Hex_Digit_Display hex_digit_display_2 (.value(LedData[27:24]));  // open: dp
  Hex_Digit_Display hex_digit_display_3 (.value(LedData[23:20]));  // open: dp
  // Probe on ID_PC[19:0]
  // Mips_Probe mips_probe_2: pin names not known; wires that end beside it: ID_IR
  Counter #(.width(16), .max('hffff), .ongoal("wrap"), .trigger("rising"), .behavior("old")) counter_1 (
    .count(not_1_out), .Q(\总周期数 ), .clk(CLK));  // open: load, D, carry, clr, preset
  Register #(.width(32), .trigger("rising"), .Select("low")) PC (
    .D(adder_1_out), .en(not_2_out), .Q(IF_PC), .clk(CLK));  // open: clr
  not not_2 (not_2_out, WEHalt);
  Hex_Digit_Display hex_digit_display_4 (.value(LedData[15:12]));  // open: dp
  Hex_Digit_Display hex_digit_display_5 (.value(LedData[19:16]));  // open: dp
  Hex_Digit_Display hex_digit_display_6 (.value(LedData[7:4]));  // open: dp
  Hex_Digit_Display hex_digit_display_7 (.value(LedData[11:8]));  // open: dp
  Clock #(.highDuration(1), .lowDuration(1)) clock_1 (.out(clock_1_out));
  // Probe on EX_PC[19:0]
  // Mips_Probe mips_probe_3: pin names not known; wires that end beside it: clock_1_out, EX_IR, CLK
  Adder #(.width(32)) adder_1 (.a(IF_PC), .b(32'h4), .out(adder_1_out));  // open: cin, cout
  Hex_Digit_Display hex_digit_display_8 (.value(LedData[3:0]));  // open: dp
  // Probe on \总周期数 
  // Probe on M_PC[19:0]
  // Mips_Probe mips_probe_4: pin names not known; wires that end beside it: MEM_IR
  // Probe on \总周期数 
  // Probe on \无条件分支数 
  // Probe on \条件分支成功数 
  // Probe on \插入气泡数 
  // Probe on \LoadUse次数 
  ROM #(.addrWidth(10), .dataWidth(32), .Select("high")) rom_1 (.addr(IF_PC[11:2]), .data(rom_1_data));
  // Probe on IF_PC[11:0]
  // Probe on WB_PC[19:0]
  // Mips_Probe mips_probe_5: pin names not known; wires that end beside it: WB_IR
  IF_ID if_id_1 (
    .PC(IF_PC), .\指令字 (rom_1_data), .\传输状态In_表明当前传输数据有效 (1'b1), .CLK(CLK), .out_7(ID_PC),
    .out_8({if_id_1_out_8, target}), .\传输状态Out_表明当前传输数据有效 (\if_id_1_传输状态out_表明当前传输数据有效 ),
    .\使能端_低电平有效_stall_高电平有效 (WEHalt));  // open: 同步清零_气泡_高电平有效
  // Probe on EX_PC[11:0]
  // Probe on ID_PC[11:0]
  // Probe on M_PC[11:0]
  D_Flip_Flop #(.trigger("high"), .Pre_Clr_Positions("LEGACY"), .NegatePresetClear("false"), .enable("true"), .NewFFLayout("false")) d_ff_1 (.Q(d_ff_1_q));  // open: clk, D, Qn, preset, en, reset
  // Probe on 13'hc
  // Probe on WB_PC[11:0]
  Comparator #(.width(13), .mode("twosComplement")) comparator_1 (
    .a(CNT_num), .b(13'hc), .eq(comparator_1_eq), .lt(comparator_1_lt));  // open: gt
  Clock #(.highDuration(1), .lowDuration(1)) clock_2 (.out(clock_2_out));
  nand nand_1 (nand_1_out, d_ff_1_q, comparator_1_eq);
  Counter #(.width(13), .max('h1fff), .ongoal("stay"), .trigger("rising"), .behavior("old")) counter_2 (
    .count(comparator_1_lt), .Q(CNT_num), .clk(clock_2_out));  // open: load, D, carry, clr, preset
  Multiplexer #(.select(1), .width(5), .disabled("Z"), .enable("false")) multiplexer_1 (
    .in0(target[20:16]), .in1(target[15:11]), .out(IDrW), .sel(\单周期硬布线控制器_1_regdst ));
  assign CLK = nand_1_out ? clock_2_out : 1'bz;  // Controlled_Buffer controlled_buffer_1
  \单周期硬布线控制器  \u_单周期硬布线控制器_1  (
    .Func(target[5:0]), .OP(if_id_1_out_8), .ALU_OP(\单周期硬布线控制器_1_alu_op ), .MemToReg(\单周期硬布线控制器_1_memtoreg ),
    .MemWrite(\单周期硬布线控制器_1_memwrite ), .ALU_SRC(\单周期硬布线控制器_1_alu_src ), .RegWrite(\单周期硬布线控制器_1_regwrite ),
    .SysCALL(IDSYSCALL), .SignedExt(SignedExt), .RegDst(\单周期硬布线控制器_1_regdst ), .JR(JRSEL), .JMP(JSEL),
    .JAL(JALSEL), ._25(target[25]), .ERET(ERET));  // open: Beq, Bne
  assign bit_extender_1_out = {{16{1'b0}}, target[15:0]};  // Bit_Extender bit_extender_1
  assign bit_extender_2_out = {{16{target[15]}}, target[15:0]};  // Bit_Extender bit_extender_2
  Pull_Resistor #(.pull(1)) pull_resistor_1 (.node(CLK));
  Multiplexer #(.select(1), .width(32), .disabled("Z"), .enable("false")) multiplexer_2 (
    .in0(bit_extender_1_out), .in1(bit_extender_2_out), .out(multiplexer_2_out), .sel(SignedExt));
  // RegisterFile registerfile_1: pin names not known; wires that end beside it: RDin, CLK, RegWrite, FinalrW, target[25:21], target[20:16], LedData, registerfile_1_p8
  ID_EX id_ex_1 (
    .ALUOP(\单周期硬布线控制器_1_alu_op ), .shamt(target[10:6]), .RegisterA(LedData),
    .Immediatenum(multiplexer_2_out), .PC(ID_PC), .\指令字 ({if_id_1_out_8, target}),
    .\传输状态In_表明当前传输数据有效 (\if_id_1_传输状态out_表明当前传输数据有效 ), .CLK(CLK), .out_37(id_ex_1_out_37),
    .out_38(id_ex_1_out_38), .out_39(id_ex_1_out_39), .out_41(id_ex_1_out_41), .out_43(EX_PC),
    .out_45(id_ex_1_out_45), .\传输状态Out_表明当前传输数据有效 (\id_ex_1_传输状态out_表明当前传输数据有效 ),
    .\使能端_低电平有效_stall_高电平有效 (WEHalt), .MemWrite(\单周期硬布线控制器_1_memwrite ), .out_36(id_ex_1_out_36),
    .RegWrite(\单周期硬布线控制器_1_regwrite ), .out_35(id_ex_1_out_35), .RegisterB(registerfile_1_p8),
    .out_40(id_ex_1_out_40), .AluSrcB(\单周期硬布线控制器_1_alu_src ), .out_34(id_ex_1_out_34),
    .MemToReg(\单周期硬布线控制器_1_memtoreg ), .out_33(id_ex_1_out_33), .finalrW(IDrW), .out_44(id_ex_1_out_44),
    .Halt(IDSYSCALL), .out_47(id_ex_1_out_47));  // open: 同步清零_气泡_高电平有效, Beq, out_31, Bne, out_32, JAL, out_30, JR, out_29, J, out_28, Target, out_27, BAddr, out_26, RetA, out_42
  Multiplexer #(.select(1), .width(32), .disabled("Z"), .enable("false")) multiplexer_3 (
    .in0(id_ex_1_out_40), .in1(id_ex_1_out_41), .out(multiplexer_3_out), .sel(id_ex_1_out_34));
  MIPS_ALU mips_alu_1 (
    .X(id_ex_1_out_39), .Y(multiplexer_3_out), .AluOP(id_ex_1_out_37), .Result(mips_alu_1_result),
    .shamt(id_ex_1_out_38));  // open: Equal, Result_2
  EX_MEM ex_mem_1 (
    .MemToReg(id_ex_1_out_33), .RegWrite(id_ex_1_out_35), .MemWrite(id_ex_1_out_36), .PC(EX_PC),
    .\指令字 (id_ex_1_out_45), .\传输状态In_表明当前传输数据有效 (\id_ex_1_传输状态out_表明当前传输数据有效 ), .CLK(CLK),
    .out_16(ex_mem_1_out_16), .out_18(ex_mem_1_out_18), .out_19(MemWrite), .out_24(M_PC),
    .out_25(ex_mem_1_out_25), .\传输状态Out_表明当前传输数据有效 (\ex_mem_1_传输状态out_表明当前传输数据有效 ),
    .\使能端_低电平有效_stall_高电平有效 (WEHalt), .AluResult(mips_alu_1_result), .out_22(ex_mem_1_out_22),
    .RegisterB(id_ex_1_out_40), .out_21(MDin), .out_27(ex_mem_1_out_27), .Halt(id_ex_1_out_47));  // open: 同步清零_气泡_高电平有效, finalrW, out_20, RetA, out_23, JAL, out_17
  RAM #(.addrWidth(10), .dataWidth(32), .bus("separate"), .Select("high")) ram_1 (
    .addr(ex_mem_1_out_22[11:2]), .din(MDin), .data(ram_1_data), .str(MemWrite), .clk(CLK));  // open: sel, ld, clr
  MEM_WB mem_wb_1 (
    .MemToReg(ex_mem_1_out_16), .RegWrite(ex_mem_1_out_18), .MemData(ram_1_data),
    .AluResult(ex_mem_1_out_22), .PC(M_PC), .\指令字 (ex_mem_1_out_25),
    .\传输状态In_表明当前传输数据有效 (\ex_mem_1_传输状态out_表明当前传输数据有效 ), .CLK(CLK), .out_15(mem_wb_1_out_15),
    .out_17(RegWrite), .out_19(mem_wb_1_out_19), .out_20(mem_wb_1_out_20), .out_22(WB_PC),
    .\使能端_低电平有效_stall_高电平有效 (WEHalt), .Halt(ex_mem_1_out_27), .out_25(WEHalt));  // open: out_23, 传输状态Out_表明当前传输数据有效, 同步清零_气泡_高电平有效, finalrW, out_18, RetA, out_21, JAL, out_16
  Multiplexer #(.select(1), .width(32), .disabled("Z"), .enable("false")) multiplexer_4 (
    .in0(mem_wb_1_out_20), .in1(mem_wb_1_out_19), .out(RDin), .sel(mem_wb_1_out_15));

  // Other names for the same wires on the sheet: FinalData[31:0] = RDin; MEM_PC[31:0] = M_PC

  // Notes on the sheet:
  //   中断源
  //   时空图监测，可删除
  //   中断等待指示
  //   数码管输出
  //   contents of rom_1 (hex, n*v repeats v):
  //   20100000 20110000 20120000 20130000 36100000 36310001 36520002 36730003 ae100000 ae110004 ae120008
  //   ae13000c 2002000a 20110000 20120000 20130000 c
  //   控制位
  //   OP
  //   rs
  //   指令字
  //   流水调试日志用
  //   暂停节拍，不能为0
  //   Func
  //   戳工具置1进入计数暂停模式，ctrl+k时钟自动运行到对应节拍暂停
  //   ctrl+k关闭时钟连续运行，将控制位置零，进入单步调试模式调试
  //   用这个时钟源需要去掉电路中的其他时钟源
  //   JMP
  //   JR
  //   OP
  //   Func
  //   可计数暂停的时钟源
  //   Beq
  //   Bne
  //   MemToReg
  //   MemWrite
  //   AluOP
  //   AluSrcB
  //   RegWrite
  //   JAL
  //   RegDst
  //   Syscall
  //   为方便自动评测，需要输出流水线各段保存的PC值，注意是PC不是PC+4，另外ID段寄存器写入信息，Mem段内存写入信息也要输出
endmodule

module \分支流水线  (
);

  wire and_1_out, and_2_out, BSEL, CLK, comparator_1_eq, ERET, ex_mem_1_out_16, ex_mem_1_out_18,
       ex_mem_1_out_19, \ex_mem_1_传输状态out_表明当前传输数据有效 , id_ex_1_out_31, id_ex_1_out_32, id_ex_1_out_33,
       id_ex_1_out_34, id_ex_1_out_35, id_ex_1_out_36, \id_ex_1_传输状态out_表明当前传输数据有效 , IDJ, IDJR,
       \if_id_1_传输状态out_表明当前传输数据有效 , JALSEL, JRSEL, JSEL, JUMP, mem_wb_1_out_15, mips_alu_1_equal,
       multiplexer_2_out, multiplexer_3_out, multiplexer_4_out, multiplexer_5_out, not_1_out, not_2_out,
       not_3_out, not_4_out, not_6_out, not_7_out, not_8_out, or_1_out, Regwrite, SignedExt, SYSCALL, WAITGO,
       WBRegwrite, \单周期硬布线控制器_1_alu_src , \单周期硬布线控制器_1_beq , \单周期硬布线控制器_1_bne , \单周期硬布线控制器_1_jal ,
       \单周期硬布线控制器_1_memtoreg , \单周期硬布线控制器_1_memwrite , \单周期硬布线控制器_1_regdst , \单周期硬布线控制器_1_regwrite ;
  wire [3:0] id_ex_1_out_37, \单周期硬布线控制器_1_alu_op ;
  wire [4:0] FinalrW, id_ex_1_out_38, id_ex_1_out_44, IDrA, IDrB, IDrW, WBFinalrW;
  wire [15:0] \总周期数 ;
  wire [25:0] IDtarget, JAddr;
  wire [31:0] adder_1_out, BAddr, bit_extender_1_out, bit_extender_2_out, controlled_buffer_1_out,
       controlled_buffer_4_out, ex_mem_1_out_21, ex_mem_1_out_22, ex_mem_1_out_24, ex_mem_1_out_25, EXPC,
       FinalData, id_ex_1_out_40, id_ex_1_out_41, id_ex_1_out_45, IDBAddr, if_id_1_out_7, JRAddr, LedData,
       mem_wb_1_out_19, mem_wb_1_out_20, mips_alu_1_result, multiplexer_1_out, multiplexer_10_out,
       multiplexer_13_out, PC_q, ram_1_data, registerfile_1_p7, registerfile_1_p8, RETA, rom_1_data,
       WBFinalData;
  wire [31:26] if_id_1_out_8;

  Clock #(.highDuration(1), .lowDuration(1)) clock_1 (.out(CLK));
  assign controlled_buffer_1_out = BSEL ? BAddr : 32'bz;  // Controlled_Buffer controlled_buffer_1
  assign controlled_buffer_1_out = or_1_out ? {EXPC[31:26], JAddr} : 32'bz;  // Controlled_Buffer controlled_buffer_2
  or or_1 (or_1_out, JSEL, JALSEL);
  assign controlled_buffer_1_out = JRSEL ? JRAddr : 32'bz;  // Controlled_Buffer controlled_buffer_3
  Multiplexer #(.select(1), .width(32), .disabled("Z"), .enable("false")) multiplexer_1 (
    .in0(adder_1_out), .in1(controlled_buffer_1_out), .out(multiplexer_1_out), .sel(JUMP));
  Register #(.width(32), .trigger("rising"), .Select("low")) PC (
    .D(multiplexer_1_out), .en(not_1_out), .Q(PC_q), .clk(CLK));  // open: clr
  not not_1 (not_1_out, multiplexer_2_out);
  Multiplexer #(.select(1), .width(1), .disabled("Z"), .enable("false")) multiplexer_2 (
    .in0(1'b0), .in1(WAITGO), .out(multiplexer_2_out), .sel(SYSCALL));
  Counter #(.width(16), .max('hffff), .ongoal("wrap"), .trigger("rising"), .behavior("old")) counter_1 (
    .count(not_2_out), .Q(\总周期数 ), .clk(CLK));  // open: load, D, carry, clr, preset
  not not_2 (not_2_out, multiplexer_3_out);
  Multiplexer #(.select(1), .width(1), .disabled("Z"), .enable("false")) multiplexer_3 (
    .in0(1'b0), .in1(WAITGO), .out(multiplexer_3_out), .sel(SYSCALL));
  Adder #(.width(32)) adder_1 (.a(PC_q), .b(32'h1), .out(adder_1_out));  // open: cin, cout
  ROM #(.addrWidth(10), .dataWidth(32), .Select("high")) rom_1 (.addr(PC_q[9:0]), .data(rom_1_data));
  not not_3 (not_3_out, multiplexer_4_out);
  Multiplexer #(.select(1), .width(1), .disabled("Z"), .enable("false")) multiplexer_4 (
    .in0(1'b0), .in1(WAITGO), .out(multiplexer_4_out), .sel(SYSCALL));
  Multiplexer #(.select(1), .width(1), .disabled("Z"), .enable("false")) multiplexer_5 (
    .in0(1'b0), .in1(1'b1), .out(multiplexer_5_out), .sel(not_3_out));
  IF_ID if_id_1 (
    .PC(PC_q), .\指令字 (rom_1_data), .\传输状态In_表明当前传输数据有效 (multiplexer_5_out), .CLK(CLK), .out_7(if_id_1_out_7),
    .out_8({if_id_1_out_8, IDtarget}), .\传输状态Out_表明当前传输数据有效 (\if_id_1_传输状态out_表明当前传输数据有效 ),
    .\同步清零_气泡_高电平有效 (JUMP), .\使能端_低电平有效_stall_高电平有效 (not_4_out));
  not not_4 (not_4_out, multiplexer_5_out);
  Multiplexer #(.select(1), .width(5), .disabled("Z"), .enable("false")) multiplexer_6 (
    .in0(IDtarget[25:21]), .in1(5'b00100), .out(IDrA), .sel(SYSCALL));
  Multiplexer #(.select(1), .width(5), .disabled("Z"), .enable("false")) multiplexer_7 (
    .in0(IDtarget[20:16]), .in1(5'b00010), .out(IDrB), .sel(SYSCALL));
  Multiplexer #(.select(1), .width(5), .disabled("Z"), .enable("false")) multiplexer_8 (
    .in0(IDtarget[20:16]), .in1(IDtarget[15:11]), .out(IDrW), .sel(\单周期硬布线控制器_1_regdst ));
  \单周期硬布线控制器  \u_单周期硬布线控制器_1  (
    .Func(IDtarget[5:0]), .OP(if_id_1_out_8), .ALU_OP(\单周期硬布线控制器_1_alu_op ),
    .MemToReg(\单周期硬布线控制器_1_memtoreg ), .MemWrite(\单周期硬布线控制器_1_memwrite ), .ALU_SRC(\单周期硬布线控制器_1_alu_src ),
    .RegWrite(\单周期硬布线控制器_1_regwrite ), .SysCALL(SYSCALL), .SignedExt(SignedExt),
    .RegDst(\单周期硬布线控制器_1_regdst ), .JR(IDJR), .JMP(IDJ), .Beq(\单周期硬布线控制器_1_beq ), .JAL(\单周期硬布线控制器_1_jal ),
    .Bne(\单周期硬布线控制器_1_bne ), ._25(IDtarget[25]), .ERET(ERET));
  assign bit_extender_1_out = {{16{1'b0}}, IDtarget[15:0]};  // Bit_Extender bit_extender_1
  assign bit_extender_2_out = {{16{IDtarget[15]}}, IDtarget[15:0]};  // Bit_Extender bit_extender_2
  Adder #(.width(32)) adder_2 (.a(32'h1), .b(if_id_1_out_7), .out(RETA));  // open: cin, cout
  Multiplexer #(.select(1), .width(1), .disabled("Z"), .enable("false")) multiplexer_9 (
    .in0(WBRegwrite), .in1(1'b1), .out(Regwrite), .sel(\单周期硬布线控制器_1_jal ));
  Multiplexer #(.select(1), .width(32), .disabled("Z"), .enable("false")) multiplexer_10 (
    .in0(bit_extender_1_out), .in1(bit_extender_2_out), .out(multiplexer_10_out), .sel(SignedExt));
  Adder #(.width(32)) adder_3 (.a(bit_extender_2_out), .b(RETA), .out(IDBAddr));  // open: cin, cout
  Multiplexer #(.select(1), .width(5), .disabled("Z"), .enable("false")) multiplexer_11 (
    .in0(WBFinalrW), .in1({5{1'b1}}), .out(FinalrW), .sel(\单周期硬布线控制器_1_jal ));
  // RegisterFile registerfile_1: pin names not known; wires that end beside it: FinalData, CLK, Regwrite, FinalrW, IDrA, IDrB, registerfile_1_p7, registerfile_1_p8
  Multiplexer #(.select(1), .width(32), .disabled("Z"), .enable("false")) multiplexer_12 (
    .in0(WBFinalData), .in1(RETA), .out(FinalData), .sel(\单周期硬布线控制器_1_jal ));
  assign controlled_buffer_4_out = comparator_1_eq ? registerfile_1_p7 : 32'bz;  // Controlled_Buffer controlled_buffer_4
  not not_5 (WAITGO, comparator_1_eq);
  Comparator #(.width(32), .mode("twosComplement")) comparator_1 (
    .a(32'h22), .b(registerfile_1_p8), .eq(comparator_1_eq));  // open: gt, lt
  Register #(.width(32), .trigger("rising"), .Select("low")) register_1 (
    .D(controlled_buffer_4_out), .Q(LedData), .clk(CLK));  // open: en, clr
  not not_6 (not_6_out, \if_id_1_传输状态out_表明当前传输数据有效 );
  ID_EX id_ex_1 (
    .ALUOP(\单周期硬布线控制器_1_alu_op ), .shamt(IDtarget[10:6]), .RegisterA(registerfile_1_p7),
    .Immediatenum(multiplexer_10_out), .PC(if_id_1_out_7), .\指令字 ({if_id_1_out_8, IDtarget}),
    .\传输状态In_表明当前传输数据有效 (\if_id_1_传输状态out_表明当前传输数据有效 ), .CLK(CLK), .out_37(id_ex_1_out_37),
    .out_38(id_ex_1_out_38), .out_39(JRAddr), .out_41(id_ex_1_out_41), .out_43(EXPC),
    .out_45(id_ex_1_out_45), .\传输状态Out_表明当前传输数据有效 (\id_ex_1_传输状态out_表明当前传输数据有效 ), .\同步清零_气泡_高电平有效 (JUMP),
    .\使能端_低电平有效_stall_高电平有效 (not_6_out), .MemWrite(\单周期硬布线控制器_1_memwrite ), .out_36(id_ex_1_out_36),
    .RegWrite(\单周期硬布线控制器_1_regwrite ), .out_35(id_ex_1_out_35), .RegisterB(registerfile_1_p8),
    .out_40(id_ex_1_out_40), .AluSrcB(\单周期硬布线控制器_1_alu_src ), .out_34(id_ex_1_out_34),
    .MemToReg(\单周期硬布线控制器_1_memtoreg ), .out_33(id_ex_1_out_33), .Beq(\单周期硬布线控制器_1_beq ),
    .out_31(id_ex_1_out_31), .Bne(\单周期硬布线控制器_1_bne ), .out_32(id_ex_1_out_32), .finalrW(IDrW),
    .out_44(id_ex_1_out_44), .JAL(\单周期硬布线控制器_1_jal ), .out_30(JALSEL), .JR(IDJR), .out_29(JRSEL), .J(IDJ),
    .out_28(JSEL), .Target(IDtarget), .out_27(JAddr), .BAddr(IDBAddr), .out_26(BAddr));  // open: Halt, out_47, RetA, out_42
  Multiplexer #(.select(1), .width(32), .disabled("Z"), .enable("false")) multiplexer_13 (
    .in0(id_ex_1_out_40), .in1(id_ex_1_out_41), .out(multiplexer_13_out), .sel(id_ex_1_out_34));
  and and_1 (and_1_out, id_ex_1_out_31, mips_alu_1_equal);
  MIPS_ALU mips_alu_1 (
    .X(JRAddr), .Y(multiplexer_13_out), .AluOP(id_ex_1_out_37), .Equal(mips_alu_1_equal),
    .Result(mips_alu_1_result), .shamt(id_ex_1_out_38));  // open: Result_2
  or or_2 (BSEL, and_1_out, and_2_out);
  and and_2 (and_2_out, id_ex_1_out_32, ~mips_alu_1_equal);  // AND_Gate
  or or_3 (JUMP, JSEL, JRSEL, JALSEL, BSEL);
  not not_7 (not_7_out, \id_ex_1_传输状态out_表明当前传输数据有效 );
  EX_MEM ex_mem_1 (
    .MemToReg(id_ex_1_out_33), .RegWrite(id_ex_1_out_35), .MemWrite(id_ex_1_out_36), .PC(EXPC),
    .\指令字 (id_ex_1_out_45), .\传输状态In_表明当前传输数据有效 (\id_ex_1_传输状态out_表明当前传输数据有效 ), .CLK(CLK),
    .out_16(ex_mem_1_out_16), .out_18(ex_mem_1_out_18), .out_19(ex_mem_1_out_19), .out_24(ex_mem_1_out_24),
    .out_25(ex_mem_1_out_25), .\传输状态Out_表明当前传输数据有效 (\ex_mem_1_传输状态out_表明当前传输数据有效 ),
    .\使能端_低电平有效_stall_高电平有效 (not_7_out), .AluResult(mips_alu_1_result), .out_22(ex_mem_1_out_22),
    .RegisterB(id_ex_1_out_40), .out_21(ex_mem_1_out_21));  // open: 同步清零_气泡_高电平有效, finalrW, out_20, out_27, Halt, RetA, out_23, JAL, out_17
  RAM #(.addrWidth(10), .dataWidth(32), .bus("separate"), .Select("high")) ram_1 (
    .addr(ex_mem_1_out_22[11:2]), .din(ex_mem_1_out_21), .data(ram_1_data), .str(ex_mem_1_out_19), .clk(CLK));  // open: sel, ld, clr
  not not_8 (not_8_out, \ex_mem_1_传输状态out_表明当前传输数据有效 );
  MEM_WB mem_wb_1 (
    .MemToReg(ex_mem_1_out_16), .RegWrite(ex_mem_1_out_18), .MemData(ram_1_data),
    .AluResult(ex_mem_1_out_22), .PC(ex_mem_1_out_24), .\指令字 (ex_mem_1_out_25),
    .\传输状态In_表明当前传输数据有效 (\ex_mem_1_传输状态out_表明当前传输数据有效 ), .CLK(CLK), .out_15(mem_wb_1_out_15),
    .out_17(WBRegwrite), .out_19(mem_wb_1_out_19), .out_20(mem_wb_1_out_20),
    .\使能端_低电平有效_stall_高电平有效 (not_8_out));  // open: out_22, out_23, 传输状态Out_表明当前传输数据有效, 同步清零_气泡_高电平有效, finalrW, out_18, Halt, out_25, RetA, out_21, JAL, out_16
  Multiplexer #(.select(1), .width(32), .disabled("Z"), .enable("false")) multiplexer_14 (
    .in0(mem_wb_1_out_20), .in1(mem_wb_1_out_19), .out(WBFinalData), .sel(mem_wb_1_out_15));

  // Other names for the same wires on the sheet: target[25:0] = JAddr; JAddr[31:26] = EXPC[31:26]

  // Notes on the sheet:
  //   contents of rom_1 (hex, n*v repeats v):
  //   20110020 20020022 8000006 20110004 20120005 20130006 10000003 20110007 20120008 20130009 14110003
  //   2011000a 2012000b 2013000c c000014 2002000a 0 0 0 c 2231ffff 0 0 0 112020 0 0 0 c 1620fff6 3e00008
  //   OP
  //   rs
  //   指令字
  //   JMP
  //   JR
  //   OP
  //   Func
  //   Beq
  //   Bne
  //   MemToReg
  //   MemWrite
  //   AluOP
  //   AluSrcB
  //   RegWrite
  //   JAL
  //   RegDst
  //   Syscall
endmodule

module \数据相关寄存器使用情况  (
  input  [5:0] OP,
  input  [5:0] FUNC,
  output rAUsed,
  output rBUsed
);

  \寄存器使用情况子电路  \u_寄存器使用情况子电路_1  (
    .OP0(OP[0]), .OP1(OP[1]), .OP2(OP[2]), .OP3(OP[3]), .OP4(OP[4]), .OP5(OP[5]), .F0(FUNC[0]), .F1(FUNC[1]),
    .F2(FUNC[2]), .F3(FUNC[3]), .F4(FUNC[4]), .F5(FUNC[5]), .rA(rAUsed), .rB(rBUsed));
endmodule

module \寄存器使用情况子电路  (
  input  OP0,
  input  OP1,
  input  OP2,
  input  OP3,
  input  OP4,
  input  OP5,
  input  F0,
  input  F1,
  input  F2,
  input  F3,
  input  F4,
  input  F5,
  output rA,
  output rB
);

  wire and_1_out, and_2_out, and_3_out, and_4_out, and_5_out, and_6_out, and_7_out, and_8_out, and_9_out,
       and_10_out, and_11_out, and_12_out, and_13_out, and_14_out, and_15_out, and_16_out, and_17_out,
       not_1_out, not_2_out, not_3_out, not_4_out, not_5_out, not_6_out, not_7_out, not_8_out, not_9_out,
       not_10_out, not_11_out, not_12_out, not_13_out, not_14_out, not_15_out, not_16_out, not_17_out,
       not_18_out, not_19_out, not_20_out, not_21_out, not_22_out, not_23_out, not_24_out, not_25_out,
       not_26_out, not_27_out, not_28_out, not_29_out, not_30_out, not_31_out, not_32_out, not_33_out,
       not_34_out, not_35_out, not_36_out, not_37_out, not_38_out, not_39_out, not_40_out, not_41_out,
       not_42_out, not_43_out, not_44_out, not_45_out, not_46_out, not_47_out, not_48_out, not_49_out,
       not_50_out, not_51_out, not_52_out, not_53_out, not_54_out, not_55_out, not_56_out, not_57_out,
       not_58_out, not_59_out, not_60_out, not_61_out, not_62_out, not_63_out, not_64_out, not_65_out,
       not_66_out, not_67_out, not_68_out, not_69_out, not_70_out, not_71_out, not_72_out, not_73_out,
       not_74_out, not_75_out, not_76_out, not_77_out, not_78_out, not_79_out, not_80_out, not_81_out,
       not_82_out, not_83_out, not_84_out, not_85_out, not_86_out, not_87_out, not_88_out, not_89_out,
       not_90_out, not_91_out, not_92_out, not_93_out, not_94_out, not_95_out, not_96_out, not_97_out,
       not_98_out, not_99_out, not_100_out, not_101_out, not_102_out;

  not not_1 (not_1_out, OP0);
  not not_2 (not_2_out, OP1);
  not not_3 (not_3_out, OP4);
  not not_4 (not_4_out, OP5);
  not not_5 (not_5_out, F0);
  not not_6 (not_6_out, F2);
  not not_7 (not_7_out, F3);
  not not_8 (not_8_out, F4);
  not not_9 (not_9_out, OP0);
  not not_10 (not_10_out, OP1);
  not not_11 (not_11_out, OP4);
  not not_12 (not_12_out, OP5);
  not not_13 (not_13_out, F1);
  not not_14 (not_14_out, F3);
  not not_15 (not_15_out, F4);
  not not_16 (not_16_out, OP0);
  not not_17 (not_17_out, OP1);
  not not_18 (not_18_out, OP4);
  not not_19 (not_19_out, OP5);
  not not_20 (not_20_out, F0);
  not not_21 (not_21_out, F1);
  not not_22 (not_22_out, F4);
  not not_23 (not_23_out, F5);
  not not_24 (not_24_out, OP0);
  not not_25 (not_25_out, OP1);
  not not_26 (not_26_out, OP4);
  not not_27 (not_27_out, OP5);
  not not_28 (not_28_out, F2);
  not not_29 (not_29_out, F4);
  not not_30 (not_30_out, OP0);
  not not_31 (not_31_out, OP1);
  not not_32 (not_32_out, OP4);
  not not_33 (not_33_out, OP5);
  not not_34 (not_34_out, F3);
  not not_35 (not_35_out, F4);
  not not_36 (not_36_out, OP0);
  not not_37 (not_37_out, OP2);
  not not_38 (not_38_out, OP4);
  not not_39 (not_39_out, OP5);
  not not_40 (not_40_out, OP1);
  not not_41 (not_41_out, OP4);
  not not_42 (not_42_out, OP5);
  not not_43 (not_43_out, OP1);
  not not_44 (not_44_out, OP4);
  not not_45 (not_45_out, OP5);
  not not_46 (not_46_out, OP2);
  not not_47 (not_47_out, OP4);
  not not_48 (not_48_out, OP0);
  not not_49 (not_49_out, OP1);
  not not_50 (not_50_out, OP3);
  not not_51 (not_51_out, OP4);
  not not_52 (not_52_out, OP5);
  not not_53 (not_53_out, F0);
  not not_54 (not_54_out, F2);
  not not_55 (not_55_out, F3);
  not not_56 (not_56_out, F4);
  not not_57 (not_57_out, OP0);
  not not_58 (not_58_out, OP1);
  not not_59 (not_59_out, OP3);
  not not_60 (not_60_out, OP4);
  not not_61 (not_61_out, OP5);
  not not_62 (not_62_out, F1);
  not not_63 (not_63_out, F3);
  not not_64 (not_64_out, F4);
  not not_65 (not_65_out, OP0);
  not not_66 (not_66_out, OP1);
  not not_67 (not_67_out, OP3);
  not not_68 (not_68_out, OP4);
  not not_69 (not_69_out, OP5);
  not not_70 (not_70_out, F0);
  not not_71 (not_71_out, F1);
  not not_72 (not_72_out, F4);
  not not_73 (not_73_out, F5);
  not not_74 (not_74_out, OP0);
  not not_75 (not_75_out, OP1);
  not not_76 (not_76_out, OP3);
  not not_77 (not_77_out, OP4);
  not not_78 (not_78_out, OP5);
  not not_79 (not_79_out, F2);
  not not_80 (not_80_out, F3);
  not not_81 (not_81_out, F4);
  not not_82 (not_82_out, F5);
  not not_83 (not_83_out, OP0);
  not not_84 (not_84_out, OP1);
  not not_85 (not_85_out, OP3);
  not not_86 (not_86_out, OP4);
  not not_87 (not_87_out, OP5);
  not not_88 (not_88_out, F2);
  not not_89 (not_89_out, F4);
  not not_90 (not_90_out, OP0);
  not not_91 (not_91_out, OP1);
  not not_92 (not_92_out, OP3);
  not not_93 (not_93_out, OP4);
  not not_94 (not_94_out, OP5);
  not not_95 (not_95_out, F3);
  not not_96 (not_96_out, F4);
  not not_97 (not_97_out, OP1);
  not not_98 (not_98_out, OP3);
  not not_99 (not_99_out, OP4);
  not not_100 (not_100_out, OP5);
  not not_101 (not_101_out, OP2);
  not not_102 (not_102_out, OP4);
  and and_1 (and_1_out, not_1_out, not_2_out, not_3_out, not_4_out, not_5_out, not_6_out, not_7_out, not_8_out, F5);
  and and_2 (and_2_out, not_9_out, not_10_out, not_11_out, not_12_out, not_13_out, not_14_out, not_15_out, F5);
  and and_3 (and_3_out, not_16_out, not_17_out, not_18_out, not_19_out, not_20_out, not_21_out, F3, not_22_out, not_23_out);
  and and_4 (and_4_out, not_24_out, not_25_out, not_26_out, not_27_out, F1, not_28_out, F3, not_29_out, F5);
  and and_5 (and_5_out, not_30_out, not_31_out, not_32_out, not_33_out, F0, F2, not_34_out, not_35_out, F5);
  and and_6 (and_6_out, not_36_out, not_37_out, OP3, not_38_out, not_39_out);
  and and_7 (and_7_out, not_40_out, OP3, not_41_out, not_42_out);
  and and_8 (and_8_out, not_43_out, OP2, not_44_out, not_45_out);
  and and_9 (and_9_out, OP0, OP1, not_46_out, not_47_out, OP5);
  and and_10 (and_10_out, not_48_out, not_49_out, not_50_out, not_51_out, not_52_out, not_53_out, not_54_out, not_55_out, not_56_out);
  and and_11 (and_11_out, not_57_out, not_58_out, not_59_out, not_60_out, not_61_out, not_62_out, not_63_out, not_64_out, F5);
  and and_12 (and_12_out, not_65_out, not_66_out, not_67_out, not_68_out, not_69_out, not_70_out, not_71_out, F2, F3, not_72_out, not_73_out);
  and and_13 (and_13_out, not_74_out, not_75_out, not_76_out, not_77_out, not_78_out, F1, not_79_out, not_80_out, not_81_out, not_82_out);
  and and_14 (and_14_out, not_83_out, not_84_out, not_85_out, not_86_out, not_87_out, F1, not_88_out, F3, not_89_out, F5);
  and and_15 (and_15_out, not_90_out, not_91_out, not_92_out, not_93_out, not_94_out, F0, F2, not_95_out, not_96_out, F5);
  and and_16 (and_16_out, not_97_out, OP2, not_98_out, not_99_out, not_100_out);
  and and_17 (and_17_out, OP0, OP1, not_101_out, OP3, not_102_out, OP5);
  or or_1 (rA, and_1_out, and_2_out, and_3_out, and_4_out, and_5_out, and_6_out, and_7_out, and_8_out, and_9_out);
  or or_2 (rB, and_10_out, and_11_out, and_12_out, and_13_out, and_14_out, and_15_out, and_16_out, and_17_out);
endmodule

module \气泡流水线  (
  output RegWrite,
  output MemWrite,
  output [31:0] IF_PC,
  output [31:0] ID_PC,
  output [31:0] EX_PC,
  output [31:0] M_PC,
  output [31:0] WB_PC,
  output [31:0] RDin,
  output [31:0] MDin,
  output [31:0] LedData
);

  wire and_1_out, and_2_out, and_3_out, and_4_out, and_5_out, and_6_out, and_7_out, and_8_out, and_9_out,
       BSEL, CLK, clock_1_out, comparator_1_eq, comparator_1_lt, comparator_2_eq, comparator_3_eq,
       comparator_4_eq, comparator_5_eq, comparator_6_eq, comparator_7_eq, comparator_8_eq, d_ff_1_q,
       Datalocked, ERET, ex_mem_1_out_16, ex_mem_1_out_17, ex_mem_1_out_18, ex_mem_1_out_27,
       \ex_mem_1_传输状态out_表明当前传输数据有效 , Go, id_ex_1_out_31, id_ex_1_out_32, id_ex_1_out_33, id_ex_1_out_34,
       id_ex_1_out_35, id_ex_1_out_36, id_ex_1_out_47, \id_ex_1_传输状态out_表明当前传输数据有效 , IDJ, IDJR, IDrAUsed,
       IDrBUsed, IDSYSCALL, \if_id_1_传输状态out_表明当前传输数据有效 , IR1, IR2, IR3, JALSEL, JRSEL, JSEL, JUMP,
       mips_alu_1_equal, multiplexer_7_out, multiplexer_8_out, multiplexer_9_out, multiplexer_10_out,
       nand_1_out, not_1_out, not_2_out, not_3_out, not_4_out, not_5_out, not_6_out, not_8_out, not_9_out,
       or_1_out, or_2_out, or_3_out, or_4_out, or_5_out, or_8_out, or_10_out, RST, SignedExt, W1, W2, W3,
       WAITGO, WBHalt, \单周期硬布线控制器_1_alu_src , \单周期硬布线控制器_1_beq , \单周期硬布线控制器_1_bne , \单周期硬布线控制器_1_memtoreg ,
       \单周期硬布线控制器_1_memwrite , \单周期硬布线控制器_1_regwrite ;
  wire [1:0] mem_wb_1_out_16, \单周期硬布线控制器_1_jal ;
  wire [3:0] id_ex_1_out_37, \单周期硬布线控制器_1_alu_op ;
  wire [4:0] EXrW, id_ex_1_out_38, IDrA, IDrB, IDrW, MEMrW, WBFinalrW;
  wire [12:0] CNT_num;
  wire [15:0] \LoadUse次数 , \总周期数 , \插入气泡数 , \无条件分支数 , \条件分支成功数 ;
  wire [27:2] JAddr;
  wire [31:0] adder_1_out, BAddr, bit_extender_1_out, bit_extender_2_out, controlled_buffer_1_out,
       controlled_buffer_5_out, EX_IR, ex_mem_1_out_22, ex_mem_1_out_23, id_ex_1_out_40, id_ex_1_out_41,
       id_ex_1_out_42, ID_IR, IDBAddr, IF_IR, JRAddr, MEM_IR, mem_wb_1_out_19, mem_wb_1_out_20,
       mem_wb_1_out_21, mips_alu_1_result, multiplexer_1_out, multiplexer_5_out, multiplexer_6_out,
       ram_1_data, registerfile_1_p7, registerfile_1_p8, RETA, shifter_1_out, WB_IR;

  Button \u_总复位  (.out(RST));
  Button _1 (.out(IR1));
  Button _2 (.out(IR2));
  Button _3 (.out(IR3));
  // Probe on \总周期数 
  // Probe on \总周期数 
  Button \u_继续运行  (.out(Go));
  LED #(.active("true")) led_1 (.in(W1));
  LED #(.active("true")) led_2 (.in(W2));
  LED #(.active("true")) led_3 (.in(W3));
  Hex_Digit_Display hex_digit_display_1 (.value(LedData[31:28]));  // open: dp
  // Probe on IF_PC[19:0]
  // Mips_Probe mips_probe_1: pin names not known; wires that end beside it: IF_IR
  Hex_Digit_Display hex_digit_display_2 (.value(LedData[27:24]));  // open: dp
  Hex_Digit_Display hex_digit_display_3 (.value(LedData[23:20]));  // open: dp
  // Probe on ID_PC[19:0]
  // Mips_Probe mips_probe_2: pin names not known; wires that end beside it: ID_IR
  Hex_Digit_Display hex_digit_display_4 (.value(LedData[15:12]));  // open: dp
  Hex_Digit_Display hex_digit_display_5 (.value(LedData[19:16]));  // open: dp
  assign controlled_buffer_1_out = BSEL ? BAddr : 32'bz;  // Controlled_Buffer controlled_buffer_1
  assign controlled_buffer_1_out = or_1_out ? {EX_PC[31:28], JAddr, 2'b00} : 32'bz;  // Controlled_Buffer controlled_buffer_2
  or or_1 (or_1_out, JSEL, JALSEL);
  assign controlled_buffer_1_out = JRSEL ? JRAddr : 32'bz;  // Controlled_Buffer controlled_buffer_3
  Hex_Digit_Display hex_digit_display_6 (.value(LedData[7:4]));  // open: dp
  Hex_Digit_Display hex_digit_display_7 (.value(LedData[11:8]));  // open: dp
  // Probe on EX_PC[19:0]
  // Mips_Probe mips_probe_3: pin names not known; wires that end beside it: EX_IR
  Multiplexer #(.select(1), .width(32), .disabled("Z"), .enable("false")) multiplexer_1 (
    .in0(adder_1_out), .in1(controlled_buffer_1_out), .out(multiplexer_1_out), .sel(JUMP));
  Hex_Digit_Display hex_digit_display_8 (.value(LedData[3:0]));  // open: dp
  not not_1 (not_1_out, or_2_out);
  or or_2 (or_2_out, and_1_out, WBHalt);
  and and_1 (and_1_out, not_2_out, Datalocked);
  not not_2 (not_2_out, JUMP);
  // Probe on \总周期数 
  // Probe on M_PC[19:0]
  // Mips_Probe mips_probe_4: pin names not known; wires that end beside it: MEM_IR
  Register #(.width(32), .trigger("rising"), .Select("low")) PC (
    .D(multiplexer_1_out), .en(not_1_out), .Q(IF_PC), .clk(CLK));  // open: clr
  // Probe on \总周期数 
  // Probe on \无条件分支数 
  // Probe on \条件分支成功数 
  // Probe on \插入气泡数 
  // Probe on \LoadUse次数 
  // Probe on IF_PC[11:0]
  // Probe on WB_PC[19:0]
  // Mips_Probe mips_probe_5: pin names not known; wires that end beside it: WB_IR
  Adder #(.width(32)) adder_1 (.a(IF_PC), .b(32'h4), .out(adder_1_out));  // open: cin, cout
  // Probe on ID_PC[11:0]
  // Probe on EX_PC[11:0]
  // Probe on M_PC[11:0]
  D_Flip_Flop #(.trigger("high"), .Pre_Clr_Positions("LEGACY"), .NegatePresetClear("false"), .enable("true"), .NewFFLayout("false")) d_ff_1 (.Q(d_ff_1_q));  // open: clk, D, Qn, preset, en, reset
  // Probe on 13'h20
  ROM #(.addrWidth(10), .dataWidth(32), .Select("high")) rom_1 (.addr(IF_PC[11:2]), .data(IF_IR));
  not not_3 (not_3_out, JUMP);
  // Probe on WB_PC[11:0]
  Comparator #(.width(13), .mode("twosComplement")) comparator_1 (
    .a(CNT_num), .b(13'h20), .eq(comparator_1_eq), .lt(comparator_1_lt));  // open: gt
  Clock #(.highDuration(1), .lowDuration(1)) clock_1 (.out(clock_1_out));
  or or_3 (or_3_out, and_2_out, WBHalt);
  and and_2 (and_2_out, not_3_out, Datalocked);
  nand nand_1 (nand_1_out, d_ff_1_q, comparator_1_eq);
  Counter #(.width(13), .max('h1fff), .ongoal("stay"), .trigger("rising"), .behavior("old")) counter_1 (
    .count(comparator_1_lt), .Q(CNT_num), .clk(clock_1_out));  // open: load, D, carry, clr, preset
  IF_ID if_id_1 (
    .PC(IF_PC), .\指令字 (IF_IR), .\传输状态In_表明当前传输数据有效 (1'b1), .CLK(CLK), .out_7(ID_PC), .out_8(ID_IR),
    .\传输状态Out_表明当前传输数据有效 (\if_id_1_传输状态out_表明当前传输数据有效 ), .\同步清零_气泡_高电平有效 (JUMP),
    .\使能端_低电平有效_stall_高电平有效 (or_3_out));
  assign CLK = nand_1_out ? clock_1_out : 1'bz;  // Controlled_Buffer controlled_buffer_4
  \数据相关寄存器使用情况  \u_数据相关寄存器使用情况_1  (.OP(ID_IR[31:26]), .FUNC(ID_IR[5:0]), .rAUsed(IDrAUsed), .rBUsed(IDrBUsed));
  Pull_Resistor #(.pull(1)) pull_resistor_1 (.node(CLK));
  Multiplexer #(.select(1), .width(5), .disabled("Z"), .enable("false")) multiplexer_2 (
    .in0(ID_IR[25:21]), .in1(5'b00100), .out(IDrA), .sel(IDSYSCALL));
  Multiplexer #(.select(1), .width(5), .disabled("Z"), .enable("false")) multiplexer_3 (
    .in0(ID_IR[20:16]), .in1(5'b00010), .out(IDrB), .sel(IDSYSCALL));
  not not_4 (not_4_out, WBHalt);
  \单周期硬布线控制器  \u_单周期硬布线控制器_1  (
    .Func(ID_IR[5:0]), .OP(ID_IR[31:26]), .ALU_OP(\单周期硬布线控制器_1_alu_op ), .MemToReg(\单周期硬布线控制器_1_memtoreg ),
    .MemWrite(\单周期硬布线控制器_1_memwrite ), .ALU_SRC(\单周期硬布线控制器_1_alu_src ), .RegWrite(\单周期硬布线控制器_1_regwrite ),
    .SysCALL(IDSYSCALL), .SignedExt(SignedExt), .RegDst(\单周期硬布线控制器_1_jal [1]), .JR(IDJR), .JMP(IDJ),
    .Beq(\单周期硬布线控制器_1_beq ), .JAL(\单周期硬布线控制器_1_jal [0]), .Bne(\单周期硬布线控制器_1_bne ), ._25(ID_IR[25]), .ERET(ERET));
  Multiplexer #(.select(2), .width(5), .disabled("Z"), .enable("false")) multiplexer_4 (
    .in0(ID_IR[20:16]), .in1({5{1'b1}}), .in2(ID_IR[15:11]), .in3({5{1'b1}}), .out(IDrW),
    .sel(\单周期硬布线控制器_1_jal ));
  assign bit_extender_1_out = {{16{ID_IR[15]}}, ID_IR[15:0]};  // Bit_Extender bit_extender_1
  Adder #(.width(32)) adder_2 (.a(32'h4), .b(ID_PC), .out(RETA));  // open: cin, cout
  Counter #(.width(16), .max('hffff), .ongoal("wrap"), .trigger("rising"), .behavior("old")) counter_2 (
    .count(not_4_out), .Q(\总周期数 ), .clk(CLK));  // open: load, D, carry, clr, preset
  assign bit_extender_2_out = {{16{1'b0}}, ID_IR[15:0]};  // Bit_Extender bit_extender_2
  Shifter #(.width(32), .shift("ll")) shifter_1 (.in(bit_extender_1_out), .\dist (5'b00010), .out(shifter_1_out));
  Multiplexer #(.select(1), .width(32), .disabled("Z"), .enable("false")) multiplexer_5 (
    .in0(bit_extender_2_out), .in1(bit_extender_1_out), .out(multiplexer_5_out), .sel(SignedExt));
  and and_3 (and_3_out, Datalocked, not_5_out);
  not not_5 (not_5_out, WBHalt);
  Adder #(.width(32)) adder_3 (.a(shifter_1_out), .b(RETA), .out(IDBAddr));  // open: cin, cout
  Counter #(.width(16), .max('hffff), .ongoal("wrap"), .trigger("rising"), .behavior("old")) counter_3 (
    .count(and_3_out), .Q(\插入气泡数 ), .clk(CLK));  // open: load, D, carry, clr, preset
  // RegisterFile registerfile_1: pin names not known; wires that end beside it: RDin, CLK, RegWrite, WBFinalrW, IDrA, IDrB, registerfile_1_p7, registerfile_1_p8
  or or_4 (or_4_out, JRSEL, JSEL, JALSEL);
  not not_6 (not_6_out, Datalocked);
  Comparator #(.width(32), .mode("twosComplement")) comparator_2 (
    .a(32'h22), .b(registerfile_1_p8), .eq(comparator_2_eq));  // open: gt, lt
  Counter #(.width(16), .max('hffff), .ongoal("wrap"), .trigger("rising"), .behavior("old")) counter_4 (
    .count(or_4_out), .Q(\无条件分支数 ), .clk(CLK));  // open: load, D, carry, clr, preset
  assign controlled_buffer_5_out = and_4_out ? registerfile_1_p7 : 32'bz;  // Controlled_Buffer controlled_buffer_5
  Register #(.width(32), .trigger("rising"), .Select("low")) register_1 (
    .D(controlled_buffer_5_out), .Q(LedData), .clk(CLK));  // open: en, clr
  and and_4 (and_4_out, not_6_out, comparator_2_eq);
  not not_7 (WAITGO, comparator_2_eq);
  and and_5 (and_5_out, IDSYSCALL, WAITGO);
  Counter #(.width(16), .max('hffff), .ongoal("wrap"), .trigger("rising"), .behavior("old")) counter_5 (
    .count(BSEL), .Q(\条件分支成功数 ), .clk(CLK));  // open: load, D, carry, clr, preset
  or or_5 (or_5_out, JUMP, Datalocked);
  ID_EX id_ex_1 (
    .ALUOP(\单周期硬布线控制器_1_alu_op ), .shamt(ID_IR[10:6]), .RegisterA(registerfile_1_p7),
    .Immediatenum(multiplexer_5_out), .PC(ID_PC), .\指令字 (ID_IR),
    .\传输状态In_表明当前传输数据有效 (\if_id_1_传输状态out_表明当前传输数据有效 ), .CLK(CLK), .out_37(id_ex_1_out_37),
    .out_38(id_ex_1_out_38), .out_39(JRAddr), .out_41(id_ex_1_out_41), .out_43(EX_PC), .out_45(EX_IR),
    .\传输状态Out_表明当前传输数据有效 (\id_ex_1_传输状态out_表明当前传输数据有效 ), .\同步清零_气泡_高电平有效 (or_5_out),
    .\使能端_低电平有效_stall_高电平有效 (WBHalt), .MemWrite(\单周期硬布线控制器_1_memwrite ), .out_36(id_ex_1_out_36),
    .RegWrite(\单周期硬布线控制器_1_regwrite ), .out_35(id_ex_1_out_35), .RegisterB(registerfile_1_p8),
    .out_40(id_ex_1_out_40), .AluSrcB(\单周期硬布线控制器_1_alu_src ), .out_34(id_ex_1_out_34),
    .MemToReg(\单周期硬布线控制器_1_memtoreg ), .out_33(id_ex_1_out_33), .Beq(\单周期硬布线控制器_1_beq ),
    .out_31(id_ex_1_out_31), .Bne(\单周期硬布线控制器_1_bne ), .out_32(id_ex_1_out_32), .finalrW(IDrW), .out_44(EXrW),
    .JAL(\单周期硬布线控制器_1_jal [0]), .out_30(JALSEL), .JR(IDJR), .out_29(JRSEL), .J(IDJ), .out_28(JSEL),
    .Target(ID_IR[25:0]), .out_27(JAddr), .BAddr(IDBAddr), .out_26(BAddr), .Halt(and_5_out),
    .out_47(id_ex_1_out_47), .RetA(RETA), .out_42(id_ex_1_out_42));
  Multiplexer #(.select(1), .width(32), .disabled("Z"), .enable("false")) multiplexer_6 (
    .in0(id_ex_1_out_40), .in1(id_ex_1_out_41), .out(multiplexer_6_out), .sel(id_ex_1_out_34));
  or or_6 (BSEL, and_6_out, and_7_out);
  and and_6 (and_6_out, id_ex_1_out_31, mips_alu_1_equal);
  MIPS_ALU mips_alu_1 (
    .X(JRAddr), .Y(multiplexer_6_out), .AluOP(id_ex_1_out_37), .Equal(mips_alu_1_equal),
    .Result(mips_alu_1_result), .shamt(id_ex_1_out_38));  // open: Result_2
  or or_7 (JUMP, JSEL, JRSEL, JALSEL, BSEL);
  and and_7 (and_7_out, id_ex_1_out_32, ~mips_alu_1_equal);  // AND_Gate
  Comparator #(.width(5), .mode("twosComplement")) comparator_3 (
    .a(EXrW), .b(IDrA), .eq(comparator_3_eq));  // open: gt, lt
  Comparator #(.width(5), .mode("twosComplement")) comparator_4 (
    .a(EXrW), .b(IDrB), .eq(comparator_4_eq));  // open: gt, lt
  Comparator #(.width(5), .mode("twosComplement")) comparator_5 (
    .a(EXrW), .b({5{1'b0}}), .eq(comparator_5_eq));  // open: gt, lt
  Multiplexer #(.select(1), .width(1), .disabled("Z"), .enable("false")) multiplexer_7 (
    .in0(1'b0), .in1(comparator_3_eq), .out(multiplexer_7_out), .sel(IDrAUsed));
  or or_8 (or_8_out, multiplexer_7_out, multiplexer_8_out);
  Multiplexer #(.select(1), .width(1), .disabled("Z"), .enable("false")) multiplexer_8 (
    .in0(1'b0), .in1(comparator_4_eq), .out(multiplexer_8_out), .sel(IDrBUsed));
  not not_8 (not_8_out, comparator_5_eq);
  or or_9 (Datalocked, and_8_out, and_9_out);
  and and_8 (and_8_out, or_8_out, not_8_out, id_ex_1_out_35);
  EX_MEM ex_mem_1 (
    .MemToReg(id_ex_1_out_33), .RegWrite(id_ex_1_out_35), .MemWrite(id_ex_1_out_36), .PC(EX_PC),
    .\指令字 (EX_IR), .\传输状态In_表明当前传输数据有效 (\id_ex_1_传输状态out_表明当前传输数据有效 ), .CLK(CLK), .out_16(ex_mem_1_out_16),
    .out_18(ex_mem_1_out_18), .out_19(MemWrite), .out_24(M_PC), .out_25(MEM_IR),
    .\传输状态Out_表明当前传输数据有效 (\ex_mem_1_传输状态out_表明当前传输数据有效 ), .\使能端_低电平有效_stall_高电平有效 (WBHalt),
    .AluResult(mips_alu_1_result), .out_22(ex_mem_1_out_22), .RegisterB(id_ex_1_out_40), .out_21(MDin),
    .finalrW(EXrW), .out_20(MEMrW), .out_27(ex_mem_1_out_27), .Halt(id_ex_1_out_47), .RetA(id_ex_1_out_42),
    .out_23(ex_mem_1_out_23), .JAL(JALSEL), .out_17(ex_mem_1_out_17));  // open: 同步清零_气泡_高电平有效
  Comparator #(.width(5), .mode("twosComplement")) comparator_6 (
    .a(MEMrW), .b(IDrA), .eq(comparator_6_eq));  // open: gt, lt
  Comparator #(.width(5), .mode("twosComplement")) comparator_7 (
    .a(MEMrW), .b(IDrB), .eq(comparator_7_eq));  // open: gt, lt
  Comparator #(.width(5), .mode("twosComplement")) comparator_8 (
    .a(MEMrW), .b({5{1'b0}}), .eq(comparator_8_eq));  // open: gt, lt
  not not_9 (not_9_out, comparator_8_eq);
  Multiplexer #(.select(1), .width(1), .disabled("Z"), .enable("false")) multiplexer_9 (
    .in0(1'b0), .in1(comparator_6_eq), .out(multiplexer_9_out), .sel(IDrAUsed));
  or or_10 (or_10_out, multiplexer_9_out, multiplexer_10_out);
  Multiplexer #(.select(1), .width(1), .disabled("Z"), .enable("false")) multiplexer_10 (
    .in0(1'b0), .in1(comparator_7_eq), .out(multiplexer_10_out), .sel(IDrBUsed));
  and and_9 (and_9_out, or_10_out, not_9_out, ex_mem_1_out_18);
  RAM #(.addrWidth(10), .dataWidth(32), .bus("separate"), .Select("high")) ram_1 (
    .addr(ex_mem_1_out_22[11:2]), .din(MDin), .data(ram_1_data), .str(MemWrite), .clk(CLK));  // open: sel, ld, clr
  MEM_WB mem_wb_1 (
    .MemToReg(ex_mem_1_out_16), .RegWrite(ex_mem_1_out_18), .MemData(ram_1_data),
    .AluResult(ex_mem_1_out_22), .PC(M_PC), .\指令字 (MEM_IR),
    .\传输状态In_表明当前传输数据有效 (\ex_mem_1_传输状态out_表明当前传输数据有效 ), .CLK(CLK), .out_15(mem_wb_1_out_16[1]),
    .out_17(RegWrite), .out_19(mem_wb_1_out_19), .out_20(mem_wb_1_out_20), .out_22(WB_PC), .out_23(WB_IR),
    .\使能端_低电平有效_stall_高电平有效 (WBHalt), .finalrW(MEMrW), .out_18(WBFinalrW), .Halt(ex_mem_1_out_27),
    .out_25(WBHalt), .RetA(ex_mem_1_out_23), .out_21(mem_wb_1_out_21), .JAL(ex_mem_1_out_17),
    .out_16(mem_wb_1_out_16[0]));  // open: 传输状态Out_表明当前传输数据有效, 同步清零_气泡_高电平有效
  Multiplexer #(.select(2), .width(32), .disabled("Z"), .enable("false")) multiplexer_11 (
    .in0(mem_wb_1_out_20), .in1(mem_wb_1_out_21), .in2(mem_wb_1_out_19), .in3(mem_wb_1_out_21), .out(RDin),
    .sel(mem_wb_1_out_16));

  // Other names for the same wires on the sheet: EXPC[31:0] = EX_PC; IDtarget[25:0] = ID_IR[25:0];
  //   target[25:0] = JAddr; JAddr[31:28] = EX_PC[31:28]; MEM_PC[31:0] = M_PC; WBFinalData[31:0] = RDin;
  //   WBRegwrite = RegWrite

  // Notes on the sheet:
  //   中断源
  //   时空图监测，可删除
  //   中断等待指示
  //   数码管输出
  //   控制位
  //   流水调试日志用
  //   暂停节拍，不能为0
  //   contents of rom_1 (hex, n*v repeats v):
  //   20110001 8000c05 20110001 20120002 20130003 8000c09 20110001 20120002 20130003 8000c0d 20110001
  //   20120002 20130003 8000c11 20110001 20120002 20130003 c000cb8 20100001 20110001 118fc0 112020
  //   20020022 c 118882 12200001 8000c15 112020 20020022 c 20110001 118880 112020 20020022 c 12200001
  //   8000c1f 20110001 118fc0 112020 20020022 c 1188c3 112020 20020022 c 118903 112020 20020022 c 118903
  //   112020 20020022 c 118903 112020 20020022 c 118903 112020 20020022 c 118903 112020 20020022 c 118903
  //   112020 20020022 c 118903 112020 20020022 c 20100001 109fc0 139fc3 8021 2012000c 24160003 26100001
  //   3210000f 20080008 20090001 139900 2709825 132020 20020022 c 1094022 1500fff9 22100001 2018000f
  //   2188024 108700 20080008 20090001 139902 2709825 132021 20020022 c 1094022 1500fff9 108702 2c9b022
  //   12c00001 8000c50 4020 1084027 84400 3508ffff 82021 20020022 c 2010ffff 20110000 ae300000 22100001
  //   22310004 ae300000 22100001 22310004 ae300000 22100001 22310004 ae300000 22100001 22310004 ae300000
  //   22100001 22310004 ae300000 22100001 22310004 ae300000 22100001 22310004 ae300000 22100001 22310004
  //   ae300000 22100001 22310004 ae300000 22100001 22310004 ae300000 22100001 22310004 ae300000 22100001
  //   22310004 ae300000 22100001 22310004 ae300000 22100001 22310004 ae300000 22100001 22310004 ae300000
  //   22100001 22310004 22100001 8020 2011003c 8e130000 8e340000 274402a 11000002 ae330000 ae140000
  //   2231fffc 1611fff8 102020 20020022 c 22100004 2011003c 1611fff2 20020032 c 20100000 22100001 102020
  //   20020022 c 22100002 102020 20020022 c 22100003 102020 20020022 c 22100004 102020 20020022 c 22100005
  //   102020 20020022 c 22100006 102020 20020022 c 22100007 102020 20020022 c 22100008 102020 20020022
  //   20020022 c 3e00008
  //   戳工具置1进入计数暂停模式，ctrl+k时钟自动运行到对应节拍暂停
  //   ctrl+k关闭时钟连续运行，将控制位置零，进入单步调试模式调试
  //   指令字
  //   可计数暂停的时钟源
  //   OP
  //   rs
  //   Beq
  //   JMP
  //   JR
  //   Bne
  //   OP
  //   JAL
  //   Func
  //   Syscall
  //   为方便自动评测，需要输出流水线各段保存的PC值，注意是PC不是PC+4，另外ID段寄存器写入信息，Mem段内存写入信息也要输出
  //   MemToReg
  //   MemWrite
  //   AluOP
  //   AluSrcB
  //   RegWrite
  //   RegDst
endmodule
module \重定向流水线  (
  output RegWrite,
  output MemWrite,
  output [31:0] IF_PC,
  output [31:0] ID_PC,
  output [31:0] EX_PC,
  output [31:0] M_PC,
  output [31:0] WB_PC,
  output [31:0] RDin,
  output [31:0] MDin,
  output [31:0] LedData
);

  wire and_5_out, and_6_out, and_7_out, and_8_out, and_10_out, BSEL, Bubble, CLK, clock_1_out,
       comparator_1_eq, comparator_1_lt, comparator_2_eq, comparator_3_eq, comparator_4_eq, comparator_5_eq,
       comparator_6_eq, comparator_7_eq, comparator_8_eq, comparator_9_eq, d_ff_1_q, ERET, ex_mem_1_out_16,
       ex_mem_1_out_17, ex_mem_1_out_18, ex_mem_1_out_27, \ex_mem_1_传输状态out_表明当前传输数据有效 , EXDataLocked,
       EXrALocked, Go, id_ex_1_out_30, id_ex_1_out_33, id_ex_1_out_34, id_ex_1_out_35, id_ex_1_out_36,
       id_ex_1_out_47, \id_ex_1_传输状态out_表明当前传输数据有效 , IDBeq, IDBne, IDJ, IDJAL, IDJR, IDrAUsed, IDrBUsed,
       IDSYSCALL, \if_id_1_传输状态out_表明当前传输数据有效 , IR1, IR2, IR3, JUMP, MEMDataLocked, MEMrALocked,
       multiplexer_10_out, multiplexer_12_out, nand_1_out, not_1_out, not_2_out, not_4_out, not_5_out,
       or_1_out, or_2_out, or_3_out, or_4_out, or_5_out, or_9_out, or_10_out, RST, SignedExt, W1, W2, W3,
       WAITGO, WBHalt, \单周期硬布线控制器_1_alu_src , \单周期硬布线控制器_1_memtoreg , \单周期硬布线控制器_1_memwrite ,
       \单周期硬布线控制器_1_regwrite ;
  wire [1:0] and_1_out, and_3_out, mem_wb_1_out_16;
  wire [1:1] \单周期硬布线控制器_1_regdst ;
  wire [3:0] id_ex_1_out_37, \单周期硬布线控制器_1_alu_op ;
  wire [4:0] EXrW, id_ex_1_out_38, IDrA, IDrB, IDrW, MEMrW, WBFinalrW;
  wire [12:0] CNT_num;
  wire [15:0] \LoadUse次数 , \总周期数 , \插入气泡数 , \无条件分支数 , \条件分支成功数 ;
  wire [31:0] adder_1_out, bit_extender_1_out, bit_extender_2_out, controlled_buffer_1_out,
       controlled_buffer_5_out, EX_IR, ex_mem_1_out_22, ex_mem_1_out_23, id_ex_1_out_39, id_ex_1_out_40,
       id_ex_1_out_41, id_ex_1_out_42, ID_IR, IDBAddr, IDJRAddr, IF_IR, MEM_IR, mem_wb_1_out_19,
       mem_wb_1_out_20, mem_wb_1_out_21, mips_alu_1_result, multiplexer_1_out, multiplexer_5_out,
       multiplexer_7_out, multiplexer_8_out, ram_1_data, registerfile_1_p7, registerfile_1_p8, RETA,
       shifter_1_out, WB_IR;

  Button \u_总复位  (.out(RST));
  Button _1 (.out(IR1));
  Button _2 (.out(IR2));
  Button _3 (.out(IR3));
  // Probe on \总周期数 
  // Probe on \总周期数 
  Button \u_继续运行  (.out(Go));
  LED #(.active("true")) led_1 (.in(W1));
  LED #(.active("true")) led_2 (.in(W2));
  LED #(.active("true")) led_3 (.in(W3));
  Hex_Digit_Display hex_digit_display_1 (.value(LedData[31:28]));  // open: dp
  // Probe on IF_PC[19:0]
  // Mips_Probe mips_probe_1: pin names not known; wires that end beside it: IF_IR
  Hex_Digit_Display hex_digit_display_2 (.value(LedData[27:24]));  // open: dp
  Hex_Digit_Display hex_digit_display_3 (.value(LedData[23:20]));  // open: dp
  // Probe on ID_PC[19:0]
  // Mips_Probe mips_probe_2: pin names not known; wires that end beside it: ID_IR
  Hex_Digit_Display hex_digit_display_4 (.value(LedData[15:12]));  // open: dp
  Hex_Digit_Display hex_digit_display_5 (.value(LedData[19:16]));  // open: dp
  assign controlled_buffer_1_out = BSEL ? IDBAddr : 32'bz;  // Controlled_Buffer controlled_buffer_1
  assign controlled_buffer_1_out = or_1_out ? {ID_PC[31:28], ID_IR[25:0], 2'b00} : 32'bz;  // Controlled_Buffer controlled_buffer_2
  or or_1 (or_1_out, IDJ, IDJAL);
  assign controlled_buffer_1_out = IDJR ? IDJRAddr : 32'bz;  // Controlled_Buffer controlled_buffer_3
  Hex_Digit_Display hex_digit_display_6 (.value(LedData[7:4]));  // open: dp
  Hex_Digit_Display hex_digit_display_7 (.value(LedData[11:8]));  // open: dp
  // Probe on EX_PC[19:0]
  // Mips_Probe mips_probe_3: pin names not known; wires that end beside it: EX_IR
  Multiplexer #(.select(1), .width(32), .disabled("Z"), .enable("false")) multiplexer_1 (
    .in0(adder_1_out), .in1(controlled_buffer_1_out), .out(multiplexer_1_out), .sel(JUMP));
  Hex_Digit_Display hex_digit_display_8 (.value(LedData[3:0]));  // open: dp
  not not_1 (not_1_out, or_2_out);
  or or_2 (or_2_out, Bubble, WBHalt);
  // Probe on \总周期数 
  // Probe on M_PC[19:0]
  // Mips_Probe mips_probe_4: pin names not known; wires that end beside it: MEM_IR
  Register #(.width(32), .trigger("rising"), .Select("low")) PC (
    .D(multiplexer_1_out), .en(not_1_out), .Q(IF_PC), .clk(CLK));  // open: clr
  // Probe on \总周期数 
  // Probe on \无条件分支数 
  // Probe on \条件分支成功数 
  // Probe on \插入气泡数 
  // Probe on \LoadUse次数 
  // Probe on IF_PC[11:0]
  // Probe on WB_PC[19:0]
  // Mips_Probe mips_probe_5: pin names not known; wires that end beside it: WB_IR
  Adder #(.width(32)) adder_1 (.a(IF_PC), .b(32'h4), .out(adder_1_out));  // open: cin, cout
  // Probe on ID_PC[11:0]
  // Probe on EX_PC[11:0]
  // Probe on M_PC[11:0]
  D_Flip_Flop #(.trigger("high"), .Pre_Clr_Positions("LEGACY"), .NegatePresetClear("false"), .enable("true"), .NewFFLayout("false")) d_ff_1 (.Q(d_ff_1_q));  // open: clk, D, Qn, preset, en, reset
  // Probe on 13'h160
  ROM #(.addrWidth(10), .dataWidth(32), .Select("high")) rom_1 (.addr(IF_PC[11:2]), .data(IF_IR));
  // Probe on WB_PC[11:0]
  Comparator #(.width(13), .mode("twosComplement")) comparator_1 (
    .a(CNT_num), .b(13'h160), .eq(comparator_1_eq), .lt(comparator_1_lt));  // open: gt
  Clock #(.highDuration(1), .lowDuration(1)) clock_1 (.out(clock_1_out));
  or or_3 (or_3_out, Bubble, WBHalt);
  nand nand_1 (nand_1_out, d_ff_1_q, comparator_1_eq);
  Counter #(.width(13), .max('h1fff), .ongoal("stay"), .trigger("rising"), .behavior("old")) counter_1 (
    .count(comparator_1_lt), .Q(CNT_num), .clk(clock_1_out));  // open: load, D, carry, clr, preset
  IF_ID if_id_1 (
    .PC(IF_PC), .\指令字 (IF_IR), .\传输状态In_表明当前传输数据有效 (1'b1), .CLK(CLK), .out_7(ID_PC), .out_8(ID_IR),
    .\传输状态Out_表明当前传输数据有效 (\if_id_1_传输状态out_表明当前传输数据有效 ), .\同步清零_气泡_高电平有效 (JUMP),
    .\使能端_低电平有效_stall_高电平有效 (or_3_out));
  assign CLK = nand_1_out ? clock_1_out : 1'bz;  // Controlled_Buffer controlled_buffer_4
  \数据相关寄存器使用情况  \u_数据相关寄存器使用情况_1  (.OP(ID_IR[31:26]), .FUNC(ID_IR[5:0]), .rAUsed(IDrAUsed), .rBUsed(IDrBUsed));
  Pull_Resistor #(.pull(1)) pull_resistor_1 (.node(CLK));
  Multiplexer #(.select(1), .width(5), .disabled("Z"), .enable("false")) multiplexer_2 (
    .in0(ID_IR[25:21]), .in1(5'b00100), .out(IDrA), .sel(IDSYSCALL));
  Multiplexer #(.select(1), .width(5), .disabled("Z"), .enable("false")) multiplexer_3 (
    .in0(ID_IR[20:16]), .in1(5'b00010), .out(IDrB), .sel(IDSYSCALL));
  not not_2 (not_2_out, WBHalt);
  \单周期硬布线控制器  \u_单周期硬布线控制器_1  (
    .Func(ID_IR[5:0]), .OP(ID_IR[31:26]), .ALU_OP(\单周期硬布线控制器_1_alu_op ), .MemToReg(\单周期硬布线控制器_1_memtoreg ),
    .MemWrite(\单周期硬布线控制器_1_memwrite ), .ALU_SRC(\单周期硬布线控制器_1_alu_src ), .RegWrite(\单周期硬布线控制器_1_regwrite ),
    .SysCALL(IDSYSCALL), .SignedExt(SignedExt), .RegDst(\单周期硬布线控制器_1_regdst [1]), .JR(IDJR), .JMP(IDJ),
    .Beq(IDBeq), .JAL(IDJAL), .Bne(IDBne), ._25(ID_IR[25]), .ERET(ERET));
  Multiplexer #(.select(2), .width(5), .disabled("Z"), .enable("false")) multiplexer_4 (
    .in0(ID_IR[20:16]), .in1({5{1'b1}}), .in2(ID_IR[15:11]), .in3({5{1'b1}}), .out(IDrW),
    .sel({\单周期硬布线控制器_1_regdst [1], IDJAL}));
  assign bit_extender_1_out = {{16{ID_IR[15]}}, ID_IR[15:0]};  // Bit_Extender bit_extender_1
  Adder #(.width(32)) adder_2 (.a(32'h4), .b(ID_PC), .out(RETA));  // open: cin, cout
  Counter #(.width(16), .max('hffff), .ongoal("wrap"), .trigger("rising"), .behavior("old")) counter_2 (
    .count(not_2_out), .Q(\总周期数 ), .clk(CLK));  // open: load, D, carry, clr, preset
  assign bit_extender_2_out = {{16{1'b0}}, ID_IR[15:0]};  // Bit_Extender bit_extender_2
  Shifter #(.width(32), .shift("ll")) shifter_1 (.in(bit_extender_1_out), .\dist (5'b00010), .out(shifter_1_out));
  Multiplexer #(.select(1), .width(32), .disabled("Z"), .enable("false")) multiplexer_5 (
    .in0(bit_extender_2_out), .in1(bit_extender_1_out), .out(multiplexer_5_out), .sel(SignedExt));
  or or_4 (or_4_out, JUMP, Bubble);
  Adder #(.width(32)) adder_3 (.a(shifter_1_out), .b(RETA), .out(IDBAddr));  // open: cin, cout
  Counter #(.width(16), .max('hffff), .ongoal("wrap"), .trigger("rising"), .behavior("old")) counter_3 (
    .count(or_4_out), .Q(\插入气泡数 ), .clk(CLK));  // open: load, D, carry, clr, preset
  Counter #(.width(16), .max('hffff), .ongoal("wrap"), .trigger("rising"), .behavior("old")) counter_4 (
    .count(Bubble), .Q(\LoadUse次数 ), .clk(CLK));  // open: load, D, carry, clr, preset
  // RegisterFile registerfile_1: pin names not known; wires that end beside it: RDin, CLK, RegWrite, WBFinalrW, IDrA, IDrB, registerfile_1_p7, registerfile_1_p8
  or or_5 (or_5_out, IDJ, IDJR, IDJAL);
  and and_1 (and_1_out[0], MEMrALocked, MEMDataLocked);
  and and_2 (and_1_out[1], EXrALocked, EXDataLocked);
  Multiplexer #(.select(2), .width(32), .disabled("Z"), .enable("false")) multiplexer_6 (
    .in0(registerfile_1_p7), .in1(ex_mem_1_out_22), .in2(mips_alu_1_result), .in3(mips_alu_1_result),
    .out(IDJRAddr), .sel(and_1_out));
  Multiplexer #(.select(2), .width(32), .disabled("Z"), .enable("false")) multiplexer_7 (
    .in0(registerfile_1_p8), .in1(ex_mem_1_out_22), .in2(mips_alu_1_result), .in3(mips_alu_1_result),
    .out(multiplexer_7_out), .sel(and_3_out));
  and and_3 (and_3_out[0], ~MEMrALocked, MEMDataLocked);  // AND_Gate
  and and_4 (and_3_out[1], ~EXrALocked, EXDataLocked);  // AND_Gate
  Counter #(.width(16), .max('hffff), .ongoal("wrap"), .trigger("rising"), .behavior("old")) counter_5 (
    .count(or_5_out), .Q(\无条件分支数 ), .clk(CLK));  // open: load, D, carry, clr, preset
  Comparator #(.width(32), .mode("twosComplement")) comparator_2 (
    .a(IDJRAddr), .b(multiplexer_7_out), .eq(comparator_2_eq));  // open: gt, lt
  or or_6 (JUMP, IDJ, IDJR, IDJAL, BSEL);
  Counter #(.width(16), .max('hffff), .ongoal("wrap"), .trigger("rising"), .behavior("old")) counter_6 (
    .count(BSEL), .Q(\条件分支成功数 ), .clk(CLK));  // open: load, D, carry, clr, preset
  or or_7 (BSEL, and_6_out, and_5_out);
  and and_5 (and_5_out, IDBne, ~comparator_2_eq);  // AND_Gate
  and and_6 (and_6_out, IDBeq, comparator_2_eq);
  assign controlled_buffer_5_out = comparator_3_eq ? IDJRAddr : 32'bz;  // Controlled_Buffer controlled_buffer_5
  Comparator #(.width(32), .mode("twosComplement")) comparator_3 (
    .a(32'h22), .b(multiplexer_7_out), .eq(comparator_3_eq));  // open: gt, lt
  Register #(.width(32), .trigger("rising"), .Select("low")) register_1 (
    .D(controlled_buffer_5_out), .Q(LedData), .clk(CLK));  // open: en, clr
  not not_3 (WAITGO, comparator_3_eq);
  and and_7 (and_7_out, IDSYSCALL, WAITGO);
  ID_EX id_ex_1 (
    .ALUOP(\单周期硬布线控制器_1_alu_op ), .shamt(ID_IR[10:6]), .RegisterA(IDJRAddr),
    .Immediatenum(multiplexer_5_out), .PC(ID_PC), .\指令字 (ID_IR),
    .\传输状态In_表明当前传输数据有效 (\if_id_1_传输状态out_表明当前传输数据有效 ), .CLK(CLK), .out_37(id_ex_1_out_37),
    .out_38(id_ex_1_out_38), .out_39(id_ex_1_out_39), .out_41(id_ex_1_out_41), .out_43(EX_PC),
    .out_45(EX_IR), .\传输状态Out_表明当前传输数据有效 (\id_ex_1_传输状态out_表明当前传输数据有效 ), .\同步清零_气泡_高电平有效 (Bubble),
    .\使能端_低电平有效_stall_高电平有效 (WBHalt), .MemWrite(\单周期硬布线控制器_1_memwrite ), .out_36(id_ex_1_out_36),
    .RegWrite(\单周期硬布线控制器_1_regwrite ), .out_35(id_ex_1_out_35), .RegisterB(multiplexer_7_out),
    .out_40(id_ex_1_out_40), .AluSrcB(\单周期硬布线控制器_1_alu_src ), .out_34(id_ex_1_out_34),
    .MemToReg(\单周期硬布线控制器_1_memtoreg ), .out_33(id_ex_1_out_33), .finalrW(IDrW), .out_44(EXrW), .JAL(IDJAL),
    .out_30(id_ex_1_out_30), .Halt(and_7_out), .out_47(id_ex_1_out_47), .RetA(RETA), .out_42(id_ex_1_out_42));  // open: Beq, out_31, Bne, out_32, JR, out_29, J, out_28, Target, out_27, BAddr, out_26
  Multiplexer #(.select(1), .width(32), .disabled("Z"), .enable("false")) multiplexer_8 (
    .in0(id_ex_1_out_40), .in1(id_ex_1_out_41), .out(multiplexer_8_out), .sel(id_ex_1_out_34));
  and and_8 (and_8_out, EXDataLocked, id_ex_1_out_33);
  MIPS_ALU mips_alu_1 (
    .X(id_ex_1_out_39), .Y(multiplexer_8_out), .AluOP(id_ex_1_out_37), .Result(mips_alu_1_result),
    .shamt(id_ex_1_out_38));  // open: Equal, Result_2
  Comparator #(.width(5), .mode("twosComplement")) comparator_4 (
    .a(EXrW), .b(IDrA), .eq(comparator_4_eq));  // open: gt, lt
  Comparator #(.width(5), .mode("twosComplement")) comparator_5 (
    .a(EXrW), .b(IDrB), .eq(comparator_5_eq));  // open: gt, lt
  Comparator #(.width(5), .mode("twosComplement")) comparator_6 (
    .a(EXrW), .b({5{1'b0}}), .eq(comparator_6_eq));  // open: gt, lt
  or or_8 (Bubble, and_10_out, and_8_out);
  Multiplexer #(.select(1), .width(1), .disabled("Z"), .enable("false")) multiplexer_9 (
    .in0(1'b0), .in1(comparator_4_eq), .out(EXrALocked), .sel(IDrAUsed));
  or or_9 (or_9_out, EXrALocked, multiplexer_10_out);
  Multiplexer #(.select(1), .width(1), .disabled("Z"), .enable("false")) multiplexer_10 (
    .in0(1'b0), .in1(comparator_5_eq), .out(multiplexer_10_out), .sel(IDrBUsed));
  not not_4 (not_4_out, comparator_6_eq);
  and and_9 (EXDataLocked, or_9_out, not_4_out, id_ex_1_out_35);
  EX_MEM ex_mem_1 (
    .MemToReg(id_ex_1_out_33), .RegWrite(id_ex_1_out_35), .MemWrite(id_ex_1_out_36), .PC(EX_PC),
    .\指令字 (EX_IR), .\传输状态In_表明当前传输数据有效 (\id_ex_1_传输状态out_表明当前传输数据有效 ), .CLK(CLK), .out_16(ex_mem_1_out_16),
    .out_18(ex_mem_1_out_18), .out_19(MemWrite), .out_24(M_PC), .out_25(MEM_IR),
    .\传输状态Out_表明当前传输数据有效 (\ex_mem_1_传输状态out_表明当前传输数据有效 ), .\使能端_低电平有效_stall_高电平有效 (WBHalt),
    .AluResult(mips_alu_1_result), .out_22(ex_mem_1_out_22), .RegisterB(id_ex_1_out_40), .out_21(MDin),
    .finalrW(EXrW), .out_20(MEMrW), .out_27(ex_mem_1_out_27), .Halt(id_ex_1_out_47), .RetA(id_ex_1_out_42),
    .out_23(ex_mem_1_out_23), .JAL(id_ex_1_out_30), .out_17(ex_mem_1_out_17));  // open: 同步清零_气泡_高电平有效
  Comparator #(.width(5), .mode("twosComplement")) comparator_7 (
    .a(MEMrW), .b(IDrA), .eq(comparator_7_eq));  // open: gt, lt
  Comparator #(.width(5), .mode("twosComplement")) comparator_8 (
    .a(MEMrW), .b(IDrB), .eq(comparator_8_eq));  // open: gt, lt
  Comparator #(.width(5), .mode("twosComplement")) comparator_9 (
    .a(MEMrW), .b({5{1'b0}}), .eq(comparator_9_eq));  // open: gt, lt
  not not_5 (not_5_out, comparator_9_eq);
  and and_10 (and_10_out, MEMDataLocked, ex_mem_1_out_16);
  Multiplexer #(.select(1), .width(1), .disabled("Z"), .enable("false")) multiplexer_11 (
    .in0(1'b0), .in1(comparator_7_eq), .out(MEMrALocked), .sel(IDrAUsed));
  or or_10 (or_10_out, MEMrALocked, multiplexer_12_out);
  Multiplexer #(.select(1), .width(1), .disabled("Z"), .enable("false")) multiplexer_12 (
    .in0(1'b0), .in1(comparator_8_eq), .out(multiplexer_12_out), .sel(IDrBUsed));
  and and_11 (MEMDataLocked, or_10_out, not_5_out, ex_mem_1_out_18);
  RAM #(.addrWidth(10), .dataWidth(32), .bus("separate"), .Select("high")) ram_1 (
    .addr(ex_mem_1_out_22[11:2]), .din(MDin), .data(ram_1_data), .str(MemWrite), .clk(CLK));  // open: sel, ld, clr
  MEM_WB mem_wb_1 (
    .MemToReg(ex_mem_1_out_16), .RegWrite(ex_mem_1_out_18), .MemData(ram_1_data),
    .AluResult(ex_mem_1_out_22), .PC(M_PC), .\指令字 (MEM_IR),
    .\传输状态In_表明当前传输数据有效 (\ex_mem_1_传输状态out_表明当前传输数据有效 ), .CLK(CLK), .out_15(mem_wb_1_out_16[1]),
    .out_17(RegWrite), .out_19(mem_wb_1_out_19), .out_20(mem_wb_1_out_20), .out_22(WB_PC), .out_23(WB_IR),
    .\使能端_低电平有效_stall_高电平有效 (WBHalt), .finalrW(MEMrW), .out_18(WBFinalrW), .Halt(ex_mem_1_out_27),
    .out_25(WBHalt), .RetA(ex_mem_1_out_23), .out_21(mem_wb_1_out_21), .JAL(ex_mem_1_out_17),
    .out_16(mem_wb_1_out_16[0]));  // open: 传输状态Out_表明当前传输数据有效, 同步清零_气泡_高电平有效
  Multiplexer #(.select(2), .width(32), .disabled("Z"), .enable("false")) multiplexer_13 (
    .in0(mem_wb_1_out_20), .in1(mem_wb_1_out_21), .in2(mem_wb_1_out_19), .in3(mem_wb_1_out_21), .out(RDin),
    .sel(mem_wb_1_out_16));

  // Other names for the same wires on the sheet: EXPC[31:0] = EX_PC; IDJAddr[31:2] = {ID_PC[31:28], ID_IR[25:0]};
  //   IDtarget[25:0] = ID_IR[25:0]; MEM_PC[31:0] = M_PC; WBFinalData[31:0] = RDin; WBRegwrite = RegWrite

  // Notes on the sheet:
  //   中断源
  //   时空图监测，可删除
  //   中断等待指示
  //   数码管输出
  //   控制位
  //   流水调试日志用
  //   暂停节拍，不能为0
  //   contents of rom_1 (hex, n*v repeats v):
  //   20110001 8000c05 20110001 20120002 20130003 8000c09 20110001 20120002 20130003 8000c0d 20110001
  //   20120002 20130003 8000c11 20110001 20120002 20130003 c000cb8 20100001 20110001 118fc0 112020
  //   20020022 c 118882 12200001 8000c15 112020 20020022 c 20110001 118880 112020 20020022 c 12200001
  //   8000c1f 20110001 118fc0 112020 20020022 c 1188c3 112020 20020022 c 118903 112020 20020022 c 118903
  //   112020 20020022 c 118903 112020 20020022 c 118903 112020 20020022 c 118903 112020 20020022 c 118903
  //   112020 20020022 c 118903 112020 20020022 c 20100001 109fc0 139fc3 8021 2012000c 24160003 26100001
  //   3210000f 20080008 20090001 139900 2709825 132020 20020022 c 1094022 1500fff9 22100001 2018000f
  //   2188024 108700 20080008 20090001 139902 2709825 132021 20020022 c 1094022 1500fff9 108702 2c9b022
  //   12c00001 8000c50 4020 1084027 84400 3508ffff 82021 20020022 c 2010ffff 20110000 ae300000 22100001
  //   22310004 ae300000 22100001 22310004 ae300000 22100001 22310004 ae300000 22100001 22310004 ae300000
  //   22100001 22310004 ae300000 22100001 22310004 ae300000 22100001 22310004 ae300000 22100001 22310004
  //   ae300000 22100001 22310004 ae300000 22100001 22310004 ae300000 22100001 22310004 ae300000 22100001
  //   22310004 ae300000 22100001 22310004 ae300000 22100001 22310004 ae300000 22100001 22310004 ae300000
  //   22100001 22310004 22100001 8020 2011003c 8e130000 8e340000 274402a 11000002 ae330000 ae140000
  //   2231fffc 1611fff8 102020 20020022 c 22100004 2011003c 1611fff2 20020032 c 20100000 22100001 102020
  //   20020022 c 22100002 102020 20020022 c 22100003 102020 20020022 c 22100004 102020 20020022 c 22100005
  //   102020 20020022 c 22100006 102020 20020022 c 22100007 102020 20020022 c 22100008 102020 20020022
  //   20020022 c 3e00008
  //   戳工具置1进入计数暂停模式，ctrl+k时钟自动运行到对应节拍暂停
  //   ctrl+k关闭时钟连续运行，将控制位置零，进入单步调试模式调试
  //   指令字
  //   可计数暂停的时钟源
  //   OP
  //   rs
  //   Beq
  //   JMP
  //   JR
  //   Bne
  //   OP
  //   JAL
  //   Func
  //   Syscall
  //   为方便自动评测，需要输出流水线各段保存的PC值，注意是PC不是PC+4，另外ID段寄存器写入信息，Mem段内存写入信息也要输出
  //   MemToReg
  //   MemWrite
  //   AluOP
  //   AluSrcB
  //   RegWrite
  //   RegDst
endmodule

module \中断按键参考电路  (
  input  CLK,
  input  in_2,
  input  \同步清零信号 ,
  output \与中断屏蔽位与 ,
  output out_5
);

  wire and_1_out, d_ff_1_q, or_2_out;

  or or_1 (out_5, \与中断屏蔽位与 , d_ff_1_q);
  D_Flip_Flop #(.trigger("rising"), .Pre_Clr_Positions("LEGACY"), .NegatePresetClear("false"), .enable("true"), .NewFFLayout("false")) d_ff_1 (
    .clk(in_2), .D(1'b1), .Q(d_ff_1_q), .reset(\与中断屏蔽位与 ));  // open: Qn, preset, en
  or or_2 (or_2_out, d_ff_1_q, \与中断屏蔽位与 );
  and and_1 (and_1_out, or_2_out, ~\同步清零信号 );  // AND_Gate
  D_Flip_Flop #(.trigger("rising"), .Pre_Clr_Positions("LEGACY"), .NegatePresetClear("false"), .enable("true"), .NewFFLayout("false")) IR1 (
    .clk(CLK), .D(and_1_out), .Q(\与中断屏蔽位与 ));  // open: Qn, preset, en, reset

  // Notes on the sheet:
  //   中断信号采样参考电路
  //   Reset 
endmodule

module \单周期MIPS_单级中断  (
  input  IR1,
  input  IR2,
  input  IR3,
  output RegWrite,
  output MemWrite,
  output [31:0] PC,
  output [31:0] IR,
  output [31:0] RDin,
  output [31:0] MDin,
  output [31:0] LedData
);

  wire and_2_out, and_3_out, BSEL, CLK, clock_2_out, comparator_1_eq, comparator_2_eq, comparator_3_eq,
       comparator_4_eq, comparator_5_eq, comparator_5_lt, comparator_6_eq, comparator_7_eq,
       controlled_buffer_9_out, d_ff_1_q, decoder_1_out1, decoder_1_out2, decoder_1_out3, ERET, Go, IE_q,
       IE_qn, IEIN, interamendPC, INTERRUPT, IR1_t, IR2_t, IR3_t, IRA, IRB, IRC, JALSEL, JRSEL, JSEL, JUMP,
       mips_alu_1_equal, multiplexer_1_out, multiplexer_3_out, multiplexer_6_out, nand_1_out, not_1_out,
       not_2_out, not_3_out, not_4_out, not_5_out, not_6_out, not_7_out, not_9_out, or_1_out, or_4_out,
       or_7_out, or_8_out, priority_encoder_1_gs, pull_resistor_1_node, pull_resistor_2_node,
       pull_resistor_3_node, SignedExt, SYSCALL, W1, W2, W3, WAITGO, \中断按键参考电路_1_与中断屏蔽位与 ,
       \中断按键参考电路_2_与中断屏蔽位与 , \中断按键参考电路_3_与中断屏蔽位与 , \单周期硬布线控制器_1_alu_src , \单周期硬布线控制器_1_beq ,
       \单周期硬布线控制器_1_bne , \单周期硬布线控制器_1_memtoreg , \单周期硬布线控制器_1_regdst ;
  wire [1:0] priority_encoder_1_out, register_1_q;
  wire [3:0] \单周期硬布线控制器_1_alu_op ;
  wire [4:0] controlled_buffer_12_out, multiplexer_8_out, multiplexer_9_out, multiplexer_10_out;
  wire [12:0] CNT_num;
  wire [15:0] \总周期数 ;
  wire [31:0] adder_2_out, bit_extender_1_out, bit_extender_2_out, controlled_buffer_2_out,
       controlled_buffer_8_out, controlled_buffer_15_out, EPCADDR, interruptaddr, JUMPAddr,
       mips_alu_1_result, multiplexer_2_out, multiplexer_4_out, multiplexer_11_out, multiplexer_12_out,
       multiplexer_13_out, PC_t, ram_1_data, registerfile_1_p7, shifter_1_out;

  Clock #(.highDuration(1), .lowDuration(1)) clock_1 ();  // open: out
  Button _1 (.out(IRA));
  Button _2 (.out(IRB));
  Button _3 (.out(IRC));
  Button \u_继续运行  (.out(Go));
  LED #(.active("true")) led_1 (.in(W1));
  LED #(.active("true")) led_2 (.in(W2));
  LED #(.active("true")) led_3 (.in(W3));
  Hex_Digit_Display hex_digit_display_1 (.value(LedData[31:28]));  // open: dp
  D_Flip_Flop #(.trigger("high"), .Pre_Clr_Positions("LEGACY"), .NegatePresetClear("false"), .enable("true"), .NewFFLayout("false")) d_ff_1 (.Q(d_ff_1_q));  // open: clk, D, Qn, preset, en, reset
  // Probe on 13'h368
  Hex_Digit_Display hex_digit_display_2 (.value(LedData[27:24]));  // open: dp
  Hex_Digit_Display hex_digit_display_3 (.value(LedData[23:20]));  // open: dp
  Comparator #(.width(16), .mode("twosComplement")) comparator_1 (
    .a(16'h23b), .b(\总周期数 ), .eq(comparator_1_eq));  // open: gt, lt
  Comparator #(.width(16), .mode("twosComplement")) comparator_2 (
    .a(\总周期数 ), .b(16'h1), .eq(comparator_2_eq));  // open: gt, lt
  Comparator #(.width(16), .mode("twosComplement")) comparator_3 (
    .a(\总周期数 ), .b(16'h4), .eq(comparator_3_eq));  // open: gt, lt
  Comparator #(.width(16), .mode("twosComplement")) comparator_4 (
    .a(\总周期数 ), .b(16'h7), .eq(comparator_4_eq));  // open: gt, lt
  not not_1 (not_1_out, multiplexer_1_out);
  Multiplexer #(.select(1), .width(1), .disabled("Z"), .enable("false")) multiplexer_1 (
    .in0(1'b0), .in1(WAITGO), .out(multiplexer_1_out), .sel(SYSCALL));
  Comparator #(.width(13), .mode("twosComplement")) comparator_5 (
    .a(CNT_num), .b(13'h368), .eq(comparator_5_eq), .lt(comparator_5_lt));  // open: gt
  Clock #(.highDuration(1), .lowDuration(1)) clock_2 (.out(clock_2_out));
  Hex_Digit_Display hex_digit_display_4 (.value(LedData[15:12]));  // open: dp
  Hex_Digit_Display hex_digit_display_5 (.value(LedData[19:16]));  // open: dp
  or or_1 (or_1_out, comparator_1_eq, comparator_2_eq);
  Pull_Resistor #(.pull(0)) pull_resistor_1 (.node(pull_resistor_1_node));
  assign pull_resistor_1_node = or_1_out ? ~CLK : 1'bz;  // Controlled_Inverter controlled_inverter_1
  Pull_Resistor #(.pull(0)) pull_resistor_2 (.node(pull_resistor_2_node));
  assign pull_resistor_2_node = comparator_3_eq ? ~CLK : 1'bz;  // Controlled_Inverter controlled_inverter_2
  Pull_Resistor #(.pull(0)) pull_resistor_3 (.node(pull_resistor_3_node));
  assign pull_resistor_3_node = comparator_4_eq ? ~CLK : 1'bz;  // Controlled_Inverter controlled_inverter_3
  Counter #(.width(16), .max('hffff), .ongoal("wrap"), .trigger("rising"), .behavior("old")) counter_1 (
    .count(not_1_out), .Q(\总周期数 ), .clk(CLK));  // open: load, D, carry, clr, preset
  nand nand_1 (nand_1_out, d_ff_1_q, comparator_5_eq);
  Counter #(.width(13), .max('h1fff), .ongoal("stay"), .trigger("rising"), .behavior("old")) counter_2 (
    .count(comparator_5_lt), .Q(CNT_num), .clk(clock_2_out));  // open: load, D, carry, clr, preset
  Hex_Digit_Display hex_digit_display_6 (.value(LedData[11:8]));  // open: dp
  Hex_Digit_Display hex_digit_display_7 (.value(LedData[7:4]));  // open: dp
  // Probe on \总周期数 
  Hex_Digit_Display hex_digit_display_8 (.value(LedData[3:0]));  // open: dp
  assign CLK = nand_1_out ? clock_2_out : 1'bz;  // Controlled_Buffer controlled_buffer_1
  Pull_Resistor #(.pull(1)) pull_resistor_4 (.node(CLK));
  or or_2 (IR1_t, IR1, IRA);
  or or_3 (JUMP, BSEL, or_4_out);
  or or_4 (or_4_out, JSEL, JALSEL, JRSEL);
  or or_5 (IR2_t, IR2, IRB);
  Register #(.width(2), .trigger("rising"), .Select("low")) register_1 (
    .D(priority_encoder_1_out), .en(interamendPC), .Q(register_1_q), .clk(CLK));  // open: clr
  Decoder #(.select(2), .tristate("false"), .disabled(0), .enable("true")) decoder_1 (
    .out1(decoder_1_out1), .out2(decoder_1_out2), .out3(decoder_1_out3), .sel(register_1_q), .en(ERET));  // open: out0
  or or_6 (IR3_t, IR3, IRC);
  Multiplexer #(.select(1), .width(32), .disabled("Z"), .enable("false")) multiplexer_2 (
    .in0(PC_t), .in1(adder_2_out), .out(multiplexer_2_out), .sel(BSEL));
  \中断按键参考电路  \u_中断按键参考电路_1  (
    .\与中断屏蔽位与 (\中断按键参考电路_1_与中断屏蔽位与 ), .\同步清零信号 (decoder_1_out1), .out_5(W1), .CLK(CLK), .in_2(IR1_t));
  \中断按键参考电路  \u_中断按键参考电路_2  (
    .\与中断屏蔽位与 (\中断按键参考电路_2_与中断屏蔽位与 ), .\同步清零信号 (decoder_1_out2), .out_5(W2), .CLK(CLK), .in_2(IR2_t));
  \中断按键参考电路  \u_中断按键参考电路_3  (
    .\与中断屏蔽位与 (\中断按键参考电路_3_与中断屏蔽位与 ), .\同步清零信号 (decoder_1_out3), .out_5(W3), .CLK(CLK), .in_2(IR3_t));
  assign controlled_buffer_2_out = ERET ? EPCADDR : 32'bz;  // Controlled_Buffer controlled_buffer_2
  assign controlled_buffer_2_out = INTERRUPT ? interruptaddr : 32'bz;  // Controlled_Buffer controlled_buffer_3
  assign JUMPAddr = or_7_out ? {PC_t[31:28], IR[25:0], 2'b00} : 32'bz;  // Controlled_Buffer controlled_buffer_4
  or or_7 (or_7_out, JSEL, JALSEL);
  assign JUMPAddr = JRSEL ? registerfile_1_p7 : 32'bz;  // Controlled_Buffer controlled_buffer_5
  assign JUMPAddr = not_2_out ? multiplexer_2_out : 32'bz;  // Controlled_Buffer controlled_buffer_6
  not not_2 (not_2_out, or_8_out);
  or or_8 (or_8_out, JSEL, JALSEL, JRSEL);
  assign controlled_buffer_2_out = not_3_out ? JUMPAddr : 32'bz;  // Controlled_Buffer controlled_buffer_7
  Register #(.width(32), .trigger("rising"), .Select("low")) u_PC (
    .D(controlled_buffer_2_out), .en(not_4_out), .Q(PC), .clk(CLK));  // open: clr
  not not_3 (not_3_out, interamendPC);
  not not_4 (not_4_out, multiplexer_3_out);
  Multiplexer #(.select(1), .width(1), .disabled("Z"), .enable("false")) multiplexer_3 (
    .in0(1'b0), .in1(WAITGO), .out(multiplexer_3_out), .sel(SYSCALL));
  assign controlled_buffer_8_out = INTERRUPT ? multiplexer_4_out : 32'bz;  // Controlled_Buffer controlled_buffer_8
  Multiplexer #(.select(1), .width(32), .disabled("Z"), .enable("false")) multiplexer_4 (
    .in0(PC_t), .in1(JUMPAddr), .out(multiplexer_4_out), .sel(JUMP));
  Priority_Encoder #(.select(2), .disabled("Z")) priority_encoder_1 (
    .in1(\中断按键参考电路_1_与中断屏蔽位与 ), .in2(\中断按键参考电路_2_与中断屏蔽位与 ), .in3(\中断按键参考电路_3_与中断屏蔽位与 ),
    .out(priority_encoder_1_out), .gs(priority_encoder_1_gs));  // open: in0, en_out, en_in
  Register #(.width(32), .trigger("rising"), .Select("low")) EPC (
    .D(controlled_buffer_8_out), .Q(EPCADDR), .clk(CLK));  // open: en, clr
  or or_9 (interamendPC, INTERRUPT, ERET);
  D_Flip_Flop #(.trigger("rising"), .Pre_Clr_Positions("LEGACY"), .NegatePresetClear("false"), .enable("true"), .NewFFLayout("false")) IE (
    .clk(CLK), .D(IEIN), .Q(IE_q), .Qn(IE_qn));  // open: preset, en, reset
  assign controlled_buffer_9_out = INTERRUPT ? 1'b0 : 1'bz;  // Controlled_Buffer controlled_buffer_9
  assign controlled_buffer_9_out = ERET ? 1'b1 : 1'bz;  // Controlled_Buffer controlled_buffer_10
  Adder #(.width(32)) adder_1 (.a(PC), .b(32'h4), .out(PC_t));  // open: cin, cout
  Multiplexer #(.select(2), .width(32), .disabled("Z"), .enable("false")) multiplexer_5 (
    .in1(32'h30ac), .in2(32'h3150), .in3(32'h31f4), .out(interruptaddr), .sel(priority_encoder_1_out));  // open: in0
  and and_1 (INTERRUPT, priority_encoder_1_gs, IE_q);
  not not_5 (not_5_out, IE_qn);
  // Probe on interruptaddr
  Multiplexer #(.select(1), .width(1), .disabled("Z"), .enable("false")) multiplexer_6 (
    .in0(not_5_out), .in1(controlled_buffer_9_out), .out(multiplexer_6_out), .sel(interamendPC));
  // Mips_Probe mips_probe_1: pin names not known; wires that end beside it: IR
  ROM #(.addrWidth(10), .dataWidth(32), .Select("high")) rom_1 (.addr(PC[11:2]), .data(IR));
  Comparator #(.width(32), .mode("twosComplement")) comparator_6 (
    .a(PC), .b({32{1'b0}}), .eq(comparator_6_eq));  // open: gt, lt
  Multiplexer #(.select(1), .width(1), .disabled("Z"), .enable("false")) multiplexer_7 (
    .in0(multiplexer_6_out), .in1(1'b1), .out(IEIN), .sel(comparator_6_eq));
  Multiplexer #(.select(1), .width(5), .disabled("Z"), .enable("false")) multiplexer_8 (
    .in0(IR[25:21]), .in1(5'b00010), .out(multiplexer_8_out), .sel(SYSCALL));
  Multiplexer #(.select(1), .width(5), .disabled("Z"), .enable("false")) multiplexer_9 (
    .in0(IR[20:16]), .in1(5'b00100), .out(multiplexer_9_out), .sel(SYSCALL));
  Multiplexer #(.select(1), .width(5), .disabled("Z"), .enable("false")) multiplexer_10 (
    .in0(multiplexer_9_out), .in1(IR[15:11]), .out(multiplexer_10_out), .sel(\单周期硬布线控制器_1_regdst ));
  not not_6 (not_6_out, JALSEL);
  \单周期硬布线控制器  \u_单周期硬布线控制器_1  (
    .Func(IR[5:0]), .OP(IR[31:26]), .ALU_OP(\单周期硬布线控制器_1_alu_op ), .MemToReg(\单周期硬布线控制器_1_memtoreg ),
    .MemWrite(MemWrite), .ALU_SRC(\单周期硬布线控制器_1_alu_src ), .RegWrite(RegWrite), .SysCALL(SYSCALL),
    .SignedExt(SignedExt), .RegDst(\单周期硬布线控制器_1_regdst ), .JR(JRSEL), .JMP(JSEL), .Beq(\单周期硬布线控制器_1_beq ),
    .JAL(JALSEL), .Bne(\单周期硬布线控制器_1_bne ), ._25(IR[25]), .ERET(ERET));
  assign RDin = JALSEL ? PC_t : 32'bz;  // Controlled_Buffer controlled_buffer_11
  assign controlled_buffer_12_out = not_6_out ? multiplexer_10_out : 5'bz;  // Controlled_Buffer controlled_buffer_12
  assign controlled_buffer_12_out = JALSEL ? {5{1'b1}} : 5'bz;  // Controlled_Buffer controlled_buffer_13
  assign bit_extender_1_out = {{16{1'b0}}, IR[15:0]};  // Bit_Extender bit_extender_1
  assign bit_extender_2_out = {{16{IR[15]}}, IR[15:0]};  // Bit_Extender bit_extender_2
  assign RDin = not_7_out ? multiplexer_11_out : 32'bz;  // Controlled_Buffer controlled_buffer_14
  Multiplexer #(.select(1), .width(32), .disabled("Z"), .enable("false")) multiplexer_11 (
    .in0(mips_alu_1_result), .in1(ram_1_data), .out(multiplexer_11_out), .sel(\单周期硬布线控制器_1_memtoreg ));
  not not_7 (not_7_out, JALSEL);
  Shifter #(.width(32), .shift("ll")) shifter_1 (.in(bit_extender_2_out), .\dist (5'b00010), .out(shifter_1_out));
  Multiplexer #(.select(1), .width(32), .disabled("Z"), .enable("false")) multiplexer_12 (
    .in0(bit_extender_1_out), .in1(bit_extender_2_out), .out(multiplexer_12_out), .sel(SignedExt));
  Adder #(.width(32)) adder_2 (.a(shifter_1_out), .b(PC_t), .out(adder_2_out));  // open: cin, cout
  Comparator #(.width(32), .mode("twosComplement")) comparator_7 (
    .a(32'h22), .b(registerfile_1_p7), .eq(comparator_7_eq));  // open: gt, lt
  or or_10 (BSEL, and_3_out, and_2_out);
  assign controlled_buffer_15_out = comparator_7_eq ? MDin : 32'bz;  // Controlled_Buffer controlled_buffer_15
  not not_8 (WAITGO, comparator_7_eq);
  // RegisterFile registerfile_1: pin names not known; wires that end beside it: RDin, CLK, RegWrite, controlled_buffer_12_out, multiplexer_8_out, multiplexer_9_out, registerfile_1_p7, MDin
  and and_2 (and_2_out, \单周期硬布线控制器_1_beq , mips_alu_1_equal);
  Register #(.width(32), .trigger("rising"), .Select("low")) register_2 (
    .D(controlled_buffer_15_out), .Q(LedData), .clk(CLK));  // open: en, clr
  and and_3 (and_3_out, \单周期硬布线控制器_1_bne , not_9_out);
  not not_9 (not_9_out, mips_alu_1_equal);
  Multiplexer #(.select(1), .width(32), .disabled("Z"), .enable("false")) multiplexer_13 (
    .in0(MDin), .in1(multiplexer_12_out), .out(multiplexer_13_out), .sel(\单周期硬布线控制器_1_alu_src ));
  MIPS_ALU mips_alu_1 (
    .X(registerfile_1_p7), .Y(multiplexer_13_out), .AluOP(\单周期硬布线控制器_1_alu_op ), .Equal(mips_alu_1_equal),
    .Result(mips_alu_1_result), .shamt(IR[10:6]));  // open: Result_2
  RAM #(.addrWidth(10), .dataWidth(32), .bus("separate"), .Select("high")) ram_1 (
    .addr(mips_alu_1_result[11:2]), .din(MDin), .data(ram_1_data), .str(MemWrite), .clk(CLK));  // open: sel, ld, clr

  // Other names for the same wires on the sheet: RETA[31:0] = PC_t; target[25:0] = IR[25:0]; oldpc[31:0] = PC

  // Notes on the sheet:
  //   中断源
  //   中断等待指示
  //   总复位信号应将除ROM以外所有存储组件全部清零
  //   单级中断测试信号模拟器
  //   控制位
  //   暂停节拍，不能为0
  //   戳工具置1进入计数暂停模式，ctrl+k时钟自动运行到对应节拍暂停
  //   ctrl+k关闭时钟连续运行，将控制位置零，进入单步调试模式调试
  //   数码管输出
  //   数码管输出应该用寄存器锁存，否则显示数据只能一闪而过
  //   可计数暂停的时钟源
  //   为方便自动评测，需要输出PC，IR，寄存器堆写如数据RDin
  //   RAM写使能MemWrite、RAM写入数据MDin等信号
  //   指令存储器
  //   OP
  //   rs
  //   指令字
  //   contents of rom_1 (hex, n*v repeats v):
  //   201d07d0 20100001 109fc0 139fc3 8021 2012000c 24160008 26100001 3210000f 20080008 20090001 139900
  //   2709825 132020 20020022 c 1094022 1500fff9 22100001 2018000f 2188024 108700 20080008 20090001 139902
  //   2709825 132021 20020022 c 1094022 1500fff9 108702 2c9b022 12c00001 8000c07 4020 1084027 84400
  //   3508ffff 82021 20020022 c 8000c01 afa20000 23bd0004 afa40000 23bd0004 afb00000 23bd0004 afb30000
  //   23bd0004 afb40000 23bd0004 afb50000 23bd0004 afb60000 23bd0004 20160001 20140003 20150001 168020
  //   108100 2149825 132020 20020022 c 1600fffa 295a022 1680fff7 23bdfffc 8fb60000 23bdfffc 8fb50000
  //   23bdfffc 8fb40000 23bdfffc 8fb30000 23bdfffc 8fb00000 23bdfffc 8fa40000 23bdfffc 8fa20000 42000018
  //   afa20000 23bd0004 afa40000 23bd0004 afb00000 23bd0004 afb30000 23bd0004 afb40000 23bd0004 afb50000
  //   23bd0004 afb60000 23bd0004 20160002 20140003 20150001 168020 108100 2149825 132020 20020022 c
  //   1600fffa 295a022 1680fff7 23bdfffc 8fb60000 23bdfffc 8fb50000 23bdfffc 8fb40000 23bdfffc 8fb30000
  //   23bdfffc 8fb00000 23bdfffc 8fa40000 23bdfffc 8fa20000 42000018 afa20000 23bd0004 afa40000 23bd0004
  //   afb00000 23bd0004 afb30000 23bd0004 afb40000 23bd0004 afb50000 23bd0004 afb60000 23bd0004 20160003
  //   20140003 20150001 168020 108100 2149825 132020 20020022 c 1600fffa 295a022 1680fff7 23bdfffc
  //   8fb60000 23bdfffc 8fb50000 23bdfffc 8fb40000 23bdfffc 8fb30000 23bdfffc 8fb00000 23bdfffc 8fa40000
  //   23bdfffc 8fa20000 42000018
  //   Func
  //   JMP
  //   JR
  //   OP
  //   Func
  //   Beq
  //   Bne
  //   MemToReg
  //   MemWrite
  //   AluOP
  //   AluSrcB
  //   RegWrite
  //   JAL
  //   RegDst
  //   Syscall
endmodule

module \单周期MIPS_多级中断  (
  input  IR1,
  input  IR2,
  input  IR3,
  output RegWrite,
  output MemWrite,
  output [31:0] PC,
  output [31:0] IR,
  output [31:0] RDin,
  output [31:0] MDin,
  output [31:0] LedData
);

  wire CLK, comparator_1_eq, comparator_2_eq, comparator_3_eq, comparator_4_eq, comparator_5_eq, Go, IR1_t,
       IR2_t, IR3_t, IRA, IRB, IRC, or_1_out, or_2_out, W1, W2, W3;
  wire [15:0] \总周期数 ;

  Clock #(.highDuration(1), .lowDuration(1)) clock_1 (.out(CLK));
  Button _1 ();  // open: out
  Button _2 ();  // open: out
  Button _3 ();  // open: out
  Button \u_继续运行  (.out(Go));
  LED #(.active("true")) led_1 (.in(W1));
  LED #(.active("true")) led_2 (.in(W2));
  LED #(.active("true")) led_3 (.in(W3));
  Hex_Digit_Display hex_digit_display_1 (.value(LedData[31:28]));  // open: dp
  Comparator #(.width(16), .mode("twosComplement")) comparator_1 (
    .a(\总周期数 ), .b(16'h7), .eq(comparator_1_eq));  // open: gt, lt
  Comparator #(.width(16), .mode("twosComplement")) comparator_2 (
    .a(\总周期数 ), .b(16'h241), .eq(comparator_2_eq));  // open: gt, lt
  Hex_Digit_Display hex_digit_display_2 (.value(LedData[27:24]));  // open: dp
  Hex_Digit_Display hex_digit_display_3 (.value(LedData[23:20]));  // open: dp
  Comparator #(.width(16), .mode("twosComplement")) comparator_3 (
    .a(16'h258), .b(\总周期数 ), .eq(comparator_3_eq));  // open: gt, lt
  or or_1 (or_1_out, comparator_3_eq, comparator_4_eq);
  Comparator #(.width(16), .mode("twosComplement")) comparator_4 (
    .a(\总周期数 ), .b(16'h1), .eq(comparator_4_eq));  // open: gt, lt
  Comparator #(.width(16), .mode("twosComplement")) comparator_5 (
    .a(\总周期数 ), .b(16'h4), .eq(comparator_5_eq));  // open: gt, lt
  or or_2 (or_2_out, comparator_1_eq, comparator_2_eq);
  Hex_Digit_Display hex_digit_display_4 (.value(LedData[15:12]));  // open: dp
  Hex_Digit_Display hex_digit_display_5 (.value(LedData[19:16]));  // open: dp
  Pull_Resistor #(.pull(0)) pull_resistor_1 (.node(IRA));
  assign IRA = or_1_out ? ~CLK : 1'bz;  // Controlled_Inverter controlled_inverter_1
  Pull_Resistor #(.pull(0)) pull_resistor_2 (.node(IRB));
  assign IRB = comparator_5_eq ? ~CLK : 1'bz;  // Controlled_Inverter controlled_inverter_2
  Pull_Resistor #(.pull(0)) pull_resistor_3 (.node(IRC));
  assign IRC = or_2_out ? ~CLK : 1'bz;  // Controlled_Inverter controlled_inverter_3
  Hex_Digit_Display hex_digit_display_6 (.value(LedData[7:4]));  // open: dp
  Hex_Digit_Display hex_digit_display_7 (.value(LedData[11:8]));  // open: dp
  // Probe on \总周期数 
  Hex_Digit_Display hex_digit_display_8 (.value(LedData[3:0]));  // open: dp
  or or_3 (IR1_t, IR1, IRA);
  or or_4 (IR2_t, IR2, IRB);
  or or_5 (IR3_t, IR3, IRC);

  // Notes on the sheet:
  //   中断源
  //   中断等待指示
  //   总复位信号应将除ROM以外所有存储组件全部清零
  //   多级中断测试信号模拟器
  //   数码管输出
  //   数码管输出应该用寄存器锁存，否则显示数据只能一闪而过
  //   为方便自动评测，需要输出PC，IR，寄存器堆写如数据RDin
  //   RAM写使能MemWrite、RAM写入数据MDin等信号
endmodule

module \封装正确性测试  (
);

  wire IR1, IR2, IR3, MemW, RegW;
  wire [31:0] EX_PC, ID_PC, IF_PC, IR, LED, MDin, MDinr, MEM_PC, PC, RDin, RDinr, WB_PC;

  \单周期MIPS  \u_单周期mips_1  (
    .RegWrite(RegW), .MemWrite(MemW), .PC(PC), .IR(IR), .RDin(RDin), .MDin(MDin), .LedData(LED));  // open: IR1, IR2, IR3
  \气泡流水线  \u_气泡流水线_1  (
    .RegWrite(RegW), .MemWrite(MemW), .IF_PC(IF_PC), .ID_PC(ID_PC), .EX_PC(EX_PC), .M_PC(MEM_PC),
    .WB_PC(WB_PC), .RDin(RDinr), .MDin(MDinr), .LedData(LED));
  \单周期MIPS_单级中断  \u_单周期mips_单级中断_1  (
    .IR1(IR1), .IR2(IR2), .IR3(IR3), .RegWrite(RegW), .MemWrite(MemW), .PC(PC), .IR(IR), .RDin(RDin),
    .MDin(MDin), .LedData(LED));
  \理想流水线  \u_理想流水线_1  (
    .RegWrite(RegW), .MemWrite(MemW), .IF_PC(IF_PC), .ID_PC(ID_PC), .EX_PC(EX_PC), .M_PC(MEM_PC),
    .WB_PC(WB_PC), .RDin(RDinr), .MDin(MDinr), .LedData(LED));
  \重定向流水线  \u_重定向流水线_1  (
    .RegWrite(RegW), .MemWrite(MemW), .IF_PC(IF_PC), .ID_PC(ID_PC), .EX_PC(EX_PC), .M_PC(MEM_PC),
    .WB_PC(WB_PC), .RDin(RDinr), .MDin(MDinr), .LedData(LED));
  \单周期MIPS_多级中断  \u_单周期mips_多级中断_1  (
    .IR1(IR1), .IR2(IR2), .IR3(IR3), .RegWrite(RegW), .MemWrite(MemW), .PC(PC), .IR(IR), .RDin(RDin),
    .MDin(MDin), .LedData(LED));

  // Notes on the sheet:
  //   单周期封装测试
  //   气泡流水封装测试
  //   单周期+单级中断封装测试
  //   请检查上面封装有无位宽不匹配，引脚标签是否和连接的标签相对应，否则无法在educoder平台上正确测试
  //   理想流水封装测试
  //   重定向流水封装测试
  //   单周期+多级中断封装测试
endmodule

module IF_ID (
  input  [31:0] PC,
  input  [31:0] \指令字 ,
  input  \传输状态In_表明当前传输数据有效 ,
  input  CLK,
  input  \同步清零_气泡_高电平有效 ,
  input  \使能端_低电平有效_stall_高电平有效 ,
  output [31:0] out_7,
  output [31:0] out_8,
  output \传输状态Out_表明当前传输数据有效 
);

  wire multiplexer_3_out, not_1_out;
  wire [31:0] multiplexer_1_out, multiplexer_2_out;

  Multiplexer #(.select(1), .width(32), .disabled("Z"), .enable("false")) multiplexer_1 (
    .in0(PC), .in1({32{1'b0}}), .out(multiplexer_1_out), .sel(\同步清零_气泡_高电平有效 ));
  Multiplexer #(.select(1), .width(32), .disabled("Z"), .enable("false")) multiplexer_2 (
    .in0(\指令字 ), .in1({32{1'b0}}), .out(multiplexer_2_out), .sel(\同步清零_气泡_高电平有效 ));
  Multiplexer #(.select(1), .width(1), .disabled("Z"), .enable("false")) multiplexer_3 (
    .in0(\传输状态In_表明当前传输数据有效 ), .in1(1'b0), .out(multiplexer_3_out), .sel(\同步清零_气泡_高电平有效 ));
  Pull_Resistor #(.pull(0)) pull_resistor_1 (.node(\同步清零_气泡_高电平有效 ));
  not not_1 (not_1_out, \使能端_低电平有效_stall_高电平有效 );
  Register #(.width(32), .trigger("rising"), .Select("low")) register_1 (
    .D(multiplexer_1_out), .en(not_1_out), .Q(out_7), .clk(CLK));  // open: clr
  Register #(.width(32), .trigger("rising"), .Select("low")) register_2 (
    .D(multiplexer_2_out), .en(not_1_out), .Q(out_8), .clk(CLK));  // open: clr
  Register #(.width(1), .trigger("rising"), .Select("low")) register_3 (
    .D(multiplexer_3_out), .en(not_1_out), .Q(\传输状态Out_表明当前传输数据有效 ), .clk(CLK));  // open: clr
  Pull_Resistor #(.pull(0)) pull_resistor_2 (.node(not_1_out));

  // Notes on the sheet:
  //   同步清零_气泡_高电平有效: pull=down
  //   使能端_低电平有效_stall_高电平有效: pull=down
endmodule

module ID_EX (
  input  [31:0] BAddr,
  input  [25:0] Target,
  input  J,
  input  JR,
  input  JAL,
  input  Beq,
  input  Bne,
  input  MemToReg,
  input  AluSrcB,
  input  RegWrite,
  input  MemWrite,
  input  [3:0] ALUOP,
  input  [4:0] shamt,
  input  [31:0] RegisterA,
  input  [31:0] RegisterB,
  input  [31:0] Immediatenum,
  input  [31:0] RetA,
  input  [31:0] PC,
  input  [4:0] finalrW,
  input  [31:0] \指令字 ,
  input  \传输状态In_表明当前传输数据有效 ,
  input  Halt,
  input  CLK,
  input  \同步清零_气泡_高电平有效 ,
  input  \使能端_低电平有效_stall_高电平有效 ,
  output [31:0] out_26,
  output [25:0] out_27,
  output out_28,
  output out_29,
  output out_30,
  output out_31,
  output out_32,
  output out_33,
  output out_34,
  output out_35,
  output out_36,
  output [3:0] out_37,
  output [4:0] out_38,
  output [31:0] out_39,
  output [31:0] out_40,
  output [31:0] out_41,
  output [31:0] out_42,
  output [31:0] out_43,
  output [4:0] out_44,
  output [31:0] out_45,
  output \传输状态Out_表明当前传输数据有效 ,
  output out_47
);

  wire multiplexer_3_out, multiplexer_4_out, multiplexer_5_out, multiplexer_6_out, multiplexer_7_out,
       multiplexer_8_out, multiplexer_9_out, multiplexer_10_out, multiplexer_11_out, multiplexer_21_out,
       multiplexer_22_out, pull_resistor_2_node;
  wire [3:0] multiplexer_12_out;
  wire [4:0] multiplexer_13_out, multiplexer_19_out;
  wire [25:0] multiplexer_2_out;
  wire [31:0] multiplexer_1_out, multiplexer_14_out, multiplexer_15_out, multiplexer_16_out,
       multiplexer_17_out, multiplexer_18_out, multiplexer_20_out;

  Multiplexer #(.select(1), .width(32), .disabled("Z"), .enable("false")) multiplexer_1 (
    .in0(BAddr), .in1({32{1'b0}}), .out(multiplexer_1_out), .sel(\同步清零_气泡_高电平有效 ));
  Multiplexer #(.select(1), .width(26), .disabled("Z"), .enable("false")) multiplexer_2 (
    .in0(Target), .in1({26{1'b0}}), .out(multiplexer_2_out), .sel(\同步清零_气泡_高电平有效 ));
  Multiplexer #(.select(1), .width(1), .disabled("Z"), .enable("false")) multiplexer_3 (
    .in0(J), .in1(1'b0), .out(multiplexer_3_out), .sel(\同步清零_气泡_高电平有效 ));
  Multiplexer #(.select(1), .width(1), .disabled("Z"), .enable("false")) multiplexer_4 (
    .in0(JR), .in1(1'b0), .out(multiplexer_4_out), .sel(\同步清零_气泡_高电平有效 ));
  Multiplexer #(.select(1), .width(1), .disabled("Z"), .enable("false")) multiplexer_5 (
    .in0(JAL), .in1(1'b0), .out(multiplexer_5_out), .sel(\同步清零_气泡_高电平有效 ));
  Multiplexer #(.select(1), .width(1), .disabled("Z"), .enable("false")) multiplexer_6 (
    .in0(Beq), .in1(1'b0), .out(multiplexer_6_out), .sel(\同步清零_气泡_高电平有效 ));
  Multiplexer #(.select(1), .width(1), .disabled("Z"), .enable("false")) multiplexer_7 (
    .in0(Bne), .in1(1'b0), .out(multiplexer_7_out), .sel(\同步清零_气泡_高电平有效 ));
  Multiplexer #(.select(1), .width(1), .disabled("Z"), .enable("false")) multiplexer_8 (
    .in0(MemToReg), .in1(1'b0), .out(multiplexer_8_out), .sel(\同步清零_气泡_高电平有效 ));
  Multiplexer #(.select(1), .width(1), .disabled("Z"), .enable("false")) multiplexer_9 (
    .in0(AluSrcB), .in1(1'b0), .out(multiplexer_9_out), .sel(\同步清零_气泡_高电平有效 ));
  Multiplexer #(.select(1), .width(1), .disabled("Z"), .enable("false")) multiplexer_10 (
    .in0(RegWrite), .in1(1'b0), .out(multiplexer_10_out), .sel(\同步清零_气泡_高电平有效 ));
  Multiplexer #(.select(1), .width(1), .disabled("Z"), .enable("false")) multiplexer_11 (
    .in0(MemWrite), .in1(1'b0), .out(multiplexer_11_out), .sel(\同步清零_气泡_高电平有效 ));
  Multiplexer #(.select(1), .width(4), .disabled("Z"), .enable("false")) multiplexer_12 (
    .in0(ALUOP), .in1(4'b0000), .out(multiplexer_12_out), .sel(\同步清零_气泡_高电平有效 ));
  Multiplexer #(.select(1), .width(5), .disabled("Z"), .enable("false")) multiplexer_13 (
    .in0(shamt), .in1({5{1'b0}}), .out(multiplexer_13_out), .sel(\同步清零_气泡_高电平有效 ));
  Multiplexer #(.select(1), .width(32), .disabled("Z"), .enable("false")) multiplexer_14 (
    .in0(RegisterA), .in1({32{1'b0}}), .out(multiplexer_14_out), .sel(\同步清零_气泡_高电平有效 ));
  Multiplexer #(.select(1), .width(32), .disabled("Z"), .enable("false")) multiplexer_15 (
    .in0(RegisterB), .in1({32{1'b0}}), .out(multiplexer_15_out), .sel(\同步清零_气泡_高电平有效 ));
  Multiplexer #(.select(1), .width(32), .disabled("Z"), .enable("false")) multiplexer_16 (
    .in0(Immediatenum), .in1({32{1'b0}}), .out(multiplexer_16_out), .sel(\同步清零_气泡_高电平有效 ));
  Multiplexer #(.select(1), .width(32), .disabled("Z"), .enable("false")) multiplexer_17 (
    .in0(RetA), .in1({32{1'b0}}), .out(multiplexer_17_out), .sel(\同步清零_气泡_高电平有效 ));
  Multiplexer #(.select(1), .width(32), .disabled("Z"), .enable("false")) multiplexer_18 (
    .in0(PC), .in1({32{1'b0}}), .out(multiplexer_18_out), .sel(\同步清零_气泡_高电平有效 ));
  Multiplexer #(.select(1), .width(5), .disabled("Z"), .enable("false")) multiplexer_19 (
    .in0(finalrW), .in1({5{1'b0}}), .out(multiplexer_19_out), .sel(\同步清零_气泡_高电平有效 ));
  Multiplexer #(.select(1), .width(32), .disabled("Z"), .enable("false")) multiplexer_20 (
    .in0(\指令字 ), .in1({32{1'b0}}), .out(multiplexer_20_out), .sel(\同步清零_气泡_高电平有效 ));
  Multiplexer #(.select(1), .width(1), .disabled("Z"), .enable("false")) multiplexer_21 (
    .in0(\传输状态In_表明当前传输数据有效 ), .in1(1'b0), .out(multiplexer_21_out), .sel(\同步清零_气泡_高电平有效 ));
  Multiplexer #(.select(1), .width(1), .disabled("Z"), .enable("false")) multiplexer_22 (
    .in0(Halt), .in1(1'b0), .out(multiplexer_22_out), .sel(\同步清零_气泡_高电平有效 ));
  Pull_Resistor #(.pull(0)) pull_resistor_1 (.node(\同步清零_气泡_高电平有效 ));
  Register #(.width(32), .trigger("rising"), .Select("low")) register_1 (
    .D(multiplexer_1_out), .en(pull_resistor_2_node), .Q(out_26), .clk(CLK));  // open: clr
  Register #(.width(26), .trigger("rising"), .Select("low")) register_2 (
    .D(multiplexer_2_out), .en(pull_resistor_2_node), .Q(out_27), .clk(CLK));  // open: clr
  Register #(.width(1), .trigger("rising"), .Select("low")) register_3 (
    .D(multiplexer_3_out), .en(pull_resistor_2_node), .Q(out_28), .clk(CLK));  // open: clr
  Register #(.width(1), .trigger("rising"), .Select("low")) register_4 (
    .D(multiplexer_4_out), .en(pull_resistor_2_node), .Q(out_29), .clk(CLK));  // open: clr
  Register #(.width(1), .trigger("rising"), .Select("low")) register_5 (
    .D(multiplexer_5_out), .en(pull_resistor_2_node), .Q(out_30), .clk(CLK));  // open: clr
  Register #(.width(1), .trigger("rising"), .Select("low")) register_6 (
    .D(multiplexer_6_out), .en(pull_resistor_2_node), .Q(out_31), .clk(CLK));  // open: clr
  Register #(.width(1), .trigger("rising"), .Select("low")) register_7 (
    .D(multiplexer_7_out), .en(pull_resistor_2_node), .Q(out_32), .clk(CLK));  // open: clr
  Register #(.width(1), .trigger("rising"), .Select("low")) register_8 (
    .D(multiplexer_8_out), .en(pull_resistor_2_node), .Q(out_33), .clk(CLK));  // open: clr
  Register #(.width(1), .trigger("rising"), .Select("low")) register_9 (
    .D(multiplexer_9_out), .en(pull_resistor_2_node), .Q(out_34), .clk(CLK));  // open: clr
  Register #(.width(1), .trigger("rising"), .Select("low")) register_10 (
    .D(multiplexer_10_out), .en(pull_resistor_2_node), .Q(out_35), .clk(CLK));  // open: clr
  Register #(.width(1), .trigger("rising"), .Select("low")) register_11 (
    .D(multiplexer_11_out), .en(pull_resistor_2_node), .Q(out_36), .clk(CLK));  // open: clr
  Register #(.width(4), .trigger("rising"), .Select("low")) register_12 (
    .D(multiplexer_12_out), .en(pull_resistor_2_node), .Q(out_37), .clk(CLK));  // open: clr
  Register #(.width(5), .trigger("rising"), .Select("low")) register_13 (
    .D(multiplexer_13_out), .en(pull_resistor_2_node), .Q(out_38), .clk(CLK));  // open: clr
  Register #(.width(32), .trigger("rising"), .Select("low")) register_14 (
    .D(multiplexer_14_out), .en(pull_resistor_2_node), .Q(out_39), .clk(CLK));  // open: clr
  Register #(.width(32), .trigger("rising"), .Select("low")) register_15 (
    .D(multiplexer_17_out), .en(pull_resistor_2_node), .Q(out_42), .clk(CLK));  // open: clr
  Register #(.width(32), .trigger("rising"), .Select("low")) register_16 (
    .D(multiplexer_18_out), .en(pull_resistor_2_node), .Q(out_43), .clk(CLK));  // open: clr
  Register #(.width(5), .trigger("rising"), .Select("low")) register_17 (
    .D(multiplexer_19_out), .en(pull_resistor_2_node), .Q(out_44), .clk(CLK));  // open: clr
  Register #(.width(32), .trigger("rising"), .Select("low")) register_18 (
    .D(multiplexer_20_out), .en(pull_resistor_2_node), .Q(out_45), .clk(CLK));  // open: clr
  Register #(.width(1), .trigger("rising"), .Select("low")) register_19 (
    .D(multiplexer_21_out), .en(pull_resistor_2_node), .Q(\传输状态Out_表明当前传输数据有效 ), .clk(CLK));  // open: clr
  Register #(.width(1), .trigger("rising"), .Select("low")) register_20 (
    .D(multiplexer_22_out), .en(pull_resistor_2_node), .Q(out_47), .clk(CLK));  // open: clr
  Pull_Resistor #(.pull(0)) pull_resistor_2 (.node(pull_resistor_2_node));
  not not_1 (pull_resistor_2_node, \使能端_低电平有效_stall_高电平有效 );
  Register #(.width(32), .trigger("rising"), .Select("low")) register_21 (
    .D(multiplexer_15_out), .en(pull_resistor_2_node), .Q(out_40), .clk(CLK));  // open: clr
  Register #(.width(32), .trigger("rising"), .Select("low")) register_22 (
    .D(multiplexer_16_out), .en(pull_resistor_2_node), .Q(out_41), .clk(CLK));  // open: clr

  // Notes on the sheet:
  //   同步清零_气泡_高电平有效: pull=down
  //   使能端_低电平有效_stall_高电平有效: pull=down
endmodule

module EX_MEM (
  input  MemToReg,
  input  JAL,
  input  RegWrite,
  input  MemWrite,
  input  [4:0] finalrW,
  input  [31:0] RegisterB,
  input  [31:0] AluResult,
  input  [31:0] RetA,
  input  [31:0] PC,
  input  [31:0] \指令字 ,
  input  \传输状态In_表明当前传输数据有效 ,
  input  Halt,
  input  CLK,
  input  \同步清零_气泡_高电平有效 ,
  input  \使能端_低电平有效_stall_高电平有效 ,
  output out_16,
  output out_17,
  output out_18,
  output out_19,
  output [4:0] out_20,
  output [31:0] out_21,
  output [31:0] out_22,
  output [31:0] out_23,
  output [31:0] out_24,
  output [31:0] out_25,
  output \传输状态Out_表明当前传输数据有效 ,
  output out_27
);

  wire multiplexer_1_out, multiplexer_2_out, multiplexer_3_out, multiplexer_4_out, multiplexer_11_out,
       multiplexer_12_out, pull_resistor_2_node;
  wire [4:0] multiplexer_5_out;
  wire [31:0] multiplexer_6_out, multiplexer_7_out, multiplexer_8_out, multiplexer_9_out, multiplexer_10_out;

  Multiplexer #(.select(1), .width(1), .disabled("Z"), .enable("false")) multiplexer_1 (
    .in0(MemToReg), .in1(1'b0), .out(multiplexer_1_out), .sel(\同步清零_气泡_高电平有效 ));
  Multiplexer #(.select(1), .width(1), .disabled("Z"), .enable("false")) multiplexer_2 (
    .in0(JAL), .in1(1'b0), .out(multiplexer_2_out), .sel(\同步清零_气泡_高电平有效 ));
  Multiplexer #(.select(1), .width(1), .disabled("Z"), .enable("false")) multiplexer_3 (
    .in0(RegWrite), .in1(1'b0), .out(multiplexer_3_out), .sel(\同步清零_气泡_高电平有效 ));
  Multiplexer #(.select(1), .width(1), .disabled("Z"), .enable("false")) multiplexer_4 (
    .in0(MemWrite), .in1(1'b0), .out(multiplexer_4_out), .sel(\同步清零_气泡_高电平有效 ));
  Multiplexer #(.select(1), .width(5), .disabled("Z"), .enable("false")) multiplexer_5 (
    .in0(finalrW), .in1({5{1'b0}}), .out(multiplexer_5_out), .sel(\同步清零_气泡_高电平有效 ));
  Multiplexer #(.select(1), .width(32), .disabled("Z"), .enable("false")) multiplexer_6 (
    .in0(RegisterB), .in1({32{1'b0}}), .out(multiplexer_6_out), .sel(\同步清零_气泡_高电平有效 ));
  Multiplexer #(.select(1), .width(32), .disabled("Z"), .enable("false")) multiplexer_7 (
    .in0(AluResult), .in1({32{1'b0}}), .out(multiplexer_7_out), .sel(\同步清零_气泡_高电平有效 ));
  Multiplexer #(.select(1), .width(32), .disabled("Z"), .enable("false")) multiplexer_8 (
    .in0(RetA), .in1({32{1'b0}}), .out(multiplexer_8_out), .sel(\同步清零_气泡_高电平有效 ));
  Multiplexer #(.select(1), .width(32), .disabled("Z"), .enable("false")) multiplexer_9 (
    .in0(PC), .in1({32{1'b0}}), .out(multiplexer_9_out), .sel(\同步清零_气泡_高电平有效 ));
  Multiplexer #(.select(1), .width(32), .disabled("Z"), .enable("false")) multiplexer_10 (
    .in0(\指令字 ), .in1({32{1'b0}}), .out(multiplexer_10_out), .sel(\同步清零_气泡_高电平有效 ));
  Multiplexer #(.select(1), .width(1), .disabled("Z"), .enable("false")) multiplexer_11 (
    .in0(\传输状态In_表明当前传输数据有效 ), .in1(1'b0), .out(multiplexer_11_out), .sel(\同步清零_气泡_高电平有效 ));
  Multiplexer #(.select(1), .width(1), .disabled("Z"), .enable("false")) multiplexer_12 (
    .in0(Halt), .in1(1'b0), .out(multiplexer_12_out), .sel(\同步清零_气泡_高电平有效 ));
  Pull_Resistor #(.pull(0)) pull_resistor_1 (.node(\同步清零_气泡_高电平有效 ));
  Register #(.width(1), .trigger("rising"), .Select("low")) register_1 (
    .D(multiplexer_1_out), .en(pull_resistor_2_node), .Q(out_16), .clk(CLK));  // open: clr
  Register #(.width(1), .trigger("rising"), .Select("low")) register_2 (
    .D(multiplexer_2_out), .en(pull_resistor_2_node), .Q(out_17), .clk(CLK));  // open: clr
  Register #(.width(1), .trigger("rising"), .Select("low")) register_3 (
    .D(multiplexer_3_out), .en(pull_resistor_2_node), .Q(out_18), .clk(CLK));  // open: clr
  Register #(.width(1), .trigger("rising"), .Select("low")) register_4 (
    .D(multiplexer_4_out), .en(pull_resistor_2_node), .Q(out_19), .clk(CLK));  // open: clr
  Register #(.width(5), .trigger("rising"), .Select("low")) register_5 (
    .D(multiplexer_5_out), .en(pull_resistor_2_node), .Q(out_20), .clk(CLK));  // open: clr
  Register #(.width(32), .trigger("rising"), .Select("low")) register_6 (
    .D(multiplexer_6_out), .en(pull_resistor_2_node), .Q(out_21), .clk(CLK));  // open: clr
  Register #(.width(32), .trigger("rising"), .Select("low")) register_7 (
    .D(multiplexer_7_out), .en(pull_resistor_2_node), .Q(out_22), .clk(CLK));  // open: clr
  Register #(.width(32), .trigger("rising"), .Select("low")) register_8 (
    .D(multiplexer_8_out), .en(pull_resistor_2_node), .Q(out_23), .clk(CLK));  // open: clr
  Register #(.width(32), .trigger("rising"), .Select("low")) register_9 (
    .D(multiplexer_9_out), .en(pull_resistor_2_node), .Q(out_24), .clk(CLK));  // open: clr
  Register #(.width(32), .trigger("rising"), .Select("low")) register_10 (
    .D(multiplexer_10_out), .en(pull_resistor_2_node), .Q(out_25), .clk(CLK));  // open: clr
  Register #(.width(1), .trigger("rising"), .Select("low")) register_11 (
    .D(multiplexer_11_out), .en(pull_resistor_2_node), .Q(\传输状态Out_表明当前传输数据有效 ), .clk(CLK));  // open: clr
  Register #(.width(1), .trigger("rising"), .Select("low")) register_12 (
    .D(multiplexer_12_out), .en(pull_resistor_2_node), .Q(out_27), .clk(CLK));  // open: clr
  Pull_Resistor #(.pull(0)) pull_resistor_2 (.node(pull_resistor_2_node));
  not not_1 (pull_resistor_2_node, \使能端_低电平有效_stall_高电平有效 );

  // Notes on the sheet:
  //   使能端_低电平有效_stall_高电平有效: pull=down
  //   同步清零_气泡_高电平有效: pull=down
endmodule

module MEM_WB (
  input  MemToReg,
  input  JAL,
  input  RegWrite,
  input  [4:0] finalrW,
  input  [31:0] MemData,
  input  [31:0] AluResult,
  input  [31:0] RetA,
  input  [31:0] PC,
  input  [31:0] \指令字 ,
  input  \传输状态In_表明当前传输数据有效 ,
  input  Halt,
  input  CLK,
  input  \同步清零_气泡_高电平有效 ,
  input  \使能端_低电平有效_stall_高电平有效 ,
  output out_15,
  output out_16,
  output out_17,
  output [4:0] out_18,
  output [31:0] out_19,
  output [31:0] out_20,
  output [31:0] out_21,
  output [31:0] out_22,
  output [31:0] out_23,
  output \传输状态Out_表明当前传输数据有效 ,
  output out_25
);

  wire multiplexer_1_out, multiplexer_2_out, multiplexer_3_out, multiplexer_10_out, multiplexer_11_out,
       pull_resistor_2_node;
  wire [4:0] multiplexer_4_out;
  wire [31:0] multiplexer_5_out, multiplexer_6_out, multiplexer_7_out, multiplexer_8_out, multiplexer_9_out;

  Multiplexer #(.select(1), .width(1), .disabled("Z"), .enable("false")) multiplexer_1 (
    .in0(MemToReg), .in1(1'b0), .out(multiplexer_1_out), .sel(\同步清零_气泡_高电平有效 ));
  Multiplexer #(.select(1), .width(1), .disabled("Z"), .enable("false")) multiplexer_2 (
    .in0(JAL), .in1(1'b0), .out(multiplexer_2_out), .sel(\同步清零_气泡_高电平有效 ));
  Multiplexer #(.select(1), .width(1), .disabled("Z"), .enable("false")) multiplexer_3 (
    .in0(RegWrite), .in1(1'b0), .out(multiplexer_3_out), .sel(\同步清零_气泡_高电平有效 ));
  Multiplexer #(.select(1), .width(5), .disabled("Z"), .enable("false")) multiplexer_4 (
    .in0(finalrW), .in1({5{1'b0}}), .out(multiplexer_4_out), .sel(\同步清零_气泡_高电平有效 ));
  Multiplexer #(.select(1), .width(32), .disabled("Z"), .enable("false")) multiplexer_5 (
    .in0(MemData), .in1({32{1'b0}}), .out(multiplexer_5_out), .sel(\同步清零_气泡_高电平有效 ));
  Multiplexer #(.select(1), .width(32), .disabled("Z"), .enable("false")) multiplexer_6 (
    .in0(AluResult), .in1({32{1'b0}}), .out(multiplexer_6_out), .sel(\同步清零_气泡_高电平有效 ));
  Multiplexer #(.select(1), .width(32), .disabled("Z"), .enable("false")) multiplexer_7 (
    .in0(RetA), .in1({32{1'b0}}), .out(multiplexer_7_out), .sel(\同步清零_气泡_高电平有效 ));
  Multiplexer #(.select(1), .width(32), .disabled("Z"), .enable("false")) multiplexer_8 (
    .in0(PC), .in1({32{1'b0}}), .out(multiplexer_8_out), .sel(\同步清零_气泡_高电平有效 ));
  Multiplexer #(.select(1), .width(32), .disabled("Z"), .enable("false")) multiplexer_9 (
    .in0(\指令字 ), .in1({32{1'b0}}), .out(multiplexer_9_out), .sel(\同步清零_气泡_高电平有效 ));
  Multiplexer #(.select(1), .width(1), .disabled("Z"), .enable("false")) multiplexer_10 (
    .in0(\传输状态In_表明当前传输数据有效 ), .in1(1'b0), .out(multiplexer_10_out), .sel(\同步清零_气泡_高电平有效 ));
  Multiplexer #(.select(1), .width(1), .disabled("Z"), .enable("false")) multiplexer_11 (
    .in0(Halt), .in1(1'b0), .out(multiplexer_11_out), .sel(\同步清零_气泡_高电平有效 ));
  Pull_Resistor #(.pull(0)) pull_resistor_1 (.node(\同步清零_气泡_高电平有效 ));
  Register #(.width(1), .trigger("rising"), .Select("low")) register_1 (
    .D(multiplexer_1_out), .en(pull_resistor_2_node), .Q(out_15), .clk(CLK));  // open: clr
  Register #(.width(1), .trigger("rising"), .Select("low")) register_2 (
    .D(multiplexer_2_out), .en(pull_resistor_2_node), .Q(out_16), .clk(CLK));  // open: clr
  Register #(.width(1), .trigger("rising"), .Select("low")) register_3 (
    .D(multiplexer_3_out), .en(pull_resistor_2_node), .Q(out_17), .clk(CLK));  // open: clr
  Register #(.width(5), .trigger("rising"), .Select("low")) register_4 (
    .D(multiplexer_4_out), .en(pull_resistor_2_node), .Q(out_18), .clk(CLK));  // open: clr
  Register #(.width(32), .trigger("rising"), .Select("low")) register_5 (
    .D(multiplexer_5_out), .en(pull_resistor_2_node), .Q(out_19), .clk(CLK));  // open: clr
  Register #(.width(32), .trigger("rising"), .Select("low")) register_6 (
    .D(multiplexer_6_out), .en(pull_resistor_2_node), .Q(out_20), .clk(CLK));  // open: clr
  Register #(.width(32), .trigger("rising"), .Select("low")) register_7 (
    .D(multiplexer_7_out), .en(pull_resistor_2_node), .Q(out_21), .clk(CLK));  // open: clr
  Register #(.width(32), .trigger("rising"), .Select("low")) register_8 (
    .D(multiplexer_8_out), .en(pull_resistor_2_node), .Q(out_22), .clk(CLK));  // open: clr
  Register #(.width(32), .trigger("rising"), .Select("low")) register_9 (
    .D(multiplexer_9_out), .en(pull_resistor_2_node), .Q(out_23), .clk(CLK));  // open: clr
  Register #(.width(1), .trigger("rising"), .Select("low")) register_10 (
    .D(multiplexer_10_out), .en(pull_resistor_2_node), .Q(\传输状态Out_表明当前传输数据有效 ), .clk(CLK));  // open: clr
  Register #(.width(1), .trigger("rising"), .Select("low")) register_11 (
    .D(multiplexer_11_out), .en(pull_resistor_2_node), .Q(out_25), .clk(CLK));  // open: clr
  Pull_Resistor #(.pull(0)) pull_resistor_2 (.node(pull_resistor_2_node));
  not not_1 (pull_resistor_2_node, \使能端_低电平有效_stall_高电平有效 );

  // Notes on the sheet:
  //   使能端_低电平有效_stall_高电平有效: pull=down
  //   同步清零_气泡_高电平有效: pull=down
endmodule
